// Logisim project tetris-16-bit.circ as structural Verilog: 16 circuits, main circuit Computer
module Computer (
);

  wire and_1_out, C_out, CLK, clock_1_out, cpu_1_break, cpu_1_write, not_1_out, RESET;
  wire [15:0] cpu_1_addressm, cpu_1_counter, cpu_1_outm, ram_1_data, rom_1_data;

  Clock clock_1 (.out(clock_1_out));
  Button R (.out(RESET));
  ROM #(.addrWidth(16), .dataWidth(16)) rom_1 (.addr(cpu_1_counter), .data(rom_1_data));  // open: sel
  // Probe on cpu_1_counter
  Button C (.out(C_out));
  not not_1 (not_1_out, cpu_1_break);
  or or_1 (CLK, C_out, and_1_out);
  and and_1 (and_1_out, clock_1_out, not_1_out);
  CPU cpu_1 (
    .instruction(rom_1_data), .inM(ram_1_data), .Write(cpu_1_write), .addressM(cpu_1_addressm),
    .outM(cpu_1_outm), .counter(cpu_1_counter), .CLK(CLK), .RESET(RESET), .BREAK(cpu_1_break));
  Display display_1 (.Address(cpu_1_addressm), .Data(cpu_1_outm), .Write(cpu_1_write), .CLK(CLK), .RESET(RESET));
  Debug_Board debug_board_1 (
    .Address(cpu_1_addressm), .Data(cpu_1_outm), .Write(cpu_1_write), .CLK(CLK), .RESET(RESET));
  RAM #(.addrWidth(16), .dataWidth(16), .bus("separate")) ram_1 (
    .addr(cpu_1_addressm), .din(cpu_1_outm), .data(ram_1_data), .str(cpu_1_write), .clk(CLK), .ld(1'b1),
    .clr(RESET));  // open: sel

  // Notes on the sheet:
  //   ROM
  //   contents of rom_1 (hex, n*v repeats v):
  //   4000 ec10 82 e090 10 e308 11 fdd8 10 fc20 e308 6 ea87
  //   RAM
endmodule

module CPU (
  input  CLK,
  input  RESET,
  input  [15:0] instruction,
  input  [15:0] inM,
  output [15:0] addressM,
  output [15:0] outM,
  output Write,
  output [15:0] counter,
  output BREAK
);

  wire ALU_ng, ALU_zr, nor_1_out, not_1_out, or_1_out;
  wire [15:0] controlled_buffer_1_out, multiplexer_1_out, Register_D_q;

  Multiplexer #(.width(16), .enable("false")) multiplexer_1 (
    .in0({16{1'b0}}), .in1(instruction), .out({multiplexer_1_out[15:4], Write, multiplexer_1_out[2:0]}),
    .sel(instruction[15]));
  not not_1 (not_1_out, instruction[15]);
  assign controlled_buffer_1_out = not_1_out ? {1'b0, instruction[14:0]} : 16'bz;  // Controlled_Buffer controlled_buffer_1
  or or_1 (or_1_out, not_1_out, multiplexer_1_out[5]);
  nor nor_1 (nor_1_out, multiplexer_1_out[13], multiplexer_1_out[14]);
  and and_1 (BREAK, nor_1_out, multiplexer_1_out[15]);
  Register #(.width(16)) Register_A (.D(controlled_buffer_1_out), .en(or_1_out), .Q(addressM), .clk(CLK), .clr(RESET));
  assign controlled_buffer_1_out = instruction[15] ? outM : 16'bz;  // Controlled_Buffer controlled_buffer_2
  Register #(.width(16)) Register_D (.D(outM), .en(multiplexer_1_out[4]), .Q(Register_D_q), .clk(CLK), .clr(RESET));
  Logic ALU (
    .CMP(multiplexer_1_out[12:6]), .A(addressM), .M(inM), .D(Register_D_q), .out(outM), .ng(ALU_ng),
    .zr(ALU_zr));
  Counter counter_1 (
    .jump_control(multiplexer_1_out[2:0]), .out_7(counter), .jump_address(addressM), .zr(ALU_zr),
    .ng(ALU_ng), .in_1(CLK), .in_2(RESET));
endmodule

module ALU (
  input  zx,
  input  nx,
  input  zy,
  input  ny,
  input  f,
  input  no,
  input  [15:0] x,
  input  [15:0] y,
  output [15:0] out,
  output zr,
  output ng
);

  wire not_3_out;
  wire [15:0] adder_1_out, and_1_out, multiplexer_1_out, multiplexer_2_out, multiplexer_3_out,
       multiplexer_4_out, multiplexer_5_out, not_1_out, not_2_out, not_4_out;

  assign not_1_out = ~multiplexer_1_out;  // NOT_Gate not_1, 16 bits wide
  Multiplexer #(.width(16), .enable("false")) multiplexer_1 (
    .in0(x), .in1({16{1'b0}}), .out(multiplexer_1_out), .sel(zx));
  Multiplexer #(.width(16), .enable("false")) multiplexer_2 (
    .in0(y), .in1({16{1'b0}}), .out(multiplexer_2_out), .sel(zy));
  assign not_2_out = ~multiplexer_2_out;  // NOT_Gate not_2, 16 bits wide
  Multiplexer #(.width(16), .enable("false")) multiplexer_3 (
    .in0(multiplexer_1_out), .in1(not_1_out), .out(multiplexer_3_out), .sel(nx));
  Multiplexer #(.width(16), .enable("false")) multiplexer_4 (
    .in0(multiplexer_2_out), .in1(not_2_out), .out(multiplexer_4_out), .sel(ny));
  Adder #(.width(16)) adder_1 (.a(multiplexer_3_out), .b(multiplexer_4_out), .out(adder_1_out));  // open: cin, cout
  assign and_1_out = multiplexer_3_out & multiplexer_4_out;  // AND_Gate and_1, 16 bits wide
  not not_3 (not_3_out, f);
  Multiplexer #(.width(16), .enable("false")) multiplexer_5 (
    .in0(adder_1_out), .in1(and_1_out), .out(multiplexer_5_out), .sel(not_3_out));
  Multiplexer #(.width(16), .enable("false")) multiplexer_6 (
    .in0(multiplexer_5_out), .in1(not_4_out), .out({ng, out[14:0]}), .sel(no));
  assign not_4_out = ~multiplexer_5_out;  // NOT_Gate not_4, 16 bits wide
  nor nor_1 (zr, ng, out[14], out[13], out[12], out[11], out[10], out[9], out[8], out[7], out[6], out[5], out[4], out[3], out[2], out[1], out[0]);

  assign out[15] = ng;
endmodule

module Logic (
  input  [6:0] CMP,
  input  [15:0] A,
  input  [15:0] M,
  input  [15:0] D,
  output [15:0] out,
  output ng,
  output zr
);

  wire [15:0] multiplexer_1_out;

  Multiplexer #(.width(16), .enable("false")) multiplexer_1 (.in0(A), .in1(M), .out(multiplexer_1_out), .sel(CMP[6]));
  ALU alu_1 (
    .x(D), .out(out), .zx(CMP[5]), .nx(CMP[4]), .zy(CMP[3]), .ny(CMP[2]), .f(CMP[1]), .no(CMP[0]), .zr(zr),
    .ng(ng), .y(multiplexer_1_out));
endmodule

module Counter (
  input  in_1,
  input  in_2,
  input  zr,
  input  ng,
  input  [15:0] jump_address,
  input  [2:0] jump_control,
  output [15:0] out_7
);

  wire not_1_out, not_2_out, rom_1_data;

  ROM #(.addrWidth(5), .dataWidth(1)) rom_1 (.addr({jump_control, zr, ng}), .data(rom_1_data));  // open: sel
  not not_1 (not_1_out, rom_1_data);
  Counter_part #(.width(16), .max('hffff)) counter_1 (
    .load(rom_1_data), .D(jump_address), .count(not_1_out), .Q(out_7), .clk(not_2_out), .clr(in_2));  // open: carry
  not not_2 (not_2_out, in_1);

  // Other names for the same wires on the sheet: CLK = in_1; RESET = in_2

  // Notes on the sheet:
  //   contents of rom_1 (hex, n*v repeats v):
  //   4*0 1 5*0 1 0 1 0 1 0 0 1 0 0 1 1 0 0 0 1 1 0 4*1
  //   Here need to invert the clock signal to prevent the next instruction reach CPU too early
endmodule

module ScreenControl (
  input  CLK,
  input  Reset,
  input  [15:0] Data,
  input  Enable,
  input  [15:0] Address,
  output [15:0] out_6,
  output [15:0] out_7,
  output [15:0] out_8,
  output [15:0] out_9,
  output [15:0] out_10,
  output [15:0] out_11,
  output [15:0] out_12,
  output [15:0] out_13,
  output [15:0] out_14,
  output [15:0] out_15,
  output [15:0] out_16,
  output [15:0] out_17,
  output [15:0] out_18,
  output [15:0] out_19,
  output [15:0] out_20,
  output [15:0] out_21
);

  wire and_1_out, and_2_out, and_3_out, and_4_out, and_5_out, and_6_out, and_7_out, and_8_out, and_9_out,
       and_10_out, and_11_out, and_12_out, and_13_out, and_14_out, and_15_out, and_16_out;

  and and_1 (and_1_out, Enable, Address[15]);
  Register #(.width(16)) register_1 (.D(Data), .en(and_1_out), .Q(out_6), .clk(CLK), .clr(Reset));
  and and_2 (and_2_out, Enable, Address[14]);
  Register #(.width(16)) register_2 (.D(Data), .en(and_2_out), .Q(out_7), .clk(CLK), .clr(Reset));
  and and_3 (and_3_out, Enable, Address[13]);
  Register #(.width(16)) register_3 (.D(Data), .en(and_3_out), .Q(out_8), .clk(CLK), .clr(Reset));
  Register #(.width(16)) register_4 (.D(Data), .en(and_4_out), .Q(out_9), .clk(CLK), .clr(Reset));
  and and_4 (and_4_out, Enable, Address[12]);
  Register #(.width(16)) register_5 (.D(Data), .en(and_5_out), .Q(out_10), .clk(CLK), .clr(Reset));
  and and_5 (and_5_out, Enable, Address[11]);
  Register #(.width(16)) register_6 (.D(Data), .en(and_6_out), .Q(out_11), .clk(CLK), .clr(Reset));
  and and_6 (and_6_out, Enable, Address[10]);
  and and_7 (and_7_out, Enable, Address[9]);
  Register #(.width(16)) register_7 (.D(Data), .en(and_7_out), .Q(out_12), .clk(CLK), .clr(Reset));
  and and_8 (and_8_out, Enable, Address[8]);
  Register #(.width(16)) register_8 (.D(Data), .en(and_8_out), .Q(out_13), .clk(CLK), .clr(Reset));
  and and_9 (and_9_out, Enable, Address[7]);
  Register #(.width(16)) register_9 (.D(Data), .en(and_9_out), .Q(out_14), .clk(CLK), .clr(Reset));
  and and_10 (and_10_out, Enable, Address[6]);
  Register #(.width(16)) register_10 (.D(Data), .en(and_10_out), .Q(out_15), .clk(CLK), .clr(Reset));
  and and_11 (and_11_out, Enable, Address[5]);
  Register #(.width(16)) register_11 (.D(Data), .en(and_11_out), .Q(out_16), .clk(CLK), .clr(Reset));
  Register #(.width(16)) register_12 (.D(Data), .en(and_12_out), .Q(out_17), .clk(CLK), .clr(Reset));
  and and_12 (and_12_out, Enable, Address[4]);
  Register #(.width(16)) register_13 (.D(Data), .en(and_13_out), .Q(out_18), .clk(CLK), .clr(Reset));
  and and_13 (and_13_out, Enable, Address[3]);
  Register #(.width(16)) register_14 (.D(Data), .en(and_14_out), .Q(out_19), .clk(CLK), .clr(Reset));
  and and_14 (and_14_out, Enable, Address[2]);
  and and_15 (and_15_out, Enable, Address[1]);
  Register #(.width(16)) register_15 (.D(Data), .en(and_15_out), .Q(out_20), .clk(CLK), .clr(Reset));
  and and_16 (and_16_out, Enable, Address[0]);
  Register #(.width(16)) register_16 (.D(Data), .en(and_16_out), .Q(out_21), .clk(CLK), .clr(Reset));

  // Other names for the same wires on the sheet: RST = Reset
endmodule

module Display (
  input  [15:0] Address,
  input  [15:0] Data,
  input  Write,
  input  CLK,
  input  RESET
);

  wire address_translator_1_active, and_1_out;
  wire [3:0] screenchip_1_out, screenchip_1_out_3;
  wire [15:0] address_translator_1_translated_address, Local_Address, screencontrol2_1_out_6,
       screencontrol2_1_out_7, screencontrol2_1_out_8, screencontrol2_1_out_9, screencontrol2_1_out_10,
       screencontrol2_1_out_11, screencontrol2_1_out_12, screencontrol2_1_out_13, screencontrol2_1_out_14,
       screencontrol2_1_out_15, screencontrol2_1_out_16, screencontrol2_1_out_17, screencontrol2_1_out_18,
       screencontrol2_1_out_19, screencontrol2_1_out_20, screencontrol2_1_out_21, screencontrol2_2_out_6,
       screencontrol2_2_out_7, screencontrol2_2_out_8, screencontrol2_2_out_9, screencontrol2_2_out_10,
       screencontrol2_2_out_11, screencontrol2_2_out_12, screencontrol2_2_out_13, screencontrol2_2_out_14,
       screencontrol2_2_out_15, screencontrol2_2_out_16, screencontrol2_2_out_17, screencontrol2_2_out_18,
       screencontrol2_2_out_19, screencontrol2_2_out_20, screencontrol2_2_out_21, screencontrol2_3_out_6,
       screencontrol2_3_out_7, screencontrol2_3_out_8, screencontrol2_3_out_9, screencontrol2_3_out_10,
       screencontrol2_3_out_11, screencontrol2_3_out_12, screencontrol2_3_out_13, screencontrol2_3_out_14,
       screencontrol2_3_out_15, screencontrol2_3_out_16, screencontrol2_3_out_17, screencontrol2_3_out_18,
       screencontrol2_3_out_19, screencontrol2_3_out_20, screencontrol2_3_out_21, screencontrol2_4_out_6,
       screencontrol2_4_out_7, screencontrol2_4_out_8, screencontrol2_4_out_9, screencontrol2_4_out_10,
       screencontrol2_4_out_11, screencontrol2_4_out_12, screencontrol2_4_out_13, screencontrol2_4_out_14,
       screencontrol2_4_out_15, screencontrol2_4_out_16, screencontrol2_4_out_17, screencontrol2_4_out_18,
       screencontrol2_4_out_19, screencontrol2_4_out_20, screencontrol2_4_out_21, screencontrol2_5_out_6,
       screencontrol2_5_out_7, screencontrol2_5_out_8, screencontrol2_5_out_9, screencontrol2_5_out_10,
       screencontrol2_5_out_11, screencontrol2_5_out_12, screencontrol2_5_out_13, screencontrol2_5_out_14,
       screencontrol2_5_out_15, screencontrol2_5_out_16, screencontrol2_5_out_17, screencontrol2_5_out_18,
       screencontrol2_5_out_19, screencontrol2_5_out_20, screencontrol2_5_out_21, screencontrol2_6_out_6,
       screencontrol2_6_out_7, screencontrol2_6_out_8, screencontrol2_6_out_9, screencontrol2_6_out_10,
       screencontrol2_6_out_11, screencontrol2_6_out_12, screencontrol2_6_out_13, screencontrol2_6_out_14,
       screencontrol2_6_out_15, screencontrol2_6_out_16, screencontrol2_6_out_17, screencontrol2_6_out_18,
       screencontrol2_6_out_19, screencontrol2_6_out_20, screencontrol2_6_out_21, screencontrol2_7_out_6,
       screencontrol2_7_out_7, screencontrol2_7_out_8, screencontrol2_7_out_9, screencontrol2_7_out_10,
       screencontrol2_7_out_11, screencontrol2_7_out_12, screencontrol2_7_out_13, screencontrol2_7_out_14,
       screencontrol2_7_out_15, screencontrol2_7_out_16, screencontrol2_7_out_17, screencontrol2_7_out_18,
       screencontrol2_7_out_19, screencontrol2_7_out_20, screencontrol2_7_out_21, screencontrol2_8_out_6,
       screencontrol2_8_out_7, screencontrol2_8_out_8, screencontrol2_8_out_9, screencontrol2_8_out_10,
       screencontrol2_8_out_11, screencontrol2_8_out_12, screencontrol2_8_out_13, screencontrol2_8_out_14,
       screencontrol2_8_out_15, screencontrol2_8_out_16, screencontrol2_8_out_17, screencontrol2_8_out_18,
       screencontrol2_8_out_19, screencontrol2_8_out_20, screencontrol2_8_out_21, screencontrol2_9_out_6,
       screencontrol2_9_out_7, screencontrol2_9_out_8, screencontrol2_9_out_9, screencontrol2_9_out_10,
       screencontrol2_9_out_11, screencontrol2_9_out_12, screencontrol2_9_out_13, screencontrol2_9_out_14,
       screencontrol2_9_out_15, screencontrol2_9_out_16, screencontrol2_9_out_17, screencontrol2_9_out_18,
       screencontrol2_9_out_19, screencontrol2_9_out_20, screencontrol2_9_out_21, screencontrol2_10_out_6,
       screencontrol2_10_out_7, screencontrol2_10_out_8, screencontrol2_10_out_9, screencontrol2_10_out_10,
       screencontrol2_10_out_11, screencontrol2_10_out_12, screencontrol2_10_out_13,
       screencontrol2_10_out_14, screencontrol2_10_out_15, screencontrol2_10_out_16,
       screencontrol2_10_out_17, screencontrol2_10_out_18, screencontrol2_10_out_19,
       screencontrol2_10_out_20, screencontrol2_10_out_21, screencontrol2_11_out_6, screencontrol2_11_out_7,
       screencontrol2_11_out_8, screencontrol2_11_out_9, screencontrol2_11_out_10, screencontrol2_11_out_11,
       screencontrol2_11_out_12, screencontrol2_11_out_13, screencontrol2_11_out_14,
       screencontrol2_11_out_15, screencontrol2_11_out_16, screencontrol2_11_out_17,
       screencontrol2_11_out_18, screencontrol2_11_out_19, screencontrol2_11_out_20,
       screencontrol2_11_out_21, screencontrol2_12_out_6, screencontrol2_12_out_7, screencontrol2_12_out_8,
       screencontrol2_12_out_9, screencontrol2_12_out_10, screencontrol2_12_out_11, screencontrol2_12_out_12,
       screencontrol2_12_out_13, screencontrol2_12_out_14, screencontrol2_12_out_15,
       screencontrol2_12_out_16, screencontrol2_12_out_17, screencontrol2_12_out_18,
       screencontrol2_12_out_19, screencontrol2_12_out_20, screencontrol2_12_out_21, screencontrol2_13_out_6,
       screencontrol2_13_out_7, screencontrol2_13_out_8, screencontrol2_13_out_9, screencontrol2_13_out_10,
       screencontrol2_13_out_11, screencontrol2_13_out_12, screencontrol2_13_out_13,
       screencontrol2_13_out_14, screencontrol2_13_out_15, screencontrol2_13_out_16,
       screencontrol2_13_out_17, screencontrol2_13_out_18, screencontrol2_13_out_19,
       screencontrol2_13_out_20, screencontrol2_13_out_21, screencontrol2_14_out_6, screencontrol2_14_out_7,
       screencontrol2_14_out_8, screencontrol2_14_out_9, screencontrol2_14_out_10, screencontrol2_14_out_11,
       screencontrol2_14_out_12, screencontrol2_14_out_13, screencontrol2_14_out_14,
       screencontrol2_14_out_15, screencontrol2_14_out_16, screencontrol2_14_out_17,
       screencontrol2_14_out_18, screencontrol2_14_out_19, screencontrol2_14_out_20,
       screencontrol2_14_out_21, screencontrol2_15_out_6, screencontrol2_15_out_7, screencontrol2_15_out_8,
       screencontrol2_15_out_9, screencontrol2_15_out_10, screencontrol2_15_out_11, screencontrol2_15_out_12,
       screencontrol2_15_out_13, screencontrol2_15_out_14, screencontrol2_15_out_15,
       screencontrol2_15_out_16, screencontrol2_15_out_17, screencontrol2_15_out_18,
       screencontrol2_15_out_19, screencontrol2_15_out_20, screencontrol2_15_out_21, screencontrol2_16_out_6,
       screencontrol2_16_out_7, screencontrol2_16_out_8, screencontrol2_16_out_9, screencontrol2_16_out_10,
       screencontrol2_16_out_11, screencontrol2_16_out_12, screencontrol2_16_out_13,
       screencontrol2_16_out_14, screencontrol2_16_out_15, screencontrol2_16_out_16,
       screencontrol2_16_out_17, screencontrol2_16_out_18, screencontrol2_16_out_19,
       screencontrol2_16_out_20, screencontrol2_16_out_21, screencontrol2_17_out_6, screencontrol2_17_out_7,
       screencontrol2_17_out_8, screencontrol2_17_out_9, screencontrol2_17_out_10, screencontrol2_17_out_11,
       screencontrol2_17_out_12, screencontrol2_17_out_13, screencontrol2_17_out_14,
       screencontrol2_17_out_15, screencontrol2_17_out_16, screencontrol2_17_out_17,
       screencontrol2_17_out_18, screencontrol2_17_out_19, screencontrol2_17_out_20,
       screencontrol2_17_out_21, screencontrol2_18_out_6, screencontrol2_18_out_7, screencontrol2_18_out_8,
       screencontrol2_18_out_9, screencontrol2_18_out_10, screencontrol2_18_out_11, screencontrol2_18_out_12,
       screencontrol2_18_out_13, screencontrol2_18_out_14, screencontrol2_18_out_15,
       screencontrol2_18_out_16, screencontrol2_18_out_17, screencontrol2_18_out_18,
       screencontrol2_18_out_19, screencontrol2_18_out_20, screencontrol2_18_out_21, screencontrol2_19_out_6,
       screencontrol2_19_out_7, screencontrol2_19_out_8, screencontrol2_19_out_9, screencontrol2_19_out_10,
       screencontrol2_19_out_11, screencontrol2_19_out_12, screencontrol2_19_out_13,
       screencontrol2_19_out_14, screencontrol2_19_out_15, screencontrol2_19_out_16,
       screencontrol2_19_out_17, screencontrol2_19_out_18, screencontrol2_19_out_19,
       screencontrol2_19_out_20, screencontrol2_19_out_21, screencontrol2_20_out_6, screencontrol2_20_out_7,
       screencontrol2_20_out_8, screencontrol2_20_out_9, screencontrol2_20_out_10, screencontrol2_20_out_11,
       screencontrol2_20_out_12, screencontrol2_20_out_13, screencontrol2_20_out_14,
       screencontrol2_20_out_15, screencontrol2_20_out_16, screencontrol2_20_out_17,
       screencontrol2_20_out_18, screencontrol2_20_out_19, screencontrol2_20_out_20,
       screencontrol2_20_out_21, screencontrol2_21_out_6, screencontrol2_21_out_7, screencontrol2_21_out_8,
       screencontrol2_21_out_9, screencontrol2_21_out_10, screencontrol2_21_out_11, screencontrol2_21_out_12,
       screencontrol2_21_out_13, screencontrol2_21_out_14, screencontrol2_21_out_15,
       screencontrol2_21_out_16, screencontrol2_21_out_17, screencontrol2_21_out_18,
       screencontrol2_21_out_19, screencontrol2_21_out_20, screencontrol2_21_out_21, screencontrol2_22_out_6,
       screencontrol2_22_out_7, screencontrol2_22_out_8, screencontrol2_22_out_9, screencontrol2_22_out_10,
       screencontrol2_22_out_11, screencontrol2_22_out_12, screencontrol2_22_out_13,
       screencontrol2_22_out_14, screencontrol2_22_out_15, screencontrol2_22_out_16,
       screencontrol2_22_out_17, screencontrol2_22_out_18, screencontrol2_22_out_19,
       screencontrol2_22_out_20, screencontrol2_22_out_21, screencontrol2_23_out_6, screencontrol2_23_out_7,
       screencontrol2_23_out_8, screencontrol2_23_out_9, screencontrol2_23_out_10, screencontrol2_23_out_11,
       screencontrol2_23_out_12, screencontrol2_23_out_13, screencontrol2_23_out_14,
       screencontrol2_23_out_15, screencontrol2_23_out_16, screencontrol2_23_out_17,
       screencontrol2_23_out_18, screencontrol2_23_out_19, screencontrol2_23_out_20,
       screencontrol2_23_out_21, screencontrol2_24_out_6, screencontrol2_24_out_7, screencontrol2_24_out_8,
       screencontrol2_24_out_9, screencontrol2_24_out_10, screencontrol2_24_out_11, screencontrol2_24_out_12,
       screencontrol2_24_out_13, screencontrol2_24_out_14, screencontrol2_24_out_15,
       screencontrol2_24_out_16, screencontrol2_24_out_17, screencontrol2_24_out_18,
       screencontrol2_24_out_19, screencontrol2_24_out_20, screencontrol2_24_out_21, screencontrol2_25_out_6,
       screencontrol2_25_out_7, screencontrol2_25_out_8, screencontrol2_25_out_9, screencontrol2_25_out_10,
       screencontrol2_25_out_11, screencontrol2_25_out_12, screencontrol2_25_out_13,
       screencontrol2_25_out_14, screencontrol2_25_out_15, screencontrol2_25_out_16,
       screencontrol2_25_out_17, screencontrol2_25_out_18, screencontrol2_25_out_19,
       screencontrol2_25_out_20, screencontrol2_25_out_21, screencontrol2_26_out_6, screencontrol2_26_out_7,
       screencontrol2_26_out_8, screencontrol2_26_out_9, screencontrol2_26_out_10, screencontrol2_26_out_11,
       screencontrol2_26_out_12, screencontrol2_26_out_13, screencontrol2_26_out_14,
       screencontrol2_26_out_15, screencontrol2_26_out_16, screencontrol2_26_out_17,
       screencontrol2_26_out_18, screencontrol2_26_out_19, screencontrol2_26_out_20,
       screencontrol2_26_out_21, screencontrol2_27_out_6, screencontrol2_27_out_7, screencontrol2_27_out_8,
       screencontrol2_27_out_9, screencontrol2_27_out_10, screencontrol2_27_out_11, screencontrol2_27_out_12,
       screencontrol2_27_out_13, screencontrol2_27_out_14, screencontrol2_27_out_15,
       screencontrol2_27_out_16, screencontrol2_27_out_17, screencontrol2_27_out_18,
       screencontrol2_27_out_19, screencontrol2_27_out_20, screencontrol2_27_out_21, screencontrol2_28_out_6,
       screencontrol2_28_out_7, screencontrol2_28_out_8, screencontrol2_28_out_9, screencontrol2_28_out_10,
       screencontrol2_28_out_11, screencontrol2_28_out_12, screencontrol2_28_out_13,
       screencontrol2_28_out_14, screencontrol2_28_out_15, screencontrol2_28_out_16,
       screencontrol2_28_out_17, screencontrol2_28_out_18, screencontrol2_28_out_19,
       screencontrol2_28_out_20, screencontrol2_28_out_21, screencontrol2_29_out_6, screencontrol2_29_out_7,
       screencontrol2_29_out_8, screencontrol2_29_out_9, screencontrol2_29_out_10, screencontrol2_29_out_11,
       screencontrol2_29_out_12, screencontrol2_29_out_13, screencontrol2_29_out_14,
       screencontrol2_29_out_15, screencontrol2_29_out_16, screencontrol2_29_out_17,
       screencontrol2_29_out_18, screencontrol2_29_out_19, screencontrol2_29_out_20,
       screencontrol2_29_out_21, screencontrol2_30_out_6, screencontrol2_30_out_7, screencontrol2_30_out_8,
       screencontrol2_30_out_9, screencontrol2_30_out_10, screencontrol2_30_out_11, screencontrol2_30_out_12,
       screencontrol2_30_out_13, screencontrol2_30_out_14, screencontrol2_30_out_15,
       screencontrol2_30_out_16, screencontrol2_30_out_17, screencontrol2_30_out_18,
       screencontrol2_30_out_19, screencontrol2_30_out_20, screencontrol2_30_out_21, screencontrol2_31_out_6,
       screencontrol2_31_out_7, screencontrol2_31_out_8, screencontrol2_31_out_9, screencontrol2_31_out_10,
       screencontrol2_31_out_11, screencontrol2_31_out_12, screencontrol2_31_out_13,
       screencontrol2_31_out_14, screencontrol2_31_out_15, screencontrol2_31_out_16,
       screencontrol2_31_out_17, screencontrol2_31_out_18, screencontrol2_31_out_19,
       screencontrol2_31_out_20, screencontrol2_31_out_21, screencontrol2_32_out_6, screencontrol2_32_out_7,
       screencontrol2_32_out_8, screencontrol2_32_out_9, screencontrol2_32_out_10, screencontrol2_32_out_11,
       screencontrol2_32_out_12, screencontrol2_32_out_13, screencontrol2_32_out_14,
       screencontrol2_32_out_15, screencontrol2_32_out_16, screencontrol2_32_out_17,
       screencontrol2_32_out_18, screencontrol2_32_out_19, screencontrol2_32_out_20, screencontrol2_32_out_21;
  wire [27:4] screenchip_1_out_2;

  and and_1 (and_1_out, Write, CLK);
  Address_Translator address_translator_1 (
    .Address(Address), .Offset(16'h4000), .Limit(16'h2000),
    .Translated_Address(address_translator_1_translated_address), .Active(address_translator_1_active));
  ScreenChip screenchip_1 (
    .Enable(address_translator_1_active), .Address(address_translator_1_translated_address),
    .Local_Address(Local_Address), .OUT({screenchip_1_out, screenchip_1_out_2, screenchip_1_out_3}));
  DotMatrix #(.inputtype("row"), .matrixcols(16), .matrixrows(16)) dotmatrix_1 (
    .row0(screencontrol2_1_out_6), .row1(screencontrol2_1_out_7), .row2(screencontrol2_1_out_8),
    .row3(screencontrol2_1_out_9), .row4(screencontrol2_1_out_10), .row5(screencontrol2_1_out_11),
    .row6(screencontrol2_1_out_12), .row7(screencontrol2_1_out_13), .row8(screencontrol2_1_out_14),
    .row9(screencontrol2_1_out_15), .row10(screencontrol2_1_out_16), .row11(screencontrol2_1_out_17),
    .row12(screencontrol2_1_out_18), .row13(screencontrol2_1_out_19), .row14(screencontrol2_1_out_20),
    .row15(screencontrol2_1_out_21));
  ScreenControl2 screencontrol2_1 (
    .CLK(and_1_out), .Data(Data), .Reset(RESET), .Enable(screenchip_1_out[0]), .Address(Local_Address),
    .out_6(screencontrol2_1_out_6), .out_7(screencontrol2_1_out_7), .out_8(screencontrol2_1_out_8),
    .out_9(screencontrol2_1_out_9), .out_10(screencontrol2_1_out_10), .out_11(screencontrol2_1_out_11),
    .out_12(screencontrol2_1_out_12), .out_13(screencontrol2_1_out_13), .out_14(screencontrol2_1_out_14),
    .out_15(screencontrol2_1_out_15), .out_16(screencontrol2_1_out_16), .out_17(screencontrol2_1_out_17),
    .out_18(screencontrol2_1_out_18), .out_19(screencontrol2_1_out_19), .out_20(screencontrol2_1_out_20),
    .out_21(screencontrol2_1_out_21));
  ScreenControl2 screencontrol2_2 (
    .CLK(and_1_out), .Data(Data), .Reset(RESET), .Enable(screenchip_1_out[1]), .Address(Local_Address),
    .out_6(screencontrol2_2_out_6), .out_7(screencontrol2_2_out_7), .out_8(screencontrol2_2_out_8),
    .out_9(screencontrol2_2_out_9), .out_10(screencontrol2_2_out_10), .out_11(screencontrol2_2_out_11),
    .out_12(screencontrol2_2_out_12), .out_13(screencontrol2_2_out_13), .out_14(screencontrol2_2_out_14),
    .out_15(screencontrol2_2_out_15), .out_16(screencontrol2_2_out_16), .out_17(screencontrol2_2_out_17),
    .out_18(screencontrol2_2_out_18), .out_19(screencontrol2_2_out_19), .out_20(screencontrol2_2_out_20),
    .out_21(screencontrol2_2_out_21));
  DotMatrix #(.inputtype("row"), .matrixcols(16), .matrixrows(16)) dotmatrix_2 (
    .row0(screencontrol2_2_out_6), .row1(screencontrol2_2_out_7), .row2(screencontrol2_2_out_8),
    .row3(screencontrol2_2_out_9), .row4(screencontrol2_2_out_10), .row5(screencontrol2_2_out_11),
    .row6(screencontrol2_2_out_12), .row7(screencontrol2_2_out_13), .row8(screencontrol2_2_out_14),
    .row9(screencontrol2_2_out_15), .row10(screencontrol2_2_out_16), .row11(screencontrol2_2_out_17),
    .row12(screencontrol2_2_out_18), .row13(screencontrol2_2_out_19), .row14(screencontrol2_2_out_20),
    .row15(screencontrol2_2_out_21));
  ScreenControl2 screencontrol2_3 (
    .CLK(and_1_out), .Data(Data), .Reset(RESET), .Enable(screenchip_1_out[2]), .Address(Local_Address),
    .out_6(screencontrol2_3_out_6), .out_7(screencontrol2_3_out_7), .out_8(screencontrol2_3_out_8),
    .out_9(screencontrol2_3_out_9), .out_10(screencontrol2_3_out_10), .out_11(screencontrol2_3_out_11),
    .out_12(screencontrol2_3_out_12), .out_13(screencontrol2_3_out_13), .out_14(screencontrol2_3_out_14),
    .out_15(screencontrol2_3_out_15), .out_16(screencontrol2_3_out_16), .out_17(screencontrol2_3_out_17),
    .out_18(screencontrol2_3_out_18), .out_19(screencontrol2_3_out_19), .out_20(screencontrol2_3_out_20),
    .out_21(screencontrol2_3_out_21));
  DotMatrix #(.inputtype("row"), .matrixcols(16), .matrixrows(16)) dotmatrix_3 (
    .row0(screencontrol2_3_out_6), .row1(screencontrol2_3_out_7), .row2(screencontrol2_3_out_8),
    .row3(screencontrol2_3_out_9), .row4(screencontrol2_3_out_10), .row5(screencontrol2_3_out_11),
    .row6(screencontrol2_3_out_12), .row7(screencontrol2_3_out_13), .row8(screencontrol2_3_out_14),
    .row9(screencontrol2_3_out_15), .row10(screencontrol2_3_out_16), .row11(screencontrol2_3_out_17),
    .row12(screencontrol2_3_out_18), .row13(screencontrol2_3_out_19), .row14(screencontrol2_3_out_20),
    .row15(screencontrol2_3_out_21));
  DotMatrix #(.inputtype("row"), .matrixcols(16), .matrixrows(16)) dotmatrix_4 (
    .row0(screencontrol2_4_out_6), .row1(screencontrol2_4_out_7), .row2(screencontrol2_4_out_8),
    .row3(screencontrol2_4_out_9), .row4(screencontrol2_4_out_10), .row5(screencontrol2_4_out_11),
    .row6(screencontrol2_4_out_12), .row7(screencontrol2_4_out_13), .row8(screencontrol2_4_out_14),
    .row9(screencontrol2_4_out_15), .row10(screencontrol2_4_out_16), .row11(screencontrol2_4_out_17),
    .row12(screencontrol2_4_out_18), .row13(screencontrol2_4_out_19), .row14(screencontrol2_4_out_20),
    .row15(screencontrol2_4_out_21));
  ScreenControl2 screencontrol2_4 (
    .CLK(and_1_out), .Data(Data), .Reset(RESET), .Enable(screenchip_1_out[3]), .Address(Local_Address),
    .out_6(screencontrol2_4_out_6), .out_7(screencontrol2_4_out_7), .out_8(screencontrol2_4_out_8),
    .out_9(screencontrol2_4_out_9), .out_10(screencontrol2_4_out_10), .out_11(screencontrol2_4_out_11),
    .out_12(screencontrol2_4_out_12), .out_13(screencontrol2_4_out_13), .out_14(screencontrol2_4_out_14),
    .out_15(screencontrol2_4_out_15), .out_16(screencontrol2_4_out_16), .out_17(screencontrol2_4_out_17),
    .out_18(screencontrol2_4_out_18), .out_19(screencontrol2_4_out_19), .out_20(screencontrol2_4_out_20),
    .out_21(screencontrol2_4_out_21));
  ScreenControl2 screencontrol2_5 (
    .CLK(and_1_out), .Data(Data), .Reset(RESET), .Enable(screenchip_1_out_2[24]), .Address(Local_Address),
    .out_6(screencontrol2_5_out_6), .out_7(screencontrol2_5_out_7), .out_8(screencontrol2_5_out_8),
    .out_9(screencontrol2_5_out_9), .out_10(screencontrol2_5_out_10), .out_11(screencontrol2_5_out_11),
    .out_12(screencontrol2_5_out_12), .out_13(screencontrol2_5_out_13), .out_14(screencontrol2_5_out_14),
    .out_15(screencontrol2_5_out_15), .out_16(screencontrol2_5_out_16), .out_17(screencontrol2_5_out_17),
    .out_18(screencontrol2_5_out_18), .out_19(screencontrol2_5_out_19), .out_20(screencontrol2_5_out_20),
    .out_21(screencontrol2_5_out_21));
  DotMatrix #(.inputtype("row"), .matrixcols(16), .matrixrows(16)) dotmatrix_5 (
    .row0(screencontrol2_5_out_6), .row1(screencontrol2_5_out_7), .row2(screencontrol2_5_out_8),
    .row3(screencontrol2_5_out_9), .row4(screencontrol2_5_out_10), .row5(screencontrol2_5_out_11),
    .row6(screencontrol2_5_out_12), .row7(screencontrol2_5_out_13), .row8(screencontrol2_5_out_14),
    .row9(screencontrol2_5_out_15), .row10(screencontrol2_5_out_16), .row11(screencontrol2_5_out_17),
    .row12(screencontrol2_5_out_18), .row13(screencontrol2_5_out_19), .row14(screencontrol2_5_out_20),
    .row15(screencontrol2_5_out_21));
  DotMatrix #(.inputtype("row"), .matrixcols(16), .matrixrows(16)) dotmatrix_6 (
    .row0(screencontrol2_6_out_6), .row1(screencontrol2_6_out_7), .row2(screencontrol2_6_out_8),
    .row3(screencontrol2_6_out_9), .row4(screencontrol2_6_out_10), .row5(screencontrol2_6_out_11),
    .row6(screencontrol2_6_out_12), .row7(screencontrol2_6_out_13), .row8(screencontrol2_6_out_14),
    .row9(screencontrol2_6_out_15), .row10(screencontrol2_6_out_16), .row11(screencontrol2_6_out_17),
    .row12(screencontrol2_6_out_18), .row13(screencontrol2_6_out_19), .row14(screencontrol2_6_out_20),
    .row15(screencontrol2_6_out_21));
  ScreenControl2 screencontrol2_6 (
    .CLK(and_1_out), .Data(Data), .Reset(RESET), .Enable(screenchip_1_out_2[25]), .Address(Local_Address),
    .out_6(screencontrol2_6_out_6), .out_7(screencontrol2_6_out_7), .out_8(screencontrol2_6_out_8),
    .out_9(screencontrol2_6_out_9), .out_10(screencontrol2_6_out_10), .out_11(screencontrol2_6_out_11),
    .out_12(screencontrol2_6_out_12), .out_13(screencontrol2_6_out_13), .out_14(screencontrol2_6_out_14),
    .out_15(screencontrol2_6_out_15), .out_16(screencontrol2_6_out_16), .out_17(screencontrol2_6_out_17),
    .out_18(screencontrol2_6_out_18), .out_19(screencontrol2_6_out_19), .out_20(screencontrol2_6_out_20),
    .out_21(screencontrol2_6_out_21));
  DotMatrix #(.inputtype("row"), .matrixcols(16), .matrixrows(16)) dotmatrix_7 (
    .row0(screencontrol2_7_out_6), .row1(screencontrol2_7_out_7), .row2(screencontrol2_7_out_8),
    .row3(screencontrol2_7_out_9), .row4(screencontrol2_7_out_10), .row5(screencontrol2_7_out_11),
    .row6(screencontrol2_7_out_12), .row7(screencontrol2_7_out_13), .row8(screencontrol2_7_out_14),
    .row9(screencontrol2_7_out_15), .row10(screencontrol2_7_out_16), .row11(screencontrol2_7_out_17),
    .row12(screencontrol2_7_out_18), .row13(screencontrol2_7_out_19), .row14(screencontrol2_7_out_20),
    .row15(screencontrol2_7_out_21));
  ScreenControl2 screencontrol2_7 (
    .CLK(and_1_out), .Data(Data), .Reset(RESET), .Enable(screenchip_1_out_2[26]), .Address(Local_Address),
    .out_6(screencontrol2_7_out_6), .out_7(screencontrol2_7_out_7), .out_8(screencontrol2_7_out_8),
    .out_9(screencontrol2_7_out_9), .out_10(screencontrol2_7_out_10), .out_11(screencontrol2_7_out_11),
    .out_12(screencontrol2_7_out_12), .out_13(screencontrol2_7_out_13), .out_14(screencontrol2_7_out_14),
    .out_15(screencontrol2_7_out_15), .out_16(screencontrol2_7_out_16), .out_17(screencontrol2_7_out_17),
    .out_18(screencontrol2_7_out_18), .out_19(screencontrol2_7_out_19), .out_20(screencontrol2_7_out_20),
    .out_21(screencontrol2_7_out_21));
  DotMatrix #(.inputtype("row"), .matrixcols(16), .matrixrows(16)) dotmatrix_8 (
    .row0(screencontrol2_8_out_6), .row1(screencontrol2_8_out_7), .row2(screencontrol2_8_out_8),
    .row3(screencontrol2_8_out_9), .row4(screencontrol2_8_out_10), .row5(screencontrol2_8_out_11),
    .row6(screencontrol2_8_out_12), .row7(screencontrol2_8_out_13), .row8(screencontrol2_8_out_14),
    .row9(screencontrol2_8_out_15), .row10(screencontrol2_8_out_16), .row11(screencontrol2_8_out_17),
    .row12(screencontrol2_8_out_18), .row13(screencontrol2_8_out_19), .row14(screencontrol2_8_out_20),
    .row15(screencontrol2_8_out_21));
  ScreenControl2 screencontrol2_8 (
    .CLK(and_1_out), .Data(Data), .Reset(RESET), .Enable(screenchip_1_out_2[27]), .Address(Local_Address),
    .out_6(screencontrol2_8_out_6), .out_7(screencontrol2_8_out_7), .out_8(screencontrol2_8_out_8),
    .out_9(screencontrol2_8_out_9), .out_10(screencontrol2_8_out_10), .out_11(screencontrol2_8_out_11),
    .out_12(screencontrol2_8_out_12), .out_13(screencontrol2_8_out_13), .out_14(screencontrol2_8_out_14),
    .out_15(screencontrol2_8_out_15), .out_16(screencontrol2_8_out_16), .out_17(screencontrol2_8_out_17),
    .out_18(screencontrol2_8_out_18), .out_19(screencontrol2_8_out_19), .out_20(screencontrol2_8_out_20),
    .out_21(screencontrol2_8_out_21));
  ScreenControl2 screencontrol2_9 (
    .CLK(and_1_out), .Data(Data), .Reset(RESET), .Enable(screenchip_1_out_2[20]), .Address(Local_Address),
    .out_6(screencontrol2_9_out_6), .out_7(screencontrol2_9_out_7), .out_8(screencontrol2_9_out_8),
    .out_9(screencontrol2_9_out_9), .out_10(screencontrol2_9_out_10), .out_11(screencontrol2_9_out_11),
    .out_12(screencontrol2_9_out_12), .out_13(screencontrol2_9_out_13), .out_14(screencontrol2_9_out_14),
    .out_15(screencontrol2_9_out_15), .out_16(screencontrol2_9_out_16), .out_17(screencontrol2_9_out_17),
    .out_18(screencontrol2_9_out_18), .out_19(screencontrol2_9_out_19), .out_20(screencontrol2_9_out_20),
    .out_21(screencontrol2_9_out_21));
  DotMatrix #(.inputtype("row"), .matrixcols(16), .matrixrows(16)) dotmatrix_9 (
    .row0(screencontrol2_9_out_6), .row1(screencontrol2_9_out_7), .row2(screencontrol2_9_out_8),
    .row3(screencontrol2_9_out_9), .row4(screencontrol2_9_out_10), .row5(screencontrol2_9_out_11),
    .row6(screencontrol2_9_out_12), .row7(screencontrol2_9_out_13), .row8(screencontrol2_9_out_14),
    .row9(screencontrol2_9_out_15), .row10(screencontrol2_9_out_16), .row11(screencontrol2_9_out_17),
    .row12(screencontrol2_9_out_18), .row13(screencontrol2_9_out_19), .row14(screencontrol2_9_out_20),
    .row15(screencontrol2_9_out_21));
  DotMatrix #(.inputtype("row"), .matrixcols(16), .matrixrows(16)) dotmatrix_10 (
    .row0(screencontrol2_10_out_6), .row1(screencontrol2_10_out_7), .row2(screencontrol2_10_out_8),
    .row3(screencontrol2_10_out_9), .row4(screencontrol2_10_out_10), .row5(screencontrol2_10_out_11),
    .row6(screencontrol2_10_out_12), .row7(screencontrol2_10_out_13), .row8(screencontrol2_10_out_14),
    .row9(screencontrol2_10_out_15), .row10(screencontrol2_10_out_16), .row11(screencontrol2_10_out_17),
    .row12(screencontrol2_10_out_18), .row13(screencontrol2_10_out_19), .row14(screencontrol2_10_out_20),
    .row15(screencontrol2_10_out_21));
  ScreenControl2 screencontrol2_10 (
    .CLK(and_1_out), .Data(Data), .Reset(RESET), .Enable(screenchip_1_out_2[21]), .Address(Local_Address),
    .out_6(screencontrol2_10_out_6), .out_7(screencontrol2_10_out_7), .out_8(screencontrol2_10_out_8),
    .out_9(screencontrol2_10_out_9), .out_10(screencontrol2_10_out_10), .out_11(screencontrol2_10_out_11),
    .out_12(screencontrol2_10_out_12), .out_13(screencontrol2_10_out_13), .out_14(screencontrol2_10_out_14),
    .out_15(screencontrol2_10_out_15), .out_16(screencontrol2_10_out_16), .out_17(screencontrol2_10_out_17),
    .out_18(screencontrol2_10_out_18), .out_19(screencontrol2_10_out_19), .out_20(screencontrol2_10_out_20),
    .out_21(screencontrol2_10_out_21));
  ScreenControl2 screencontrol2_11 (
    .CLK(and_1_out), .Data(Data), .Reset(RESET), .Enable(screenchip_1_out_2[22]), .Address(Local_Address),
    .out_6(screencontrol2_11_out_6), .out_7(screencontrol2_11_out_7), .out_8(screencontrol2_11_out_8),
    .out_9(screencontrol2_11_out_9), .out_10(screencontrol2_11_out_10), .out_11(screencontrol2_11_out_11),
    .out_12(screencontrol2_11_out_12), .out_13(screencontrol2_11_out_13), .out_14(screencontrol2_11_out_14),
    .out_15(screencontrol2_11_out_15), .out_16(screencontrol2_11_out_16), .out_17(screencontrol2_11_out_17),
    .out_18(screencontrol2_11_out_18), .out_19(screencontrol2_11_out_19), .out_20(screencontrol2_11_out_20),
    .out_21(screencontrol2_11_out_21));
  DotMatrix #(.inputtype("row"), .matrixcols(16), .matrixrows(16)) dotmatrix_11 (
    .row0(screencontrol2_11_out_6), .row1(screencontrol2_11_out_7), .row2(screencontrol2_11_out_8),
    .row3(screencontrol2_11_out_9), .row4(screencontrol2_11_out_10), .row5(screencontrol2_11_out_11),
    .row6(screencontrol2_11_out_12), .row7(screencontrol2_11_out_13), .row8(screencontrol2_11_out_14),
    .row9(screencontrol2_11_out_15), .row10(screencontrol2_11_out_16), .row11(screencontrol2_11_out_17),
    .row12(screencontrol2_11_out_18), .row13(screencontrol2_11_out_19), .row14(screencontrol2_11_out_20),
    .row15(screencontrol2_11_out_21));
  DotMatrix #(.inputtype("row"), .matrixcols(16), .matrixrows(16)) dotmatrix_12 (
    .row0(screencontrol2_12_out_6), .row1(screencontrol2_12_out_7), .row2(screencontrol2_12_out_8),
    .row3(screencontrol2_12_out_9), .row4(screencontrol2_12_out_10), .row5(screencontrol2_12_out_11),
    .row6(screencontrol2_12_out_12), .row7(screencontrol2_12_out_13), .row8(screencontrol2_12_out_14),
    .row9(screencontrol2_12_out_15), .row10(screencontrol2_12_out_16), .row11(screencontrol2_12_out_17),
    .row12(screencontrol2_12_out_18), .row13(screencontrol2_12_out_19), .row14(screencontrol2_12_out_20),
    .row15(screencontrol2_12_out_21));
  ScreenControl2 screencontrol2_12 (
    .CLK(and_1_out), .Data(Data), .Reset(RESET), .Enable(screenchip_1_out_2[23]), .Address(Local_Address),
    .out_6(screencontrol2_12_out_6), .out_7(screencontrol2_12_out_7), .out_8(screencontrol2_12_out_8),
    .out_9(screencontrol2_12_out_9), .out_10(screencontrol2_12_out_10), .out_11(screencontrol2_12_out_11),
    .out_12(screencontrol2_12_out_12), .out_13(screencontrol2_12_out_13), .out_14(screencontrol2_12_out_14),
    .out_15(screencontrol2_12_out_15), .out_16(screencontrol2_12_out_16), .out_17(screencontrol2_12_out_17),
    .out_18(screencontrol2_12_out_18), .out_19(screencontrol2_12_out_19), .out_20(screencontrol2_12_out_20),
    .out_21(screencontrol2_12_out_21));
  ScreenControl2 screencontrol2_13 (
    .CLK(and_1_out), .Data(Data), .Reset(RESET), .Enable(screenchip_1_out_2[16]), .Address(Local_Address),
    .out_6(screencontrol2_13_out_6), .out_7(screencontrol2_13_out_7), .out_8(screencontrol2_13_out_8),
    .out_9(screencontrol2_13_out_9), .out_10(screencontrol2_13_out_10), .out_11(screencontrol2_13_out_11),
    .out_12(screencontrol2_13_out_12), .out_13(screencontrol2_13_out_13), .out_14(screencontrol2_13_out_14),
    .out_15(screencontrol2_13_out_15), .out_16(screencontrol2_13_out_16), .out_17(screencontrol2_13_out_17),
    .out_18(screencontrol2_13_out_18), .out_19(screencontrol2_13_out_19), .out_20(screencontrol2_13_out_20),
    .out_21(screencontrol2_13_out_21));
  DotMatrix #(.inputtype("row"), .matrixcols(16), .matrixrows(16)) dotmatrix_13 (
    .row0(screencontrol2_13_out_6), .row1(screencontrol2_13_out_7), .row2(screencontrol2_13_out_8),
    .row3(screencontrol2_13_out_9), .row4(screencontrol2_13_out_10), .row5(screencontrol2_13_out_11),
    .row6(screencontrol2_13_out_12), .row7(screencontrol2_13_out_13), .row8(screencontrol2_13_out_14),
    .row9(screencontrol2_13_out_15), .row10(screencontrol2_13_out_16), .row11(screencontrol2_13_out_17),
    .row12(screencontrol2_13_out_18), .row13(screencontrol2_13_out_19), .row14(screencontrol2_13_out_20),
    .row15(screencontrol2_13_out_21));
  DotMatrix #(.inputtype("row"), .matrixcols(16), .matrixrows(16)) dotmatrix_14 (
    .row0(screencontrol2_14_out_6), .row1(screencontrol2_14_out_7), .row2(screencontrol2_14_out_8),
    .row3(screencontrol2_14_out_9), .row4(screencontrol2_14_out_10), .row5(screencontrol2_14_out_11),
    .row6(screencontrol2_14_out_12), .row7(screencontrol2_14_out_13), .row8(screencontrol2_14_out_14),
    .row9(screencontrol2_14_out_15), .row10(screencontrol2_14_out_16), .row11(screencontrol2_14_out_17),
    .row12(screencontrol2_14_out_18), .row13(screencontrol2_14_out_19), .row14(screencontrol2_14_out_20),
    .row15(screencontrol2_14_out_21));
  ScreenControl2 screencontrol2_14 (
    .CLK(and_1_out), .Data(Data), .Reset(RESET), .Enable(screenchip_1_out_2[17]), .Address(Local_Address),
    .out_6(screencontrol2_14_out_6), .out_7(screencontrol2_14_out_7), .out_8(screencontrol2_14_out_8),
    .out_9(screencontrol2_14_out_9), .out_10(screencontrol2_14_out_10), .out_11(screencontrol2_14_out_11),
    .out_12(screencontrol2_14_out_12), .out_13(screencontrol2_14_out_13), .out_14(screencontrol2_14_out_14),
    .out_15(screencontrol2_14_out_15), .out_16(screencontrol2_14_out_16), .out_17(screencontrol2_14_out_17),
    .out_18(screencontrol2_14_out_18), .out_19(screencontrol2_14_out_19), .out_20(screencontrol2_14_out_20),
    .out_21(screencontrol2_14_out_21));
  DotMatrix #(.inputtype("row"), .matrixcols(16), .matrixrows(16)) dotmatrix_15 (
    .row0(screencontrol2_15_out_6), .row1(screencontrol2_15_out_7), .row2(screencontrol2_15_out_8),
    .row3(screencontrol2_15_out_9), .row4(screencontrol2_15_out_10), .row5(screencontrol2_15_out_11),
    .row6(screencontrol2_15_out_12), .row7(screencontrol2_15_out_13), .row8(screencontrol2_15_out_14),
    .row9(screencontrol2_15_out_15), .row10(screencontrol2_15_out_16), .row11(screencontrol2_15_out_17),
    .row12(screencontrol2_15_out_18), .row13(screencontrol2_15_out_19), .row14(screencontrol2_15_out_20),
    .row15(screencontrol2_15_out_21));
  ScreenControl2 screencontrol2_15 (
    .CLK(and_1_out), .Data(Data), .Reset(RESET), .Enable(screenchip_1_out_2[18]), .Address(Local_Address),
    .out_6(screencontrol2_15_out_6), .out_7(screencontrol2_15_out_7), .out_8(screencontrol2_15_out_8),
    .out_9(screencontrol2_15_out_9), .out_10(screencontrol2_15_out_10), .out_11(screencontrol2_15_out_11),
    .out_12(screencontrol2_15_out_12), .out_13(screencontrol2_15_out_13), .out_14(screencontrol2_15_out_14),
    .out_15(screencontrol2_15_out_15), .out_16(screencontrol2_15_out_16), .out_17(screencontrol2_15_out_17),
    .out_18(screencontrol2_15_out_18), .out_19(screencontrol2_15_out_19), .out_20(screencontrol2_15_out_20),
    .out_21(screencontrol2_15_out_21));
  DotMatrix #(.inputtype("row"), .matrixcols(16), .matrixrows(16)) dotmatrix_16 (
    .row0(screencontrol2_16_out_6), .row1(screencontrol2_16_out_7), .row2(screencontrol2_16_out_8),
    .row3(screencontrol2_16_out_9), .row4(screencontrol2_16_out_10), .row5(screencontrol2_16_out_11),
    .row6(screencontrol2_16_out_12), .row7(screencontrol2_16_out_13), .row8(screencontrol2_16_out_14),
    .row9(screencontrol2_16_out_15), .row10(screencontrol2_16_out_16), .row11(screencontrol2_16_out_17),
    .row12(screencontrol2_16_out_18), .row13(screencontrol2_16_out_19), .row14(screencontrol2_16_out_20),
    .row15(screencontrol2_16_out_21));
  ScreenControl2 screencontrol2_16 (
    .CLK(and_1_out), .Data(Data), .Reset(RESET), .Enable(screenchip_1_out_2[19]), .Address(Local_Address),
    .out_6(screencontrol2_16_out_6), .out_7(screencontrol2_16_out_7), .out_8(screencontrol2_16_out_8),
    .out_9(screencontrol2_16_out_9), .out_10(screencontrol2_16_out_10), .out_11(screencontrol2_16_out_11),
    .out_12(screencontrol2_16_out_12), .out_13(screencontrol2_16_out_13), .out_14(screencontrol2_16_out_14),
    .out_15(screencontrol2_16_out_15), .out_16(screencontrol2_16_out_16), .out_17(screencontrol2_16_out_17),
    .out_18(screencontrol2_16_out_18), .out_19(screencontrol2_16_out_19), .out_20(screencontrol2_16_out_20),
    .out_21(screencontrol2_16_out_21));
  ScreenControl2 screencontrol2_17 (
    .CLK(and_1_out), .Data(Data), .Reset(RESET), .Enable(screenchip_1_out_2[12]), .Address(Local_Address),
    .out_6(screencontrol2_17_out_6), .out_7(screencontrol2_17_out_7), .out_8(screencontrol2_17_out_8),
    .out_9(screencontrol2_17_out_9), .out_10(screencontrol2_17_out_10), .out_11(screencontrol2_17_out_11),
    .out_12(screencontrol2_17_out_12), .out_13(screencontrol2_17_out_13), .out_14(screencontrol2_17_out_14),
    .out_15(screencontrol2_17_out_15), .out_16(screencontrol2_17_out_16), .out_17(screencontrol2_17_out_17),
    .out_18(screencontrol2_17_out_18), .out_19(screencontrol2_17_out_19), .out_20(screencontrol2_17_out_20),
    .out_21(screencontrol2_17_out_21));
  DotMatrix #(.inputtype("row"), .matrixcols(16), .matrixrows(16)) dotmatrix_17 (
    .row0(screencontrol2_17_out_6), .row1(screencontrol2_17_out_7), .row2(screencontrol2_17_out_8),
    .row3(screencontrol2_17_out_9), .row4(screencontrol2_17_out_10), .row5(screencontrol2_17_out_11),
    .row6(screencontrol2_17_out_12), .row7(screencontrol2_17_out_13), .row8(screencontrol2_17_out_14),
    .row9(screencontrol2_17_out_15), .row10(screencontrol2_17_out_16), .row11(screencontrol2_17_out_17),
    .row12(screencontrol2_17_out_18), .row13(screencontrol2_17_out_19), .row14(screencontrol2_17_out_20),
    .row15(screencontrol2_17_out_21));
  DotMatrix #(.inputtype("row"), .matrixcols(16), .matrixrows(16)) dotmatrix_18 (
    .row0(screencontrol2_18_out_6), .row1(screencontrol2_18_out_7), .row2(screencontrol2_18_out_8),
    .row3(screencontrol2_18_out_9), .row4(screencontrol2_18_out_10), .row5(screencontrol2_18_out_11),
    .row6(screencontrol2_18_out_12), .row7(screencontrol2_18_out_13), .row8(screencontrol2_18_out_14),
    .row9(screencontrol2_18_out_15), .row10(screencontrol2_18_out_16), .row11(screencontrol2_18_out_17),
    .row12(screencontrol2_18_out_18), .row13(screencontrol2_18_out_19), .row14(screencontrol2_18_out_20),
    .row15(screencontrol2_18_out_21));
  ScreenControl2 screencontrol2_18 (
    .CLK(and_1_out), .Data(Data), .Reset(RESET), .Enable(screenchip_1_out_2[13]), .Address(Local_Address),
    .out_6(screencontrol2_18_out_6), .out_7(screencontrol2_18_out_7), .out_8(screencontrol2_18_out_8),
    .out_9(screencontrol2_18_out_9), .out_10(screencontrol2_18_out_10), .out_11(screencontrol2_18_out_11),
    .out_12(screencontrol2_18_out_12), .out_13(screencontrol2_18_out_13), .out_14(screencontrol2_18_out_14),
    .out_15(screencontrol2_18_out_15), .out_16(screencontrol2_18_out_16), .out_17(screencontrol2_18_out_17),
    .out_18(screencontrol2_18_out_18), .out_19(screencontrol2_18_out_19), .out_20(screencontrol2_18_out_20),
    .out_21(screencontrol2_18_out_21));
  ScreenControl2 screencontrol2_19 (
    .CLK(and_1_out), .Data(Data), .Reset(RESET), .Enable(screenchip_1_out_2[14]), .Address(Local_Address),
    .out_6(screencontrol2_19_out_6), .out_7(screencontrol2_19_out_7), .out_8(screencontrol2_19_out_8),
    .out_9(screencontrol2_19_out_9), .out_10(screencontrol2_19_out_10), .out_11(screencontrol2_19_out_11),
    .out_12(screencontrol2_19_out_12), .out_13(screencontrol2_19_out_13), .out_14(screencontrol2_19_out_14),
    .out_15(screencontrol2_19_out_15), .out_16(screencontrol2_19_out_16), .out_17(screencontrol2_19_out_17),
    .out_18(screencontrol2_19_out_18), .out_19(screencontrol2_19_out_19), .out_20(screencontrol2_19_out_20),
    .out_21(screencontrol2_19_out_21));
  DotMatrix #(.inputtype("row"), .matrixcols(16), .matrixrows(16)) dotmatrix_19 (
    .row0(screencontrol2_19_out_6), .row1(screencontrol2_19_out_7), .row2(screencontrol2_19_out_8),
    .row3(screencontrol2_19_out_9), .row4(screencontrol2_19_out_10), .row5(screencontrol2_19_out_11),
    .row6(screencontrol2_19_out_12), .row7(screencontrol2_19_out_13), .row8(screencontrol2_19_out_14),
    .row9(screencontrol2_19_out_15), .row10(screencontrol2_19_out_16), .row11(screencontrol2_19_out_17),
    .row12(screencontrol2_19_out_18), .row13(screencontrol2_19_out_19), .row14(screencontrol2_19_out_20),
    .row15(screencontrol2_19_out_21));
  DotMatrix #(.inputtype("row"), .matrixcols(16), .matrixrows(16)) dotmatrix_20 (
    .row0(screencontrol2_20_out_6), .row1(screencontrol2_20_out_7), .row2(screencontrol2_20_out_8),
    .row3(screencontrol2_20_out_9), .row4(screencontrol2_20_out_10), .row5(screencontrol2_20_out_11),
    .row6(screencontrol2_20_out_12), .row7(screencontrol2_20_out_13), .row8(screencontrol2_20_out_14),
    .row9(screencontrol2_20_out_15), .row10(screencontrol2_20_out_16), .row11(screencontrol2_20_out_17),
    .row12(screencontrol2_20_out_18), .row13(screencontrol2_20_out_19), .row14(screencontrol2_20_out_20),
    .row15(screencontrol2_20_out_21));
  ScreenControl2 screencontrol2_20 (
    .CLK(and_1_out), .Data(Data), .Reset(RESET), .Enable(screenchip_1_out_2[15]), .Address(Local_Address),
    .out_6(screencontrol2_20_out_6), .out_7(screencontrol2_20_out_7), .out_8(screencontrol2_20_out_8),
    .out_9(screencontrol2_20_out_9), .out_10(screencontrol2_20_out_10), .out_11(screencontrol2_20_out_11),
    .out_12(screencontrol2_20_out_12), .out_13(screencontrol2_20_out_13), .out_14(screencontrol2_20_out_14),
    .out_15(screencontrol2_20_out_15), .out_16(screencontrol2_20_out_16), .out_17(screencontrol2_20_out_17),
    .out_18(screencontrol2_20_out_18), .out_19(screencontrol2_20_out_19), .out_20(screencontrol2_20_out_20),
    .out_21(screencontrol2_20_out_21));
  ScreenControl2 screencontrol2_21 (
    .CLK(and_1_out), .Data(Data), .Reset(RESET), .Enable(screenchip_1_out_2[8]), .Address(Local_Address),
    .out_6(screencontrol2_21_out_6), .out_7(screencontrol2_21_out_7), .out_8(screencontrol2_21_out_8),
    .out_9(screencontrol2_21_out_9), .out_10(screencontrol2_21_out_10), .out_11(screencontrol2_21_out_11),
    .out_12(screencontrol2_21_out_12), .out_13(screencontrol2_21_out_13), .out_14(screencontrol2_21_out_14),
    .out_15(screencontrol2_21_out_15), .out_16(screencontrol2_21_out_16), .out_17(screencontrol2_21_out_17),
    .out_18(screencontrol2_21_out_18), .out_19(screencontrol2_21_out_19), .out_20(screencontrol2_21_out_20),
    .out_21(screencontrol2_21_out_21));
  DotMatrix #(.inputtype("row"), .matrixcols(16), .matrixrows(16)) dotmatrix_21 (
    .row0(screencontrol2_21_out_6), .row1(screencontrol2_21_out_7), .row2(screencontrol2_21_out_8),
    .row3(screencontrol2_21_out_9), .row4(screencontrol2_21_out_10), .row5(screencontrol2_21_out_11),
    .row6(screencontrol2_21_out_12), .row7(screencontrol2_21_out_13), .row8(screencontrol2_21_out_14),
    .row9(screencontrol2_21_out_15), .row10(screencontrol2_21_out_16), .row11(screencontrol2_21_out_17),
    .row12(screencontrol2_21_out_18), .row13(screencontrol2_21_out_19), .row14(screencontrol2_21_out_20),
    .row15(screencontrol2_21_out_21));
  ScreenControl2 screencontrol2_22 (
    .CLK(and_1_out), .Data(Data), .Reset(RESET), .Enable(screenchip_1_out_2[9]), .Address(Local_Address),
    .out_6(screencontrol2_22_out_6), .out_7(screencontrol2_22_out_7), .out_8(screencontrol2_22_out_8),
    .out_9(screencontrol2_22_out_9), .out_10(screencontrol2_22_out_10), .out_11(screencontrol2_22_out_11),
    .out_12(screencontrol2_22_out_12), .out_13(screencontrol2_22_out_13), .out_14(screencontrol2_22_out_14),
    .out_15(screencontrol2_22_out_15), .out_16(screencontrol2_22_out_16), .out_17(screencontrol2_22_out_17),
    .out_18(screencontrol2_22_out_18), .out_19(screencontrol2_22_out_19), .out_20(screencontrol2_22_out_20),
    .out_21(screencontrol2_22_out_21));
  DotMatrix #(.inputtype("row"), .matrixcols(16), .matrixrows(16)) dotmatrix_22 (
    .row0(screencontrol2_22_out_6), .row1(screencontrol2_22_out_7), .row2(screencontrol2_22_out_8),
    .row3(screencontrol2_22_out_9), .row4(screencontrol2_22_out_10), .row5(screencontrol2_22_out_11),
    .row6(screencontrol2_22_out_12), .row7(screencontrol2_22_out_13), .row8(screencontrol2_22_out_14),
    .row9(screencontrol2_22_out_15), .row10(screencontrol2_22_out_16), .row11(screencontrol2_22_out_17),
    .row12(screencontrol2_22_out_18), .row13(screencontrol2_22_out_19), .row14(screencontrol2_22_out_20),
    .row15(screencontrol2_22_out_21));
  DotMatrix #(.inputtype("row"), .matrixcols(16), .matrixrows(16)) dotmatrix_23 (
    .row0(screencontrol2_23_out_6), .row1(screencontrol2_23_out_7), .row2(screencontrol2_23_out_8),
    .row3(screencontrol2_23_out_9), .row4(screencontrol2_23_out_10), .row5(screencontrol2_23_out_11),
    .row6(screencontrol2_23_out_12), .row7(screencontrol2_23_out_13), .row8(screencontrol2_23_out_14),
    .row9(screencontrol2_23_out_15), .row10(screencontrol2_23_out_16), .row11(screencontrol2_23_out_17),
    .row12(screencontrol2_23_out_18), .row13(screencontrol2_23_out_19), .row14(screencontrol2_23_out_20),
    .row15(screencontrol2_23_out_21));
  ScreenControl2 screencontrol2_23 (
    .CLK(and_1_out), .Data(Data), .Reset(RESET), .Enable(screenchip_1_out_2[10]), .Address(Local_Address),
    .out_6(screencontrol2_23_out_6), .out_7(screencontrol2_23_out_7), .out_8(screencontrol2_23_out_8),
    .out_9(screencontrol2_23_out_9), .out_10(screencontrol2_23_out_10), .out_11(screencontrol2_23_out_11),
    .out_12(screencontrol2_23_out_12), .out_13(screencontrol2_23_out_13), .out_14(screencontrol2_23_out_14),
    .out_15(screencontrol2_23_out_15), .out_16(screencontrol2_23_out_16), .out_17(screencontrol2_23_out_17),
    .out_18(screencontrol2_23_out_18), .out_19(screencontrol2_23_out_19), .out_20(screencontrol2_23_out_20),
    .out_21(screencontrol2_23_out_21));
  DotMatrix #(.inputtype("row"), .matrixcols(16), .matrixrows(16)) dotmatrix_24 (
    .row0(screencontrol2_24_out_6), .row1(screencontrol2_24_out_7), .row2(screencontrol2_24_out_8),
    .row3(screencontrol2_24_out_9), .row4(screencontrol2_24_out_10), .row5(screencontrol2_24_out_11),
    .row6(screencontrol2_24_out_12), .row7(screencontrol2_24_out_13), .row8(screencontrol2_24_out_14),
    .row9(screencontrol2_24_out_15), .row10(screencontrol2_24_out_16), .row11(screencontrol2_24_out_17),
    .row12(screencontrol2_24_out_18), .row13(screencontrol2_24_out_19), .row14(screencontrol2_24_out_20),
    .row15(screencontrol2_24_out_21));
  ScreenControl2 screencontrol2_24 (
    .CLK(and_1_out), .Data(Data), .Reset(RESET), .Enable(screenchip_1_out_2[11]), .Address(Local_Address),
    .out_6(screencontrol2_24_out_6), .out_7(screencontrol2_24_out_7), .out_8(screencontrol2_24_out_8),
    .out_9(screencontrol2_24_out_9), .out_10(screencontrol2_24_out_10), .out_11(screencontrol2_24_out_11),
    .out_12(screencontrol2_24_out_12), .out_13(screencontrol2_24_out_13), .out_14(screencontrol2_24_out_14),
    .out_15(screencontrol2_24_out_15), .out_16(screencontrol2_24_out_16), .out_17(screencontrol2_24_out_17),
    .out_18(screencontrol2_24_out_18), .out_19(screencontrol2_24_out_19), .out_20(screencontrol2_24_out_20),
    .out_21(screencontrol2_24_out_21));
  DotMatrix #(.inputtype("row"), .matrixcols(16), .matrixrows(16)) dotmatrix_25 (
    .row0(screencontrol2_25_out_6), .row1(screencontrol2_25_out_7), .row2(screencontrol2_25_out_8),
    .row3(screencontrol2_25_out_9), .row4(screencontrol2_25_out_10), .row5(screencontrol2_25_out_11),
    .row6(screencontrol2_25_out_12), .row7(screencontrol2_25_out_13), .row8(screencontrol2_25_out_14),
    .row9(screencontrol2_25_out_15), .row10(screencontrol2_25_out_16), .row11(screencontrol2_25_out_17),
    .row12(screencontrol2_25_out_18), .row13(screencontrol2_25_out_19), .row14(screencontrol2_25_out_20),
    .row15(screencontrol2_25_out_21));
  ScreenControl2 screencontrol2_25 (
    .CLK(and_1_out), .Data(Data), .Reset(RESET), .Enable(screenchip_1_out_2[4]), .Address(Local_Address),
    .out_6(screencontrol2_25_out_6), .out_7(screencontrol2_25_out_7), .out_8(screencontrol2_25_out_8),
    .out_9(screencontrol2_25_out_9), .out_10(screencontrol2_25_out_10), .out_11(screencontrol2_25_out_11),
    .out_12(screencontrol2_25_out_12), .out_13(screencontrol2_25_out_13), .out_14(screencontrol2_25_out_14),
    .out_15(screencontrol2_25_out_15), .out_16(screencontrol2_25_out_16), .out_17(screencontrol2_25_out_17),
    .out_18(screencontrol2_25_out_18), .out_19(screencontrol2_25_out_19), .out_20(screencontrol2_25_out_20),
    .out_21(screencontrol2_25_out_21));
  ScreenControl2 screencontrol2_26 (
    .CLK(and_1_out), .Data(Data), .Reset(RESET), .Enable(screenchip_1_out_2[5]), .Address(Local_Address),
    .out_6(screencontrol2_26_out_6), .out_7(screencontrol2_26_out_7), .out_8(screencontrol2_26_out_8),
    .out_9(screencontrol2_26_out_9), .out_10(screencontrol2_26_out_10), .out_11(screencontrol2_26_out_11),
    .out_12(screencontrol2_26_out_12), .out_13(screencontrol2_26_out_13), .out_14(screencontrol2_26_out_14),
    .out_15(screencontrol2_26_out_15), .out_16(screencontrol2_26_out_16), .out_17(screencontrol2_26_out_17),
    .out_18(screencontrol2_26_out_18), .out_19(screencontrol2_26_out_19), .out_20(screencontrol2_26_out_20),
    .out_21(screencontrol2_26_out_21));
  DotMatrix #(.inputtype("row"), .matrixcols(16), .matrixrows(16)) dotmatrix_26 (
    .row0(screencontrol2_26_out_6), .row1(screencontrol2_26_out_7), .row2(screencontrol2_26_out_8),
    .row3(screencontrol2_26_out_9), .row4(screencontrol2_26_out_10), .row5(screencontrol2_26_out_11),
    .row6(screencontrol2_26_out_12), .row7(screencontrol2_26_out_13), .row8(screencontrol2_26_out_14),
    .row9(screencontrol2_26_out_15), .row10(screencontrol2_26_out_16), .row11(screencontrol2_26_out_17),
    .row12(screencontrol2_26_out_18), .row13(screencontrol2_26_out_19), .row14(screencontrol2_26_out_20),
    .row15(screencontrol2_26_out_21));
  ScreenControl2 screencontrol2_27 (
    .CLK(and_1_out), .Data(Data), .Reset(RESET), .Enable(screenchip_1_out_2[6]), .Address(Local_Address),
    .out_6(screencontrol2_27_out_6), .out_7(screencontrol2_27_out_7), .out_8(screencontrol2_27_out_8),
    .out_9(screencontrol2_27_out_9), .out_10(screencontrol2_27_out_10), .out_11(screencontrol2_27_out_11),
    .out_12(screencontrol2_27_out_12), .out_13(screencontrol2_27_out_13), .out_14(screencontrol2_27_out_14),
    .out_15(screencontrol2_27_out_15), .out_16(screencontrol2_27_out_16), .out_17(screencontrol2_27_out_17),
    .out_18(screencontrol2_27_out_18), .out_19(screencontrol2_27_out_19), .out_20(screencontrol2_27_out_20),
    .out_21(screencontrol2_27_out_21));
  DotMatrix #(.inputtype("row"), .matrixcols(16), .matrixrows(16)) dotmatrix_27 (
    .row0(screencontrol2_27_out_6), .row1(screencontrol2_27_out_7), .row2(screencontrol2_27_out_8),
    .row3(screencontrol2_27_out_9), .row4(screencontrol2_27_out_10), .row5(screencontrol2_27_out_11),
    .row6(screencontrol2_27_out_12), .row7(screencontrol2_27_out_13), .row8(screencontrol2_27_out_14),
    .row9(screencontrol2_27_out_15), .row10(screencontrol2_27_out_16), .row11(screencontrol2_27_out_17),
    .row12(screencontrol2_27_out_18), .row13(screencontrol2_27_out_19), .row14(screencontrol2_27_out_20),
    .row15(screencontrol2_27_out_21));
  ScreenControl2 screencontrol2_28 (
    .CLK(and_1_out), .Data(Data), .Reset(RESET), .Enable(screenchip_1_out_2[7]), .Address(Local_Address),
    .out_6(screencontrol2_28_out_6), .out_7(screencontrol2_28_out_7), .out_8(screencontrol2_28_out_8),
    .out_9(screencontrol2_28_out_9), .out_10(screencontrol2_28_out_10), .out_11(screencontrol2_28_out_11),
    .out_12(screencontrol2_28_out_12), .out_13(screencontrol2_28_out_13), .out_14(screencontrol2_28_out_14),
    .out_15(screencontrol2_28_out_15), .out_16(screencontrol2_28_out_16), .out_17(screencontrol2_28_out_17),
    .out_18(screencontrol2_28_out_18), .out_19(screencontrol2_28_out_19), .out_20(screencontrol2_28_out_20),
    .out_21(screencontrol2_28_out_21));
  DotMatrix #(.inputtype("row"), .matrixcols(16), .matrixrows(16)) dotmatrix_28 (
    .row0(screencontrol2_28_out_6), .row1(screencontrol2_28_out_7), .row2(screencontrol2_28_out_8),
    .row3(screencontrol2_28_out_9), .row4(screencontrol2_28_out_10), .row5(screencontrol2_28_out_11),
    .row6(screencontrol2_28_out_12), .row7(screencontrol2_28_out_13), .row8(screencontrol2_28_out_14),
    .row9(screencontrol2_28_out_15), .row10(screencontrol2_28_out_16), .row11(screencontrol2_28_out_17),
    .row12(screencontrol2_28_out_18), .row13(screencontrol2_28_out_19), .row14(screencontrol2_28_out_20),
    .row15(screencontrol2_28_out_21));
  ScreenControl2 screencontrol2_29 (
    .CLK(and_1_out), .Data(Data), .Reset(RESET), .Enable(screenchip_1_out_3[0]), .Address(Local_Address),
    .out_6(screencontrol2_29_out_6), .out_7(screencontrol2_29_out_7), .out_8(screencontrol2_29_out_8),
    .out_9(screencontrol2_29_out_9), .out_10(screencontrol2_29_out_10), .out_11(screencontrol2_29_out_11),
    .out_12(screencontrol2_29_out_12), .out_13(screencontrol2_29_out_13), .out_14(screencontrol2_29_out_14),
    .out_15(screencontrol2_29_out_15), .out_16(screencontrol2_29_out_16), .out_17(screencontrol2_29_out_17),
    .out_18(screencontrol2_29_out_18), .out_19(screencontrol2_29_out_19), .out_20(screencontrol2_29_out_20),
    .out_21(screencontrol2_29_out_21));
  DotMatrix #(.inputtype("row"), .matrixcols(16), .matrixrows(16)) dotmatrix_29 (
    .row0(screencontrol2_29_out_6), .row1(screencontrol2_29_out_7), .row2(screencontrol2_29_out_8),
    .row3(screencontrol2_29_out_9), .row4(screencontrol2_29_out_10), .row5(screencontrol2_29_out_11),
    .row6(screencontrol2_29_out_12), .row7(screencontrol2_29_out_13), .row8(screencontrol2_29_out_14),
    .row9(screencontrol2_29_out_15), .row10(screencontrol2_29_out_16), .row11(screencontrol2_29_out_17),
    .row12(screencontrol2_29_out_18), .row13(screencontrol2_29_out_19), .row14(screencontrol2_29_out_20),
    .row15(screencontrol2_29_out_21));
  DotMatrix #(.inputtype("row"), .matrixcols(16), .matrixrows(16)) dotmatrix_30 (
    .row0(screencontrol2_30_out_6), .row1(screencontrol2_30_out_7), .row2(screencontrol2_30_out_8),
    .row3(screencontrol2_30_out_9), .row4(screencontrol2_30_out_10), .row5(screencontrol2_30_out_11),
    .row6(screencontrol2_30_out_12), .row7(screencontrol2_30_out_13), .row8(screencontrol2_30_out_14),
    .row9(screencontrol2_30_out_15), .row10(screencontrol2_30_out_16), .row11(screencontrol2_30_out_17),
    .row12(screencontrol2_30_out_18), .row13(screencontrol2_30_out_19), .row14(screencontrol2_30_out_20),
    .row15(screencontrol2_30_out_21));
  ScreenControl2 screencontrol2_30 (
    .CLK(and_1_out), .Data(Data), .Reset(RESET), .Enable(screenchip_1_out_3[1]), .Address(Local_Address),
    .out_6(screencontrol2_30_out_6), .out_7(screencontrol2_30_out_7), .out_8(screencontrol2_30_out_8),
    .out_9(screencontrol2_30_out_9), .out_10(screencontrol2_30_out_10), .out_11(screencontrol2_30_out_11),
    .out_12(screencontrol2_30_out_12), .out_13(screencontrol2_30_out_13), .out_14(screencontrol2_30_out_14),
    .out_15(screencontrol2_30_out_15), .out_16(screencontrol2_30_out_16), .out_17(screencontrol2_30_out_17),
    .out_18(screencontrol2_30_out_18), .out_19(screencontrol2_30_out_19), .out_20(screencontrol2_30_out_20),
    .out_21(screencontrol2_30_out_21));
  DotMatrix #(.inputtype("row"), .matrixcols(16), .matrixrows(16)) dotmatrix_31 (
    .row0(screencontrol2_31_out_6), .row1(screencontrol2_31_out_7), .row2(screencontrol2_31_out_8),
    .row3(screencontrol2_31_out_9), .row4(screencontrol2_31_out_10), .row5(screencontrol2_31_out_11),
    .row6(screencontrol2_31_out_12), .row7(screencontrol2_31_out_13), .row8(screencontrol2_31_out_14),
    .row9(screencontrol2_31_out_15), .row10(screencontrol2_31_out_16), .row11(screencontrol2_31_out_17),
    .row12(screencontrol2_31_out_18), .row13(screencontrol2_31_out_19), .row14(screencontrol2_31_out_20),
    .row15(screencontrol2_31_out_21));
  ScreenControl2 screencontrol2_31 (
    .CLK(and_1_out), .Data(Data), .Reset(RESET), .Enable(screenchip_1_out_3[2]), .Address(Local_Address),
    .out_6(screencontrol2_31_out_6), .out_7(screencontrol2_31_out_7), .out_8(screencontrol2_31_out_8),
    .out_9(screencontrol2_31_out_9), .out_10(screencontrol2_31_out_10), .out_11(screencontrol2_31_out_11),
    .out_12(screencontrol2_31_out_12), .out_13(screencontrol2_31_out_13), .out_14(screencontrol2_31_out_14),
    .out_15(screencontrol2_31_out_15), .out_16(screencontrol2_31_out_16), .out_17(screencontrol2_31_out_17),
    .out_18(screencontrol2_31_out_18), .out_19(screencontrol2_31_out_19), .out_20(screencontrol2_31_out_20),
    .out_21(screencontrol2_31_out_21));
  DotMatrix #(.inputtype("row"), .matrixcols(16), .matrixrows(16)) dotmatrix_32 (
    .row0(screencontrol2_32_out_6), .row1(screencontrol2_32_out_7), .row2(screencontrol2_32_out_8),
    .row3(screencontrol2_32_out_9), .row4(screencontrol2_32_out_10), .row5(screencontrol2_32_out_11),
    .row6(screencontrol2_32_out_12), .row7(screencontrol2_32_out_13), .row8(screencontrol2_32_out_14),
    .row9(screencontrol2_32_out_15), .row10(screencontrol2_32_out_16), .row11(screencontrol2_32_out_17),
    .row12(screencontrol2_32_out_18), .row13(screencontrol2_32_out_19), .row14(screencontrol2_32_out_20),
    .row15(screencontrol2_32_out_21));
  ScreenControl2 screencontrol2_32 (
    .CLK(and_1_out), .Data(Data), .Reset(RESET), .Enable(screenchip_1_out_3[3]), .Address(Local_Address),
    .out_6(screencontrol2_32_out_6), .out_7(screencontrol2_32_out_7), .out_8(screencontrol2_32_out_8),
    .out_9(screencontrol2_32_out_9), .out_10(screencontrol2_32_out_10), .out_11(screencontrol2_32_out_11),
    .out_12(screencontrol2_32_out_12), .out_13(screencontrol2_32_out_13), .out_14(screencontrol2_32_out_14),
    .out_15(screencontrol2_32_out_15), .out_16(screencontrol2_32_out_16), .out_17(screencontrol2_32_out_17),
    .out_18(screencontrol2_32_out_18), .out_19(screencontrol2_32_out_19), .out_20(screencontrol2_32_out_20),
    .out_21(screencontrol2_32_out_21));

  // Notes on the sheet:
  //   Screen Offset
  //   Screen Size
endmodule

module ScreenControl2 (
  input  [15:0] Data,
  input  CLK,
  input  Reset,
  input  Enable,
  input  [15:0] Address,
  output [15:0] out_6,
  output [15:0] out_7,
  output [15:0] out_8,
  output [15:0] out_9,
  output [15:0] out_10,
  output [15:0] out_11,
  output [15:0] out_12,
  output [15:0] out_13,
  output [15:0] out_14,
  output [15:0] out_15,
  output [15:0] out_16,
  output [15:0] out_17,
  output [15:0] out_18,
  output [15:0] out_19,
  output [15:0] out_20,
  output [15:0] out_21
);

  wire and_1_out, and_2_out, and_3_out, and_4_out, and_5_out, and_6_out, and_7_out, and_8_out, and_9_out,
       and_10_out, and_11_out, and_12_out, and_13_out, and_14_out, and_15_out, and_16_out;
  wire [3:0] decoder_1_out0, decoder_1_out4, decoder_1_out8, decoder_1_out12;

  Decoder #(.select(4), .enable("false")) decoder_1 (
    .out0(decoder_1_out0[0]), .out1(decoder_1_out0[1]), .out2(decoder_1_out0[2]), .out3(decoder_1_out0[3]),
    .out4(decoder_1_out4[0]), .out5(decoder_1_out4[1]), .out6(decoder_1_out4[2]), .out7(decoder_1_out4[3]),
    .out8(decoder_1_out8[0]), .out9(decoder_1_out8[1]), .out10(decoder_1_out8[2]), .out11(decoder_1_out8[3]),
    .out12(decoder_1_out12[0]), .out13(decoder_1_out12[1]), .out14(decoder_1_out12[2]),
    .out15(decoder_1_out12[3]), .sel(Address[3:0]));
  and and_1 (and_1_out, Enable, decoder_1_out0[0]);
  and and_2 (and_2_out, Enable, decoder_1_out0[1]);
  and and_3 (and_3_out, Enable, decoder_1_out0[2]);
  and and_4 (and_4_out, Enable, decoder_1_out0[3]);
  and and_5 (and_5_out, Enable, decoder_1_out4[0]);
  and and_6 (and_6_out, Enable, decoder_1_out4[1]);
  and and_7 (and_7_out, Enable, decoder_1_out4[2]);
  and and_8 (and_8_out, Enable, decoder_1_out4[3]);
  and and_9 (and_9_out, Enable, decoder_1_out8[0]);
  and and_10 (and_10_out, Enable, decoder_1_out8[1]);
  and and_11 (and_11_out, Enable, decoder_1_out8[2]);
  and and_12 (and_12_out, Enable, decoder_1_out8[3]);
  and and_13 (and_13_out, Enable, decoder_1_out12[0]);
  and and_14 (and_14_out, Enable, decoder_1_out12[1]);
  and and_15 (and_15_out, Enable, decoder_1_out12[2]);
  and and_16 (and_16_out, Enable, decoder_1_out12[3]);
  Register #(.width(16)) register_1 (
    .D({Data[0], Data[1], Data[2], Data[3], Data[4], Data[5], Data[6], Data[7], Data[8], Data[9], Data[10], Data[11], Data[12], Data[13], Data[14], Data[15]}),
    .en(and_1_out), .Q(out_6), .clk(CLK), .clr(Reset));
  Register #(.width(16)) register_2 (
    .D({Data[0], Data[1], Data[2], Data[3], Data[4], Data[5], Data[6], Data[7], Data[8], Data[9], Data[10], Data[11], Data[12], Data[13], Data[14], Data[15]}),
    .en(and_2_out), .Q(out_7), .clk(CLK), .clr(Reset));
  Register #(.width(16)) register_3 (
    .D({Data[0], Data[1], Data[2], Data[3], Data[4], Data[5], Data[6], Data[7], Data[8], Data[9], Data[10], Data[11], Data[12], Data[13], Data[14], Data[15]}),
    .en(and_3_out), .Q(out_8), .clk(CLK), .clr(Reset));
  Register #(.width(16)) register_4 (
    .D({Data[0], Data[1], Data[2], Data[3], Data[4], Data[5], Data[6], Data[7], Data[8], Data[9], Data[10], Data[11], Data[12], Data[13], Data[14], Data[15]}),
    .en(and_4_out), .Q(out_9), .clk(CLK), .clr(Reset));
  Register #(.width(16)) register_5 (
    .D({Data[0], Data[1], Data[2], Data[3], Data[4], Data[5], Data[6], Data[7], Data[8], Data[9], Data[10], Data[11], Data[12], Data[13], Data[14], Data[15]}),
    .en(and_5_out), .Q(out_10), .clk(CLK), .clr(Reset));
  Register #(.width(16)) register_6 (
    .D({Data[0], Data[1], Data[2], Data[3], Data[4], Data[5], Data[6], Data[7], Data[8], Data[9], Data[10], Data[11], Data[12], Data[13], Data[14], Data[15]}),
    .en(and_6_out), .Q(out_11), .clk(CLK), .clr(Reset));
  Register #(.width(16)) register_7 (
    .D({Data[0], Data[1], Data[2], Data[3], Data[4], Data[5], Data[6], Data[7], Data[8], Data[9], Data[10], Data[11], Data[12], Data[13], Data[14], Data[15]}),
    .en(and_7_out), .Q(out_12), .clk(CLK), .clr(Reset));
  Register #(.width(16)) register_8 (
    .D({Data[0], Data[1], Data[2], Data[3], Data[4], Data[5], Data[6], Data[7], Data[8], Data[9], Data[10], Data[11], Data[12], Data[13], Data[14], Data[15]}),
    .en(and_8_out), .Q(out_13), .clk(CLK), .clr(Reset));
  Register #(.width(16)) register_9 (
    .D({Data[0], Data[1], Data[2], Data[3], Data[4], Data[5], Data[6], Data[7], Data[8], Data[9], Data[10], Data[11], Data[12], Data[13], Data[14], Data[15]}),
    .en(and_9_out), .Q(out_14), .clk(CLK), .clr(Reset));
  Register #(.width(16)) register_10 (
    .D({Data[0], Data[1], Data[2], Data[3], Data[4], Data[5], Data[6], Data[7], Data[8], Data[9], Data[10], Data[11], Data[12], Data[13], Data[14], Data[15]}),
    .en(and_10_out), .Q(out_15), .clk(CLK), .clr(Reset));
  Register #(.width(16)) register_11 (
    .D({Data[0], Data[1], Data[2], Data[3], Data[4], Data[5], Data[6], Data[7], Data[8], Data[9], Data[10], Data[11], Data[12], Data[13], Data[14], Data[15]}),
    .en(and_11_out), .Q(out_16), .clk(CLK), .clr(Reset));
  Register #(.width(16)) register_12 (
    .D({Data[0], Data[1], Data[2], Data[3], Data[4], Data[5], Data[6], Data[7], Data[8], Data[9], Data[10], Data[11], Data[12], Data[13], Data[14], Data[15]}),
    .en(and_12_out), .Q(out_17), .clk(CLK), .clr(Reset));
  Register #(.width(16)) register_13 (
    .D({Data[0], Data[1], Data[2], Data[3], Data[4], Data[5], Data[6], Data[7], Data[8], Data[9], Data[10], Data[11], Data[12], Data[13], Data[14], Data[15]}),
    .en(and_13_out), .Q(out_18), .clk(CLK), .clr(Reset));
  Register #(.width(16)) register_14 (
    .D({Data[0], Data[1], Data[2], Data[3], Data[4], Data[5], Data[6], Data[7], Data[8], Data[9], Data[10], Data[11], Data[12], Data[13], Data[14], Data[15]}),
    .en(and_14_out), .Q(out_19), .clk(CLK), .clr(Reset));
  Register #(.width(16)) register_15 (
    .D({Data[0], Data[1], Data[2], Data[3], Data[4], Data[5], Data[6], Data[7], Data[8], Data[9], Data[10], Data[11], Data[12], Data[13], Data[14], Data[15]}),
    .en(and_15_out), .Q(out_20), .clk(CLK), .clr(Reset));
  Register #(.width(16)) register_16 (
    .D({Data[0], Data[1], Data[2], Data[3], Data[4], Data[5], Data[6], Data[7], Data[8], Data[9], Data[10], Data[11], Data[12], Data[13], Data[14], Data[15]}),
    .en(and_16_out), .Q(out_21), .clk(CLK), .clr(Reset));

  // Other names for the same wires on the sheet: RST = Reset
endmodule

module ScreenControlTest (
  input  [15:0] Data,
  input  CLK,
  input  Reset,
  input  Enable,
  input  [15:0] Address,
  output [15:0] out_6,
  output [15:0] out_7,
  output [15:0] out_8,
  output [15:0] out_9,
  output [15:0] out_10,
  output [15:0] out_11,
  output [15:0] out_12,
  output [15:0] out_13,
  output [15:0] out_14,
  output [15:0] out_15,
  output [15:0] out_16,
  output [15:0] out_17,
  output [15:0] out_18,
  output [15:0] out_19,
  output [15:0] out_20,
  output [15:0] out_21
);

  wire and_1_out, and_2_out, and_3_out, and_4_out, and_5_out, and_6_out, and_7_out, and_8_out, and_9_out,
       and_10_out, and_11_out, and_12_out, and_13_out, and_14_out, and_15_out, and_16_out;
  wire [3:0] decoder_1_out0, decoder_1_out4, decoder_1_out8, decoder_1_out12;

  Decoder #(.select(4), .enable("false")) decoder_1 (
    .out0(decoder_1_out0[0]), .out1(decoder_1_out0[1]), .out2(decoder_1_out0[2]), .out3(decoder_1_out0[3]),
    .out4(decoder_1_out4[0]), .out5(decoder_1_out4[1]), .out6(decoder_1_out4[2]), .out7(decoder_1_out4[3]),
    .out8(decoder_1_out8[0]), .out9(decoder_1_out8[1]), .out10(decoder_1_out8[2]), .out11(decoder_1_out8[3]),
    .out12(decoder_1_out12[0]), .out13(decoder_1_out12[1]), .out14(decoder_1_out12[2]),
    .out15(decoder_1_out12[3]), .sel(Address[3:0]));
  and and_1 (and_1_out, Enable, decoder_1_out0[0]);
  and and_2 (and_2_out, Enable, decoder_1_out0[1]);
  and and_3 (and_3_out, Enable, decoder_1_out0[2]);
  and and_4 (and_4_out, Enable, decoder_1_out0[3]);
  and and_5 (and_5_out, Enable, decoder_1_out4[0]);
  and and_6 (and_6_out, Enable, decoder_1_out4[1]);
  and and_7 (and_7_out, Enable, decoder_1_out4[2]);
  and and_8 (and_8_out, Enable, decoder_1_out4[3]);
  and and_9 (and_9_out, Enable, decoder_1_out8[0]);
  and and_10 (and_10_out, Enable, decoder_1_out8[1]);
  and and_11 (and_11_out, Enable, decoder_1_out8[2]);
  and and_12 (and_12_out, Enable, decoder_1_out8[3]);
  and and_13 (and_13_out, Enable, decoder_1_out12[0]);
  and and_14 (and_14_out, Enable, decoder_1_out12[1]);
  and and_15 (and_15_out, Enable, decoder_1_out12[2]);
  and and_16 (and_16_out, Enable, decoder_1_out12[3]);
  Register #(.width(16)) register_1 (
    .D({Data[0], Data[1], Data[2], Data[3], Data[4], Data[5], Data[6], Data[7], Data[8], Data[9], Data[10], Data[11], Data[12], Data[13], Data[14], Data[15]}),
    .en(and_1_out), .Q(out_6), .clk(CLK), .clr(Reset));
  Register #(.width(16)) register_2 (
    .D({Data[0], Data[1], Data[2], Data[3], Data[4], Data[5], Data[6], Data[7], Data[8], Data[9], Data[10], Data[11], Data[12], Data[13], Data[14], Data[15]}),
    .en(and_2_out), .Q(out_7), .clk(CLK), .clr(Reset));
  Register #(.width(16)) register_3 (
    .D({Data[0], Data[1], Data[2], Data[3], Data[4], Data[5], Data[6], Data[7], Data[8], Data[9], Data[10], Data[11], Data[12], Data[13], Data[14], Data[15]}),
    .en(and_3_out), .Q(out_8), .clk(CLK), .clr(Reset));
  Register #(.width(16)) register_4 (
    .D({Data[0], Data[1], Data[2], Data[3], Data[4], Data[5], Data[6], Data[7], Data[8], Data[9], Data[10], Data[11], Data[12], Data[13], Data[14], Data[15]}),
    .en(and_4_out), .Q(out_9), .clk(CLK), .clr(Reset));
  Register #(.width(16)) register_5 (
    .D({Data[0], Data[1], Data[2], Data[3], Data[4], Data[5], Data[6], Data[7], Data[8], Data[9], Data[10], Data[11], Data[12], Data[13], Data[14], Data[15]}),
    .en(and_5_out), .Q(out_10), .clk(CLK), .clr(Reset));
  Register #(.width(16)) register_6 (
    .D({Data[0], Data[1], Data[2], Data[3], Data[4], Data[5], Data[6], Data[7], Data[8], Data[9], Data[10], Data[11], Data[12], Data[13], Data[14], Data[15]}),
    .en(and_6_out), .Q(out_11), .clk(CLK), .clr(Reset));
  Register #(.width(16)) register_7 (
    .D({Data[0], Data[1], Data[2], Data[3], Data[4], Data[5], Data[6], Data[7], Data[8], Data[9], Data[10], Data[11], Data[12], Data[13], Data[14], Data[15]}),
    .en(and_7_out), .Q(out_12), .clk(CLK), .clr(Reset));
  Register #(.width(16)) register_8 (
    .D({Data[0], Data[1], Data[2], Data[3], Data[4], Data[5], Data[6], Data[7], Data[8], Data[9], Data[10], Data[11], Data[12], Data[13], Data[14], Data[15]}),
    .en(and_8_out), .Q(out_13), .clk(CLK), .clr(Reset));
  Register #(.width(16)) register_9 (
    .D({Data[0], Data[1], Data[2], Data[3], Data[4], Data[5], Data[6], Data[7], Data[8], Data[9], Data[10], Data[11], Data[12], Data[13], Data[14], Data[15]}),
    .en(and_9_out), .Q(out_14), .clk(CLK), .clr(Reset));
  Register #(.width(16)) register_10 (
    .D({Data[0], Data[1], Data[2], Data[3], Data[4], Data[5], Data[6], Data[7], Data[8], Data[9], Data[10], Data[11], Data[12], Data[13], Data[14], Data[15]}),
    .en(and_10_out), .Q(out_15), .clk(CLK), .clr(Reset));
  Register #(.width(16)) register_11 (
    .D({Data[0], Data[1], Data[2], Data[3], Data[4], Data[5], Data[6], Data[7], Data[8], Data[9], Data[10], Data[11], Data[12], Data[13], Data[14], Data[15]}),
    .en(and_11_out), .Q(out_16), .clk(CLK), .clr(Reset));
  Register #(.width(16)) register_12 (
    .D({Data[0], Data[1], Data[2], Data[3], Data[4], Data[5], Data[6], Data[7], Data[8], Data[9], Data[10], Data[11], Data[12], Data[13], Data[14], Data[15]}),
    .en(and_12_out), .Q(out_17), .clk(CLK), .clr(Reset));
  Register #(.width(16)) register_13 (
    .D({Data[0], Data[1], Data[2], Data[3], Data[4], Data[5], Data[6], Data[7], Data[8], Data[9], Data[10], Data[11], Data[12], Data[13], Data[14], Data[15]}),
    .en(and_13_out), .Q(out_18), .clk(CLK), .clr(Reset));
  Register #(.width(16)) register_14 (
    .D({Data[0], Data[1], Data[2], Data[3], Data[4], Data[5], Data[6], Data[7], Data[8], Data[9], Data[10], Data[11], Data[12], Data[13], Data[14], Data[15]}),
    .en(and_14_out), .Q(out_19), .clk(CLK), .clr(Reset));
  Register #(.width(16)) register_15 (
    .D({Data[0], Data[1], Data[2], Data[3], Data[4], Data[5], Data[6], Data[7], Data[8], Data[9], Data[10], Data[11], Data[12], Data[13], Data[14], Data[15]}),
    .en(and_15_out), .Q(out_20), .clk(CLK), .clr(Reset));
  Register #(.width(16)) register_16 (
    .D({Data[0], Data[1], Data[2], Data[3], Data[4], Data[5], Data[6], Data[7], Data[8], Data[9], Data[10], Data[11], Data[12], Data[13], Data[14], Data[15]}),
    .en(and_16_out), .Q(out_21), .clk(CLK), .clr(Reset));

  // Other names for the same wires on the sheet: RST = Reset
endmodule

module ScreenMatrix (
  input  in_1,
  input  in_2,
  input  in_3,
  input  in_4,
  input  in_5,
  input  in_6,
  input  in_7,
  input  in_8,
  input  in_9,
  input  in_10,
  input  in_11,
  input  in_12,
  output out_13,
  output out_14,
  output out_15,
  output out_16,
  output out_17,
  output out_18,
  output out_19,
  output out_20,
  output out_21,
  output out_22,
  output out_23,
  output out_24,
  output out_25,
  output out_26,
  output out_27,
  output out_28,
  output out_29,
  output out_30,
  output out_31,
  output out_32,
  output out_33,
  output out_34,
  output out_35,
  output out_36,
  output out_37,
  output out_38,
  output out_39,
  output out_40,
  output out_41,
  output out_42,
  output out_43,
  output out_44
);

  and and_1 (out_13, in_9, in_1);
  and and_2 (out_21, in_10, in_1);
  and and_3 (out_29, in_11, in_1);
  and and_4 (out_37, in_12, in_1);
  and and_5 (out_14, in_9, in_2);
  and and_6 (out_22, in_10, in_2);
  and and_7 (out_30, in_11, in_2);
  and and_8 (out_38, in_12, in_2);
  and and_9 (out_15, in_9, in_3);
  and and_10 (out_23, in_10, in_3);
  and and_11 (out_31, in_11, in_3);
  and and_12 (out_39, in_12, in_3);
  and and_13 (out_16, in_9, in_4);
  and and_14 (out_24, in_10, in_4);
  and and_15 (out_32, in_11, in_4);
  and and_16 (out_40, in_12, in_4);
  and and_17 (out_17, in_9, in_5);
  and and_18 (out_25, in_10, in_5);
  and and_19 (out_33, in_11, in_5);
  and and_20 (out_41, in_12, in_5);
  and and_21 (out_18, in_9, in_6);
  and and_22 (out_26, in_10, in_6);
  and and_23 (out_34, in_11, in_6);
  and and_24 (out_42, in_12, in_6);
  and and_25 (out_19, in_9, in_7);
  and and_26 (out_27, in_10, in_7);
  and and_27 (out_35, in_11, in_7);
  and and_28 (out_43, in_12, in_7);
  and and_29 (out_20, in_9, in_8);
  and and_30 (out_28, in_10, in_8);
  and and_31 (out_36, in_11, in_8);
  and and_32 (out_44, in_12, in_8);
endmodule
module ScreenMapper (
  input  CLK,
  input  RESET,
  input  [15:0] Data,
  input  [15:0] Offset,
  input  [15:0] Address
);

  wire [3:0] screenchip_1_p5;
  wire [15:0] Local_Address, screencontrol2_1_out_6, screencontrol2_1_out_7, screencontrol2_1_out_8,
       screencontrol2_1_out_9, screencontrol2_1_out_10, screencontrol2_1_out_11, screencontrol2_1_out_12,
       screencontrol2_1_out_13, screencontrol2_1_out_14, screencontrol2_1_out_15, screencontrol2_1_out_16,
       screencontrol2_1_out_17, screencontrol2_1_out_18, screencontrol2_1_out_19, screencontrol2_1_out_20,
       screencontrol2_1_out_21, screencontrol2_2_out_6, screencontrol2_2_out_7, screencontrol2_2_out_8,
       screencontrol2_2_out_9, screencontrol2_2_out_10, screencontrol2_2_out_11, screencontrol2_2_out_12,
       screencontrol2_2_out_13, screencontrol2_2_out_14, screencontrol2_2_out_15, screencontrol2_2_out_16,
       screencontrol2_2_out_17, screencontrol2_2_out_18, screencontrol2_2_out_19, screencontrol2_2_out_20,
       screencontrol2_2_out_21, screencontrol2_3_out_6, screencontrol2_3_out_7, screencontrol2_3_out_8,
       screencontrol2_3_out_9, screencontrol2_3_out_10, screencontrol2_3_out_11, screencontrol2_3_out_12,
       screencontrol2_3_out_13, screencontrol2_3_out_14, screencontrol2_3_out_15, screencontrol2_3_out_16,
       screencontrol2_3_out_17, screencontrol2_3_out_18, screencontrol2_3_out_19, screencontrol2_3_out_20,
       screencontrol2_3_out_21, screencontrol2_4_out_6, screencontrol2_4_out_7, screencontrol2_4_out_8,
       screencontrol2_4_out_9, screencontrol2_4_out_10, screencontrol2_4_out_11, screencontrol2_4_out_12,
       screencontrol2_4_out_13, screencontrol2_4_out_14, screencontrol2_4_out_15, screencontrol2_4_out_16,
       screencontrol2_4_out_17, screencontrol2_4_out_18, screencontrol2_4_out_19, screencontrol2_4_out_20,
       screencontrol2_4_out_21, screencontrol2_5_out_6, screencontrol2_5_out_7, screencontrol2_5_out_8,
       screencontrol2_5_out_9, screencontrol2_5_out_10, screencontrol2_5_out_11, screencontrol2_5_out_12,
       screencontrol2_5_out_13, screencontrol2_5_out_14, screencontrol2_5_out_15, screencontrol2_5_out_16,
       screencontrol2_5_out_17, screencontrol2_5_out_18, screencontrol2_5_out_19, screencontrol2_5_out_20,
       screencontrol2_5_out_21, screencontrol2_6_out_6, screencontrol2_6_out_7, screencontrol2_6_out_8,
       screencontrol2_6_out_9, screencontrol2_6_out_10, screencontrol2_6_out_11, screencontrol2_6_out_12,
       screencontrol2_6_out_13, screencontrol2_6_out_14, screencontrol2_6_out_15, screencontrol2_6_out_16,
       screencontrol2_6_out_17, screencontrol2_6_out_18, screencontrol2_6_out_19, screencontrol2_6_out_20,
       screencontrol2_6_out_21, screencontrol2_7_out_6, screencontrol2_7_out_7, screencontrol2_7_out_8,
       screencontrol2_7_out_9, screencontrol2_7_out_10, screencontrol2_7_out_11, screencontrol2_7_out_12,
       screencontrol2_7_out_13, screencontrol2_7_out_14, screencontrol2_7_out_15, screencontrol2_7_out_16,
       screencontrol2_7_out_17, screencontrol2_7_out_18, screencontrol2_7_out_19, screencontrol2_7_out_20,
       screencontrol2_7_out_21, screencontrol2_8_out_6, screencontrol2_8_out_7, screencontrol2_8_out_8,
       screencontrol2_8_out_9, screencontrol2_8_out_10, screencontrol2_8_out_11, screencontrol2_8_out_12,
       screencontrol2_8_out_13, screencontrol2_8_out_14, screencontrol2_8_out_15, screencontrol2_8_out_16,
       screencontrol2_8_out_17, screencontrol2_8_out_18, screencontrol2_8_out_19, screencontrol2_8_out_20,
       screencontrol2_8_out_21, screencontrol2_9_out_6, screencontrol2_9_out_7, screencontrol2_9_out_8,
       screencontrol2_9_out_9, screencontrol2_9_out_10, screencontrol2_9_out_11, screencontrol2_9_out_12,
       screencontrol2_9_out_13, screencontrol2_9_out_14, screencontrol2_9_out_15, screencontrol2_9_out_16,
       screencontrol2_9_out_17, screencontrol2_9_out_18, screencontrol2_9_out_19, screencontrol2_9_out_20,
       screencontrol2_9_out_21, screencontrol2_10_out_6, screencontrol2_10_out_7, screencontrol2_10_out_8,
       screencontrol2_10_out_9, screencontrol2_10_out_10, screencontrol2_10_out_11, screencontrol2_10_out_12,
       screencontrol2_10_out_13, screencontrol2_10_out_14, screencontrol2_10_out_15,
       screencontrol2_10_out_16, screencontrol2_10_out_17, screencontrol2_10_out_18,
       screencontrol2_10_out_19, screencontrol2_10_out_20, screencontrol2_10_out_21, screencontrol2_11_out_6,
       screencontrol2_11_out_7, screencontrol2_11_out_8, screencontrol2_11_out_9, screencontrol2_11_out_10,
       screencontrol2_11_out_11, screencontrol2_11_out_12, screencontrol2_11_out_13,
       screencontrol2_11_out_14, screencontrol2_11_out_15, screencontrol2_11_out_16,
       screencontrol2_11_out_17, screencontrol2_11_out_18, screencontrol2_11_out_19,
       screencontrol2_11_out_20, screencontrol2_11_out_21, screencontrol2_12_out_6, screencontrol2_12_out_7,
       screencontrol2_12_out_8, screencontrol2_12_out_9, screencontrol2_12_out_10, screencontrol2_12_out_11,
       screencontrol2_12_out_12, screencontrol2_12_out_13, screencontrol2_12_out_14,
       screencontrol2_12_out_15, screencontrol2_12_out_16, screencontrol2_12_out_17,
       screencontrol2_12_out_18, screencontrol2_12_out_19, screencontrol2_12_out_20,
       screencontrol2_12_out_21, screencontrol2_13_out_6, screencontrol2_13_out_7, screencontrol2_13_out_8,
       screencontrol2_13_out_9, screencontrol2_13_out_10, screencontrol2_13_out_11, screencontrol2_13_out_12,
       screencontrol2_13_out_13, screencontrol2_13_out_14, screencontrol2_13_out_15,
       screencontrol2_13_out_16, screencontrol2_13_out_17, screencontrol2_13_out_18,
       screencontrol2_13_out_19, screencontrol2_13_out_20, screencontrol2_13_out_21, screencontrol2_14_out_6,
       screencontrol2_14_out_7, screencontrol2_14_out_8, screencontrol2_14_out_9, screencontrol2_14_out_10,
       screencontrol2_14_out_11, screencontrol2_14_out_12, screencontrol2_14_out_13,
       screencontrol2_14_out_14, screencontrol2_14_out_15, screencontrol2_14_out_16,
       screencontrol2_14_out_17, screencontrol2_14_out_18, screencontrol2_14_out_19,
       screencontrol2_14_out_20, screencontrol2_14_out_21, screencontrol2_15_out_6, screencontrol2_15_out_7,
       screencontrol2_15_out_8, screencontrol2_15_out_9, screencontrol2_15_out_10, screencontrol2_15_out_11,
       screencontrol2_15_out_12, screencontrol2_15_out_13, screencontrol2_15_out_14,
       screencontrol2_15_out_15, screencontrol2_15_out_16, screencontrol2_15_out_17,
       screencontrol2_15_out_18, screencontrol2_15_out_19, screencontrol2_15_out_20,
       screencontrol2_15_out_21, screencontrol2_16_out_6, screencontrol2_16_out_7, screencontrol2_16_out_8,
       screencontrol2_16_out_9, screencontrol2_16_out_10, screencontrol2_16_out_11, screencontrol2_16_out_12,
       screencontrol2_16_out_13, screencontrol2_16_out_14, screencontrol2_16_out_15,
       screencontrol2_16_out_16, screencontrol2_16_out_17, screencontrol2_16_out_18,
       screencontrol2_16_out_19, screencontrol2_16_out_20, screencontrol2_16_out_21, screencontrol2_17_out_6,
       screencontrol2_17_out_7, screencontrol2_17_out_8, screencontrol2_17_out_9, screencontrol2_17_out_10,
       screencontrol2_17_out_11, screencontrol2_17_out_12, screencontrol2_17_out_13,
       screencontrol2_17_out_14, screencontrol2_17_out_15, screencontrol2_17_out_16,
       screencontrol2_17_out_17, screencontrol2_17_out_18, screencontrol2_17_out_19,
       screencontrol2_17_out_20, screencontrol2_17_out_21, screencontrol2_18_out_6, screencontrol2_18_out_7,
       screencontrol2_18_out_8, screencontrol2_18_out_9, screencontrol2_18_out_10, screencontrol2_18_out_11,
       screencontrol2_18_out_12, screencontrol2_18_out_13, screencontrol2_18_out_14,
       screencontrol2_18_out_15, screencontrol2_18_out_16, screencontrol2_18_out_17,
       screencontrol2_18_out_18, screencontrol2_18_out_19, screencontrol2_18_out_20,
       screencontrol2_18_out_21, screencontrol2_19_out_6, screencontrol2_19_out_7, screencontrol2_19_out_8,
       screencontrol2_19_out_9, screencontrol2_19_out_10, screencontrol2_19_out_11, screencontrol2_19_out_12,
       screencontrol2_19_out_13, screencontrol2_19_out_14, screencontrol2_19_out_15,
       screencontrol2_19_out_16, screencontrol2_19_out_17, screencontrol2_19_out_18,
       screencontrol2_19_out_19, screencontrol2_19_out_20, screencontrol2_19_out_21, screencontrol2_20_out_6,
       screencontrol2_20_out_7, screencontrol2_20_out_8, screencontrol2_20_out_9, screencontrol2_20_out_10,
       screencontrol2_20_out_11, screencontrol2_20_out_12, screencontrol2_20_out_13,
       screencontrol2_20_out_14, screencontrol2_20_out_15, screencontrol2_20_out_16,
       screencontrol2_20_out_17, screencontrol2_20_out_18, screencontrol2_20_out_19,
       screencontrol2_20_out_20, screencontrol2_20_out_21, screencontrol2_21_out_6, screencontrol2_21_out_7,
       screencontrol2_21_out_8, screencontrol2_21_out_9, screencontrol2_21_out_10, screencontrol2_21_out_11,
       screencontrol2_21_out_12, screencontrol2_21_out_13, screencontrol2_21_out_14,
       screencontrol2_21_out_15, screencontrol2_21_out_16, screencontrol2_21_out_17,
       screencontrol2_21_out_18, screencontrol2_21_out_19, screencontrol2_21_out_20,
       screencontrol2_21_out_21, screencontrol2_22_out_6, screencontrol2_22_out_7, screencontrol2_22_out_8,
       screencontrol2_22_out_9, screencontrol2_22_out_10, screencontrol2_22_out_11, screencontrol2_22_out_12,
       screencontrol2_22_out_13, screencontrol2_22_out_14, screencontrol2_22_out_15,
       screencontrol2_22_out_16, screencontrol2_22_out_17, screencontrol2_22_out_18,
       screencontrol2_22_out_19, screencontrol2_22_out_20, screencontrol2_22_out_21, screencontrol2_23_out_6,
       screencontrol2_23_out_7, screencontrol2_23_out_8, screencontrol2_23_out_9, screencontrol2_23_out_10,
       screencontrol2_23_out_11, screencontrol2_23_out_12, screencontrol2_23_out_13,
       screencontrol2_23_out_14, screencontrol2_23_out_15, screencontrol2_23_out_16,
       screencontrol2_23_out_17, screencontrol2_23_out_18, screencontrol2_23_out_19,
       screencontrol2_23_out_20, screencontrol2_23_out_21, screencontrol2_24_out_6, screencontrol2_24_out_7,
       screencontrol2_24_out_8, screencontrol2_24_out_9, screencontrol2_24_out_10, screencontrol2_24_out_11,
       screencontrol2_24_out_12, screencontrol2_24_out_13, screencontrol2_24_out_14,
       screencontrol2_24_out_15, screencontrol2_24_out_16, screencontrol2_24_out_17,
       screencontrol2_24_out_18, screencontrol2_24_out_19, screencontrol2_24_out_20,
       screencontrol2_24_out_21, screencontrol2_25_out_6, screencontrol2_25_out_7, screencontrol2_25_out_8,
       screencontrol2_25_out_9, screencontrol2_25_out_10, screencontrol2_25_out_11, screencontrol2_25_out_12,
       screencontrol2_25_out_13, screencontrol2_25_out_14, screencontrol2_25_out_15,
       screencontrol2_25_out_16, screencontrol2_25_out_17, screencontrol2_25_out_18,
       screencontrol2_25_out_19, screencontrol2_25_out_20, screencontrol2_25_out_21, screencontrol2_26_out_6,
       screencontrol2_26_out_7, screencontrol2_26_out_8, screencontrol2_26_out_9, screencontrol2_26_out_10,
       screencontrol2_26_out_11, screencontrol2_26_out_12, screencontrol2_26_out_13,
       screencontrol2_26_out_14, screencontrol2_26_out_15, screencontrol2_26_out_16,
       screencontrol2_26_out_17, screencontrol2_26_out_18, screencontrol2_26_out_19,
       screencontrol2_26_out_20, screencontrol2_26_out_21, screencontrol2_27_out_6, screencontrol2_27_out_7,
       screencontrol2_27_out_8, screencontrol2_27_out_9, screencontrol2_27_out_10, screencontrol2_27_out_11,
       screencontrol2_27_out_12, screencontrol2_27_out_13, screencontrol2_27_out_14,
       screencontrol2_27_out_15, screencontrol2_27_out_16, screencontrol2_27_out_17,
       screencontrol2_27_out_18, screencontrol2_27_out_19, screencontrol2_27_out_20,
       screencontrol2_27_out_21, screencontrol2_28_out_6, screencontrol2_28_out_7, screencontrol2_28_out_8,
       screencontrol2_28_out_9, screencontrol2_28_out_10, screencontrol2_28_out_11, screencontrol2_28_out_12,
       screencontrol2_28_out_13, screencontrol2_28_out_14, screencontrol2_28_out_15,
       screencontrol2_28_out_16, screencontrol2_28_out_17, screencontrol2_28_out_18,
       screencontrol2_28_out_19, screencontrol2_28_out_20, screencontrol2_28_out_21, screencontrol2_29_out_6,
       screencontrol2_29_out_7, screencontrol2_29_out_8, screencontrol2_29_out_9, screencontrol2_29_out_10,
       screencontrol2_29_out_11, screencontrol2_29_out_12, screencontrol2_29_out_13,
       screencontrol2_29_out_14, screencontrol2_29_out_15, screencontrol2_29_out_16,
       screencontrol2_29_out_17, screencontrol2_29_out_18, screencontrol2_29_out_19,
       screencontrol2_29_out_20, screencontrol2_29_out_21, screencontrol2_30_out_6, screencontrol2_30_out_7,
       screencontrol2_30_out_8, screencontrol2_30_out_9, screencontrol2_30_out_10, screencontrol2_30_out_11,
       screencontrol2_30_out_12, screencontrol2_30_out_13, screencontrol2_30_out_14,
       screencontrol2_30_out_15, screencontrol2_30_out_16, screencontrol2_30_out_17,
       screencontrol2_30_out_18, screencontrol2_30_out_19, screencontrol2_30_out_20,
       screencontrol2_30_out_21, screencontrol2_31_out_6, screencontrol2_31_out_7, screencontrol2_31_out_8,
       screencontrol2_31_out_9, screencontrol2_31_out_10, screencontrol2_31_out_11, screencontrol2_31_out_12,
       screencontrol2_31_out_13, screencontrol2_31_out_14, screencontrol2_31_out_15,
       screencontrol2_31_out_16, screencontrol2_31_out_17, screencontrol2_31_out_18,
       screencontrol2_31_out_19, screencontrol2_31_out_20, screencontrol2_31_out_21, screencontrol2_32_out_6,
       screencontrol2_32_out_7, screencontrol2_32_out_8, screencontrol2_32_out_9, screencontrol2_32_out_10,
       screencontrol2_32_out_11, screencontrol2_32_out_12, screencontrol2_32_out_13,
       screencontrol2_32_out_14, screencontrol2_32_out_15, screencontrol2_32_out_16,
       screencontrol2_32_out_17, screencontrol2_32_out_18, screencontrol2_32_out_19,
       screencontrol2_32_out_20, screencontrol2_32_out_21;
  wire [27:0] screenchip_1_p5_2;

  // ScreenChip screenchip_1: pin names not known; wires that end beside it: Offset, CLK, RESET, Address, {screenchip_1_p5, screenchip_1_p5_2}
  DotMatrix #(.inputtype("row"), .matrixcols(16), .matrixrows(16)) dotmatrix_1 (
    .row0(screencontrol2_1_out_6), .row1(screencontrol2_1_out_7), .row2(screencontrol2_1_out_8),
    .row3(screencontrol2_1_out_9), .row4(screencontrol2_1_out_10), .row5(screencontrol2_1_out_11),
    .row6(screencontrol2_1_out_12), .row7(screencontrol2_1_out_13), .row8(screencontrol2_1_out_14),
    .row9(screencontrol2_1_out_15), .row10(screencontrol2_1_out_16), .row11(screencontrol2_1_out_17),
    .row12(screencontrol2_1_out_18), .row13(screencontrol2_1_out_19), .row14(screencontrol2_1_out_20),
    .row15(screencontrol2_1_out_21));
  ScreenControl2 screencontrol2_1 (
    .CLK(CLK), .Data(Data), .Reset(RESET), .Enable(screenchip_1_p5[0]), .Address(Local_Address),
    .out_6(screencontrol2_1_out_6), .out_7(screencontrol2_1_out_7), .out_8(screencontrol2_1_out_8),
    .out_9(screencontrol2_1_out_9), .out_10(screencontrol2_1_out_10), .out_11(screencontrol2_1_out_11),
    .out_12(screencontrol2_1_out_12), .out_13(screencontrol2_1_out_13), .out_14(screencontrol2_1_out_14),
    .out_15(screencontrol2_1_out_15), .out_16(screencontrol2_1_out_16), .out_17(screencontrol2_1_out_17),
    .out_18(screencontrol2_1_out_18), .out_19(screencontrol2_1_out_19), .out_20(screencontrol2_1_out_20),
    .out_21(screencontrol2_1_out_21));
  DotMatrix #(.inputtype("row"), .matrixcols(16), .matrixrows(16)) dotmatrix_2 (
    .row0(screencontrol2_2_out_6), .row1(screencontrol2_2_out_7), .row2(screencontrol2_2_out_8),
    .row3(screencontrol2_2_out_9), .row4(screencontrol2_2_out_10), .row5(screencontrol2_2_out_11),
    .row6(screencontrol2_2_out_12), .row7(screencontrol2_2_out_13), .row8(screencontrol2_2_out_14),
    .row9(screencontrol2_2_out_15), .row10(screencontrol2_2_out_16), .row11(screencontrol2_2_out_17),
    .row12(screencontrol2_2_out_18), .row13(screencontrol2_2_out_19), .row14(screencontrol2_2_out_20),
    .row15(screencontrol2_2_out_21));
  ScreenControl2 screencontrol2_2 (
    .CLK(CLK), .Data(Data), .Reset(RESET), .Enable(screenchip_1_p5[1]), .Address(Local_Address),
    .out_6(screencontrol2_2_out_6), .out_7(screencontrol2_2_out_7), .out_8(screencontrol2_2_out_8),
    .out_9(screencontrol2_2_out_9), .out_10(screencontrol2_2_out_10), .out_11(screencontrol2_2_out_11),
    .out_12(screencontrol2_2_out_12), .out_13(screencontrol2_2_out_13), .out_14(screencontrol2_2_out_14),
    .out_15(screencontrol2_2_out_15), .out_16(screencontrol2_2_out_16), .out_17(screencontrol2_2_out_17),
    .out_18(screencontrol2_2_out_18), .out_19(screencontrol2_2_out_19), .out_20(screencontrol2_2_out_20),
    .out_21(screencontrol2_2_out_21));
  ScreenControl2 screencontrol2_3 (
    .CLK(CLK), .Data(Data), .Reset(RESET), .Enable(screenchip_1_p5[2]), .Address(Local_Address),
    .out_6(screencontrol2_3_out_6), .out_7(screencontrol2_3_out_7), .out_8(screencontrol2_3_out_8),
    .out_9(screencontrol2_3_out_9), .out_10(screencontrol2_3_out_10), .out_11(screencontrol2_3_out_11),
    .out_12(screencontrol2_3_out_12), .out_13(screencontrol2_3_out_13), .out_14(screencontrol2_3_out_14),
    .out_15(screencontrol2_3_out_15), .out_16(screencontrol2_3_out_16), .out_17(screencontrol2_3_out_17),
    .out_18(screencontrol2_3_out_18), .out_19(screencontrol2_3_out_19), .out_20(screencontrol2_3_out_20),
    .out_21(screencontrol2_3_out_21));
  DotMatrix #(.inputtype("row"), .matrixcols(16), .matrixrows(16)) dotmatrix_3 (
    .row0(screencontrol2_3_out_6), .row1(screencontrol2_3_out_7), .row2(screencontrol2_3_out_8),
    .row3(screencontrol2_3_out_9), .row4(screencontrol2_3_out_10), .row5(screencontrol2_3_out_11),
    .row6(screencontrol2_3_out_12), .row7(screencontrol2_3_out_13), .row8(screencontrol2_3_out_14),
    .row9(screencontrol2_3_out_15), .row10(screencontrol2_3_out_16), .row11(screencontrol2_3_out_17),
    .row12(screencontrol2_3_out_18), .row13(screencontrol2_3_out_19), .row14(screencontrol2_3_out_20),
    .row15(screencontrol2_3_out_21));
  ScreenControl2 screencontrol2_4 (
    .CLK(CLK), .Data(Data), .Reset(RESET), .Enable(screenchip_1_p5[3]), .Address(Local_Address),
    .out_6(screencontrol2_4_out_6), .out_7(screencontrol2_4_out_7), .out_8(screencontrol2_4_out_8),
    .out_9(screencontrol2_4_out_9), .out_10(screencontrol2_4_out_10), .out_11(screencontrol2_4_out_11),
    .out_12(screencontrol2_4_out_12), .out_13(screencontrol2_4_out_13), .out_14(screencontrol2_4_out_14),
    .out_15(screencontrol2_4_out_15), .out_16(screencontrol2_4_out_16), .out_17(screencontrol2_4_out_17),
    .out_18(screencontrol2_4_out_18), .out_19(screencontrol2_4_out_19), .out_20(screencontrol2_4_out_20),
    .out_21(screencontrol2_4_out_21));
  DotMatrix #(.inputtype("row"), .matrixcols(16), .matrixrows(16)) dotmatrix_4 (
    .row0(screencontrol2_4_out_6), .row1(screencontrol2_4_out_7), .row2(screencontrol2_4_out_8),
    .row3(screencontrol2_4_out_9), .row4(screencontrol2_4_out_10), .row5(screencontrol2_4_out_11),
    .row6(screencontrol2_4_out_12), .row7(screencontrol2_4_out_13), .row8(screencontrol2_4_out_14),
    .row9(screencontrol2_4_out_15), .row10(screencontrol2_4_out_16), .row11(screencontrol2_4_out_17),
    .row12(screencontrol2_4_out_18), .row13(screencontrol2_4_out_19), .row14(screencontrol2_4_out_20),
    .row15(screencontrol2_4_out_21));
  DotMatrix #(.inputtype("row"), .matrixcols(16), .matrixrows(16)) dotmatrix_5 (
    .row0(screencontrol2_5_out_6), .row1(screencontrol2_5_out_7), .row2(screencontrol2_5_out_8),
    .row3(screencontrol2_5_out_9), .row4(screencontrol2_5_out_10), .row5(screencontrol2_5_out_11),
    .row6(screencontrol2_5_out_12), .row7(screencontrol2_5_out_13), .row8(screencontrol2_5_out_14),
    .row9(screencontrol2_5_out_15), .row10(screencontrol2_5_out_16), .row11(screencontrol2_5_out_17),
    .row12(screencontrol2_5_out_18), .row13(screencontrol2_5_out_19), .row14(screencontrol2_5_out_20),
    .row15(screencontrol2_5_out_21));
  ScreenControl2 screencontrol2_5 (
    .CLK(CLK), .Data(Data), .Reset(RESET), .Enable(screenchip_1_p5_2[24]), .Address(Local_Address),
    .out_6(screencontrol2_5_out_6), .out_7(screencontrol2_5_out_7), .out_8(screencontrol2_5_out_8),
    .out_9(screencontrol2_5_out_9), .out_10(screencontrol2_5_out_10), .out_11(screencontrol2_5_out_11),
    .out_12(screencontrol2_5_out_12), .out_13(screencontrol2_5_out_13), .out_14(screencontrol2_5_out_14),
    .out_15(screencontrol2_5_out_15), .out_16(screencontrol2_5_out_16), .out_17(screencontrol2_5_out_17),
    .out_18(screencontrol2_5_out_18), .out_19(screencontrol2_5_out_19), .out_20(screencontrol2_5_out_20),
    .out_21(screencontrol2_5_out_21));
  DotMatrix #(.inputtype("row"), .matrixcols(16), .matrixrows(16)) dotmatrix_6 (
    .row0(screencontrol2_6_out_6), .row1(screencontrol2_6_out_7), .row2(screencontrol2_6_out_8),
    .row3(screencontrol2_6_out_9), .row4(screencontrol2_6_out_10), .row5(screencontrol2_6_out_11),
    .row6(screencontrol2_6_out_12), .row7(screencontrol2_6_out_13), .row8(screencontrol2_6_out_14),
    .row9(screencontrol2_6_out_15), .row10(screencontrol2_6_out_16), .row11(screencontrol2_6_out_17),
    .row12(screencontrol2_6_out_18), .row13(screencontrol2_6_out_19), .row14(screencontrol2_6_out_20),
    .row15(screencontrol2_6_out_21));
  ScreenControl2 screencontrol2_6 (
    .CLK(CLK), .Data(Data), .Reset(RESET), .Enable(screenchip_1_p5_2[25]), .Address(Local_Address),
    .out_6(screencontrol2_6_out_6), .out_7(screencontrol2_6_out_7), .out_8(screencontrol2_6_out_8),
    .out_9(screencontrol2_6_out_9), .out_10(screencontrol2_6_out_10), .out_11(screencontrol2_6_out_11),
    .out_12(screencontrol2_6_out_12), .out_13(screencontrol2_6_out_13), .out_14(screencontrol2_6_out_14),
    .out_15(screencontrol2_6_out_15), .out_16(screencontrol2_6_out_16), .out_17(screencontrol2_6_out_17),
    .out_18(screencontrol2_6_out_18), .out_19(screencontrol2_6_out_19), .out_20(screencontrol2_6_out_20),
    .out_21(screencontrol2_6_out_21));
  ScreenControl2 screencontrol2_7 (
    .CLK(CLK), .Data(Data), .Reset(RESET), .Enable(screenchip_1_p5_2[26]), .Address(Local_Address),
    .out_6(screencontrol2_7_out_6), .out_7(screencontrol2_7_out_7), .out_8(screencontrol2_7_out_8),
    .out_9(screencontrol2_7_out_9), .out_10(screencontrol2_7_out_10), .out_11(screencontrol2_7_out_11),
    .out_12(screencontrol2_7_out_12), .out_13(screencontrol2_7_out_13), .out_14(screencontrol2_7_out_14),
    .out_15(screencontrol2_7_out_15), .out_16(screencontrol2_7_out_16), .out_17(screencontrol2_7_out_17),
    .out_18(screencontrol2_7_out_18), .out_19(screencontrol2_7_out_19), .out_20(screencontrol2_7_out_20),
    .out_21(screencontrol2_7_out_21));
  DotMatrix #(.inputtype("row"), .matrixcols(16), .matrixrows(16)) dotmatrix_7 (
    .row0(screencontrol2_7_out_6), .row1(screencontrol2_7_out_7), .row2(screencontrol2_7_out_8),
    .row3(screencontrol2_7_out_9), .row4(screencontrol2_7_out_10), .row5(screencontrol2_7_out_11),
    .row6(screencontrol2_7_out_12), .row7(screencontrol2_7_out_13), .row8(screencontrol2_7_out_14),
    .row9(screencontrol2_7_out_15), .row10(screencontrol2_7_out_16), .row11(screencontrol2_7_out_17),
    .row12(screencontrol2_7_out_18), .row13(screencontrol2_7_out_19), .row14(screencontrol2_7_out_20),
    .row15(screencontrol2_7_out_21));
  ScreenControl2 screencontrol2_8 (
    .CLK(CLK), .Data(Data), .Reset(RESET), .Enable(screenchip_1_p5_2[27]), .Address(Local_Address),
    .out_6(screencontrol2_8_out_6), .out_7(screencontrol2_8_out_7), .out_8(screencontrol2_8_out_8),
    .out_9(screencontrol2_8_out_9), .out_10(screencontrol2_8_out_10), .out_11(screencontrol2_8_out_11),
    .out_12(screencontrol2_8_out_12), .out_13(screencontrol2_8_out_13), .out_14(screencontrol2_8_out_14),
    .out_15(screencontrol2_8_out_15), .out_16(screencontrol2_8_out_16), .out_17(screencontrol2_8_out_17),
    .out_18(screencontrol2_8_out_18), .out_19(screencontrol2_8_out_19), .out_20(screencontrol2_8_out_20),
    .out_21(screencontrol2_8_out_21));
  DotMatrix #(.inputtype("row"), .matrixcols(16), .matrixrows(16)) dotmatrix_8 (
    .row0(screencontrol2_8_out_6), .row1(screencontrol2_8_out_7), .row2(screencontrol2_8_out_8),
    .row3(screencontrol2_8_out_9), .row4(screencontrol2_8_out_10), .row5(screencontrol2_8_out_11),
    .row6(screencontrol2_8_out_12), .row7(screencontrol2_8_out_13), .row8(screencontrol2_8_out_14),
    .row9(screencontrol2_8_out_15), .row10(screencontrol2_8_out_16), .row11(screencontrol2_8_out_17),
    .row12(screencontrol2_8_out_18), .row13(screencontrol2_8_out_19), .row14(screencontrol2_8_out_20),
    .row15(screencontrol2_8_out_21));
  DotMatrix #(.inputtype("row"), .matrixcols(16), .matrixrows(16)) dotmatrix_9 (
    .row0(screencontrol2_9_out_6), .row1(screencontrol2_9_out_7), .row2(screencontrol2_9_out_8),
    .row3(screencontrol2_9_out_9), .row4(screencontrol2_9_out_10), .row5(screencontrol2_9_out_11),
    .row6(screencontrol2_9_out_12), .row7(screencontrol2_9_out_13), .row8(screencontrol2_9_out_14),
    .row9(screencontrol2_9_out_15), .row10(screencontrol2_9_out_16), .row11(screencontrol2_9_out_17),
    .row12(screencontrol2_9_out_18), .row13(screencontrol2_9_out_19), .row14(screencontrol2_9_out_20),
    .row15(screencontrol2_9_out_21));
  ScreenControl2 screencontrol2_9 (
    .CLK(CLK), .Data(Data), .Reset(RESET), .Enable(screenchip_1_p5_2[20]), .Address(Local_Address),
    .out_6(screencontrol2_9_out_6), .out_7(screencontrol2_9_out_7), .out_8(screencontrol2_9_out_8),
    .out_9(screencontrol2_9_out_9), .out_10(screencontrol2_9_out_10), .out_11(screencontrol2_9_out_11),
    .out_12(screencontrol2_9_out_12), .out_13(screencontrol2_9_out_13), .out_14(screencontrol2_9_out_14),
    .out_15(screencontrol2_9_out_15), .out_16(screencontrol2_9_out_16), .out_17(screencontrol2_9_out_17),
    .out_18(screencontrol2_9_out_18), .out_19(screencontrol2_9_out_19), .out_20(screencontrol2_9_out_20),
    .out_21(screencontrol2_9_out_21));
  DotMatrix #(.inputtype("row"), .matrixcols(16), .matrixrows(16)) dotmatrix_10 (
    .row0(screencontrol2_10_out_6), .row1(screencontrol2_10_out_7), .row2(screencontrol2_10_out_8),
    .row3(screencontrol2_10_out_9), .row4(screencontrol2_10_out_10), .row5(screencontrol2_10_out_11),
    .row6(screencontrol2_10_out_12), .row7(screencontrol2_10_out_13), .row8(screencontrol2_10_out_14),
    .row9(screencontrol2_10_out_15), .row10(screencontrol2_10_out_16), .row11(screencontrol2_10_out_17),
    .row12(screencontrol2_10_out_18), .row13(screencontrol2_10_out_19), .row14(screencontrol2_10_out_20),
    .row15(screencontrol2_10_out_21));
  ScreenControl2 screencontrol2_10 (
    .CLK(CLK), .Data(Data), .Reset(RESET), .Enable(screenchip_1_p5_2[21]), .Address(Local_Address),
    .out_6(screencontrol2_10_out_6), .out_7(screencontrol2_10_out_7), .out_8(screencontrol2_10_out_8),
    .out_9(screencontrol2_10_out_9), .out_10(screencontrol2_10_out_10), .out_11(screencontrol2_10_out_11),
    .out_12(screencontrol2_10_out_12), .out_13(screencontrol2_10_out_13), .out_14(screencontrol2_10_out_14),
    .out_15(screencontrol2_10_out_15), .out_16(screencontrol2_10_out_16), .out_17(screencontrol2_10_out_17),
    .out_18(screencontrol2_10_out_18), .out_19(screencontrol2_10_out_19), .out_20(screencontrol2_10_out_20),
    .out_21(screencontrol2_10_out_21));
  DotMatrix #(.inputtype("row"), .matrixcols(16), .matrixrows(16)) dotmatrix_11 (
    .row0(screencontrol2_11_out_6), .row1(screencontrol2_11_out_7), .row2(screencontrol2_11_out_8),
    .row3(screencontrol2_11_out_9), .row4(screencontrol2_11_out_10), .row5(screencontrol2_11_out_11),
    .row6(screencontrol2_11_out_12), .row7(screencontrol2_11_out_13), .row8(screencontrol2_11_out_14),
    .row9(screencontrol2_11_out_15), .row10(screencontrol2_11_out_16), .row11(screencontrol2_11_out_17),
    .row12(screencontrol2_11_out_18), .row13(screencontrol2_11_out_19), .row14(screencontrol2_11_out_20),
    .row15(screencontrol2_11_out_21));
  ScreenControl2 screencontrol2_11 (
    .CLK(CLK), .Data(Data), .Reset(RESET), .Enable(screenchip_1_p5_2[22]), .Address(Local_Address),
    .out_6(screencontrol2_11_out_6), .out_7(screencontrol2_11_out_7), .out_8(screencontrol2_11_out_8),
    .out_9(screencontrol2_11_out_9), .out_10(screencontrol2_11_out_10), .out_11(screencontrol2_11_out_11),
    .out_12(screencontrol2_11_out_12), .out_13(screencontrol2_11_out_13), .out_14(screencontrol2_11_out_14),
    .out_15(screencontrol2_11_out_15), .out_16(screencontrol2_11_out_16), .out_17(screencontrol2_11_out_17),
    .out_18(screencontrol2_11_out_18), .out_19(screencontrol2_11_out_19), .out_20(screencontrol2_11_out_20),
    .out_21(screencontrol2_11_out_21));
  DotMatrix #(.inputtype("row"), .matrixcols(16), .matrixrows(16)) dotmatrix_12 (
    .row0(screencontrol2_12_out_6), .row1(screencontrol2_12_out_7), .row2(screencontrol2_12_out_8),
    .row3(screencontrol2_12_out_9), .row4(screencontrol2_12_out_10), .row5(screencontrol2_12_out_11),
    .row6(screencontrol2_12_out_12), .row7(screencontrol2_12_out_13), .row8(screencontrol2_12_out_14),
    .row9(screencontrol2_12_out_15), .row10(screencontrol2_12_out_16), .row11(screencontrol2_12_out_17),
    .row12(screencontrol2_12_out_18), .row13(screencontrol2_12_out_19), .row14(screencontrol2_12_out_20),
    .row15(screencontrol2_12_out_21));
  ScreenControl2 screencontrol2_12 (
    .CLK(CLK), .Data(Data), .Reset(RESET), .Enable(screenchip_1_p5_2[23]), .Address(Local_Address),
    .out_6(screencontrol2_12_out_6), .out_7(screencontrol2_12_out_7), .out_8(screencontrol2_12_out_8),
    .out_9(screencontrol2_12_out_9), .out_10(screencontrol2_12_out_10), .out_11(screencontrol2_12_out_11),
    .out_12(screencontrol2_12_out_12), .out_13(screencontrol2_12_out_13), .out_14(screencontrol2_12_out_14),
    .out_15(screencontrol2_12_out_15), .out_16(screencontrol2_12_out_16), .out_17(screencontrol2_12_out_17),
    .out_18(screencontrol2_12_out_18), .out_19(screencontrol2_12_out_19), .out_20(screencontrol2_12_out_20),
    .out_21(screencontrol2_12_out_21));
  DotMatrix #(.inputtype("row"), .matrixcols(16), .matrixrows(16)) dotmatrix_13 (
    .row0(screencontrol2_13_out_6), .row1(screencontrol2_13_out_7), .row2(screencontrol2_13_out_8),
    .row3(screencontrol2_13_out_9), .row4(screencontrol2_13_out_10), .row5(screencontrol2_13_out_11),
    .row6(screencontrol2_13_out_12), .row7(screencontrol2_13_out_13), .row8(screencontrol2_13_out_14),
    .row9(screencontrol2_13_out_15), .row10(screencontrol2_13_out_16), .row11(screencontrol2_13_out_17),
    .row12(screencontrol2_13_out_18), .row13(screencontrol2_13_out_19), .row14(screencontrol2_13_out_20),
    .row15(screencontrol2_13_out_21));
  ScreenControl2 screencontrol2_13 (
    .CLK(CLK), .Data(Data), .Reset(RESET), .Enable(screenchip_1_p5_2[16]), .Address(Local_Address),
    .out_6(screencontrol2_13_out_6), .out_7(screencontrol2_13_out_7), .out_8(screencontrol2_13_out_8),
    .out_9(screencontrol2_13_out_9), .out_10(screencontrol2_13_out_10), .out_11(screencontrol2_13_out_11),
    .out_12(screencontrol2_13_out_12), .out_13(screencontrol2_13_out_13), .out_14(screencontrol2_13_out_14),
    .out_15(screencontrol2_13_out_15), .out_16(screencontrol2_13_out_16), .out_17(screencontrol2_13_out_17),
    .out_18(screencontrol2_13_out_18), .out_19(screencontrol2_13_out_19), .out_20(screencontrol2_13_out_20),
    .out_21(screencontrol2_13_out_21));
  DotMatrix #(.inputtype("row"), .matrixcols(16), .matrixrows(16)) dotmatrix_14 (
    .row0(screencontrol2_14_out_6), .row1(screencontrol2_14_out_7), .row2(screencontrol2_14_out_8),
    .row3(screencontrol2_14_out_9), .row4(screencontrol2_14_out_10), .row5(screencontrol2_14_out_11),
    .row6(screencontrol2_14_out_12), .row7(screencontrol2_14_out_13), .row8(screencontrol2_14_out_14),
    .row9(screencontrol2_14_out_15), .row10(screencontrol2_14_out_16), .row11(screencontrol2_14_out_17),
    .row12(screencontrol2_14_out_18), .row13(screencontrol2_14_out_19), .row14(screencontrol2_14_out_20),
    .row15(screencontrol2_14_out_21));
  ScreenControl2 screencontrol2_14 (
    .CLK(CLK), .Data(Data), .Reset(RESET), .Enable(screenchip_1_p5_2[17]), .Address(Local_Address),
    .out_6(screencontrol2_14_out_6), .out_7(screencontrol2_14_out_7), .out_8(screencontrol2_14_out_8),
    .out_9(screencontrol2_14_out_9), .out_10(screencontrol2_14_out_10), .out_11(screencontrol2_14_out_11),
    .out_12(screencontrol2_14_out_12), .out_13(screencontrol2_14_out_13), .out_14(screencontrol2_14_out_14),
    .out_15(screencontrol2_14_out_15), .out_16(screencontrol2_14_out_16), .out_17(screencontrol2_14_out_17),
    .out_18(screencontrol2_14_out_18), .out_19(screencontrol2_14_out_19), .out_20(screencontrol2_14_out_20),
    .out_21(screencontrol2_14_out_21));
  ScreenControl2 screencontrol2_15 (
    .CLK(CLK), .Data(Data), .Reset(RESET), .Enable(screenchip_1_p5_2[18]), .Address(Local_Address),
    .out_6(screencontrol2_15_out_6), .out_7(screencontrol2_15_out_7), .out_8(screencontrol2_15_out_8),
    .out_9(screencontrol2_15_out_9), .out_10(screencontrol2_15_out_10), .out_11(screencontrol2_15_out_11),
    .out_12(screencontrol2_15_out_12), .out_13(screencontrol2_15_out_13), .out_14(screencontrol2_15_out_14),
    .out_15(screencontrol2_15_out_15), .out_16(screencontrol2_15_out_16), .out_17(screencontrol2_15_out_17),
    .out_18(screencontrol2_15_out_18), .out_19(screencontrol2_15_out_19), .out_20(screencontrol2_15_out_20),
    .out_21(screencontrol2_15_out_21));
  DotMatrix #(.inputtype("row"), .matrixcols(16), .matrixrows(16)) dotmatrix_15 (
    .row0(screencontrol2_15_out_6), .row1(screencontrol2_15_out_7), .row2(screencontrol2_15_out_8),
    .row3(screencontrol2_15_out_9), .row4(screencontrol2_15_out_10), .row5(screencontrol2_15_out_11),
    .row6(screencontrol2_15_out_12), .row7(screencontrol2_15_out_13), .row8(screencontrol2_15_out_14),
    .row9(screencontrol2_15_out_15), .row10(screencontrol2_15_out_16), .row11(screencontrol2_15_out_17),
    .row12(screencontrol2_15_out_18), .row13(screencontrol2_15_out_19), .row14(screencontrol2_15_out_20),
    .row15(screencontrol2_15_out_21));
  ScreenControl2 screencontrol2_16 (
    .CLK(CLK), .Data(Data), .Reset(RESET), .Enable(screenchip_1_p5_2[19]), .Address(Local_Address),
    .out_6(screencontrol2_16_out_6), .out_7(screencontrol2_16_out_7), .out_8(screencontrol2_16_out_8),
    .out_9(screencontrol2_16_out_9), .out_10(screencontrol2_16_out_10), .out_11(screencontrol2_16_out_11),
    .out_12(screencontrol2_16_out_12), .out_13(screencontrol2_16_out_13), .out_14(screencontrol2_16_out_14),
    .out_15(screencontrol2_16_out_15), .out_16(screencontrol2_16_out_16), .out_17(screencontrol2_16_out_17),
    .out_18(screencontrol2_16_out_18), .out_19(screencontrol2_16_out_19), .out_20(screencontrol2_16_out_20),
    .out_21(screencontrol2_16_out_21));
  DotMatrix #(.inputtype("row"), .matrixcols(16), .matrixrows(16)) dotmatrix_16 (
    .row0(screencontrol2_16_out_6), .row1(screencontrol2_16_out_7), .row2(screencontrol2_16_out_8),
    .row3(screencontrol2_16_out_9), .row4(screencontrol2_16_out_10), .row5(screencontrol2_16_out_11),
    .row6(screencontrol2_16_out_12), .row7(screencontrol2_16_out_13), .row8(screencontrol2_16_out_14),
    .row9(screencontrol2_16_out_15), .row10(screencontrol2_16_out_16), .row11(screencontrol2_16_out_17),
    .row12(screencontrol2_16_out_18), .row13(screencontrol2_16_out_19), .row14(screencontrol2_16_out_20),
    .row15(screencontrol2_16_out_21));
  DotMatrix #(.inputtype("row"), .matrixcols(16), .matrixrows(16)) dotmatrix_17 (
    .row0(screencontrol2_17_out_6), .row1(screencontrol2_17_out_7), .row2(screencontrol2_17_out_8),
    .row3(screencontrol2_17_out_9), .row4(screencontrol2_17_out_10), .row5(screencontrol2_17_out_11),
    .row6(screencontrol2_17_out_12), .row7(screencontrol2_17_out_13), .row8(screencontrol2_17_out_14),
    .row9(screencontrol2_17_out_15), .row10(screencontrol2_17_out_16), .row11(screencontrol2_17_out_17),
    .row12(screencontrol2_17_out_18), .row13(screencontrol2_17_out_19), .row14(screencontrol2_17_out_20),
    .row15(screencontrol2_17_out_21));
  ScreenControl2 screencontrol2_17 (
    .CLK(CLK), .Data(Data), .Reset(RESET), .Enable(screenchip_1_p5_2[12]), .Address(Local_Address),
    .out_6(screencontrol2_17_out_6), .out_7(screencontrol2_17_out_7), .out_8(screencontrol2_17_out_8),
    .out_9(screencontrol2_17_out_9), .out_10(screencontrol2_17_out_10), .out_11(screencontrol2_17_out_11),
    .out_12(screencontrol2_17_out_12), .out_13(screencontrol2_17_out_13), .out_14(screencontrol2_17_out_14),
    .out_15(screencontrol2_17_out_15), .out_16(screencontrol2_17_out_16), .out_17(screencontrol2_17_out_17),
    .out_18(screencontrol2_17_out_18), .out_19(screencontrol2_17_out_19), .out_20(screencontrol2_17_out_20),
    .out_21(screencontrol2_17_out_21));
  ScreenControl2 screencontrol2_18 (
    .CLK(CLK), .Data(Data), .Reset(RESET), .Enable(screenchip_1_p5_2[13]), .Address(Local_Address),
    .out_6(screencontrol2_18_out_6), .out_7(screencontrol2_18_out_7), .out_8(screencontrol2_18_out_8),
    .out_9(screencontrol2_18_out_9), .out_10(screencontrol2_18_out_10), .out_11(screencontrol2_18_out_11),
    .out_12(screencontrol2_18_out_12), .out_13(screencontrol2_18_out_13), .out_14(screencontrol2_18_out_14),
    .out_15(screencontrol2_18_out_15), .out_16(screencontrol2_18_out_16), .out_17(screencontrol2_18_out_17),
    .out_18(screencontrol2_18_out_18), .out_19(screencontrol2_18_out_19), .out_20(screencontrol2_18_out_20),
    .out_21(screencontrol2_18_out_21));
  DotMatrix #(.inputtype("row"), .matrixcols(16), .matrixrows(16)) dotmatrix_18 (
    .row0(screencontrol2_18_out_6), .row1(screencontrol2_18_out_7), .row2(screencontrol2_18_out_8),
    .row3(screencontrol2_18_out_9), .row4(screencontrol2_18_out_10), .row5(screencontrol2_18_out_11),
    .row6(screencontrol2_18_out_12), .row7(screencontrol2_18_out_13), .row8(screencontrol2_18_out_14),
    .row9(screencontrol2_18_out_15), .row10(screencontrol2_18_out_16), .row11(screencontrol2_18_out_17),
    .row12(screencontrol2_18_out_18), .row13(screencontrol2_18_out_19), .row14(screencontrol2_18_out_20),
    .row15(screencontrol2_18_out_21));
  DotMatrix #(.inputtype("row"), .matrixcols(16), .matrixrows(16)) dotmatrix_19 (
    .row0(screencontrol2_19_out_6), .row1(screencontrol2_19_out_7), .row2(screencontrol2_19_out_8),
    .row3(screencontrol2_19_out_9), .row4(screencontrol2_19_out_10), .row5(screencontrol2_19_out_11),
    .row6(screencontrol2_19_out_12), .row7(screencontrol2_19_out_13), .row8(screencontrol2_19_out_14),
    .row9(screencontrol2_19_out_15), .row10(screencontrol2_19_out_16), .row11(screencontrol2_19_out_17),
    .row12(screencontrol2_19_out_18), .row13(screencontrol2_19_out_19), .row14(screencontrol2_19_out_20),
    .row15(screencontrol2_19_out_21));
  ScreenControl2 screencontrol2_19 (
    .CLK(CLK), .Data(Data), .Reset(RESET), .Enable(screenchip_1_p5_2[14]), .Address(Local_Address),
    .out_6(screencontrol2_19_out_6), .out_7(screencontrol2_19_out_7), .out_8(screencontrol2_19_out_8),
    .out_9(screencontrol2_19_out_9), .out_10(screencontrol2_19_out_10), .out_11(screencontrol2_19_out_11),
    .out_12(screencontrol2_19_out_12), .out_13(screencontrol2_19_out_13), .out_14(screencontrol2_19_out_14),
    .out_15(screencontrol2_19_out_15), .out_16(screencontrol2_19_out_16), .out_17(screencontrol2_19_out_17),
    .out_18(screencontrol2_19_out_18), .out_19(screencontrol2_19_out_19), .out_20(screencontrol2_19_out_20),
    .out_21(screencontrol2_19_out_21));
  ScreenControl2 screencontrol2_20 (
    .CLK(CLK), .Data(Data), .Reset(RESET), .Enable(screenchip_1_p5_2[15]), .Address(Local_Address),
    .out_6(screencontrol2_20_out_6), .out_7(screencontrol2_20_out_7), .out_8(screencontrol2_20_out_8),
    .out_9(screencontrol2_20_out_9), .out_10(screencontrol2_20_out_10), .out_11(screencontrol2_20_out_11),
    .out_12(screencontrol2_20_out_12), .out_13(screencontrol2_20_out_13), .out_14(screencontrol2_20_out_14),
    .out_15(screencontrol2_20_out_15), .out_16(screencontrol2_20_out_16), .out_17(screencontrol2_20_out_17),
    .out_18(screencontrol2_20_out_18), .out_19(screencontrol2_20_out_19), .out_20(screencontrol2_20_out_20),
    .out_21(screencontrol2_20_out_21));
  DotMatrix #(.inputtype("row"), .matrixcols(16), .matrixrows(16)) dotmatrix_20 (
    .row0(screencontrol2_20_out_6), .row1(screencontrol2_20_out_7), .row2(screencontrol2_20_out_8),
    .row3(screencontrol2_20_out_9), .row4(screencontrol2_20_out_10), .row5(screencontrol2_20_out_11),
    .row6(screencontrol2_20_out_12), .row7(screencontrol2_20_out_13), .row8(screencontrol2_20_out_14),
    .row9(screencontrol2_20_out_15), .row10(screencontrol2_20_out_16), .row11(screencontrol2_20_out_17),
    .row12(screencontrol2_20_out_18), .row13(screencontrol2_20_out_19), .row14(screencontrol2_20_out_20),
    .row15(screencontrol2_20_out_21));
  DotMatrix #(.inputtype("row"), .matrixcols(16), .matrixrows(16)) dotmatrix_21 (
    .row0(screencontrol2_21_out_6), .row1(screencontrol2_21_out_7), .row2(screencontrol2_21_out_8),
    .row3(screencontrol2_21_out_9), .row4(screencontrol2_21_out_10), .row5(screencontrol2_21_out_11),
    .row6(screencontrol2_21_out_12), .row7(screencontrol2_21_out_13), .row8(screencontrol2_21_out_14),
    .row9(screencontrol2_21_out_15), .row10(screencontrol2_21_out_16), .row11(screencontrol2_21_out_17),
    .row12(screencontrol2_21_out_18), .row13(screencontrol2_21_out_19), .row14(screencontrol2_21_out_20),
    .row15(screencontrol2_21_out_21));
  ScreenControl2 screencontrol2_21 (
    .CLK(CLK), .Data(Data), .Reset(RESET), .Enable(screenchip_1_p5_2[8]), .Address(Local_Address),
    .out_6(screencontrol2_21_out_6), .out_7(screencontrol2_21_out_7), .out_8(screencontrol2_21_out_8),
    .out_9(screencontrol2_21_out_9), .out_10(screencontrol2_21_out_10), .out_11(screencontrol2_21_out_11),
    .out_12(screencontrol2_21_out_12), .out_13(screencontrol2_21_out_13), .out_14(screencontrol2_21_out_14),
    .out_15(screencontrol2_21_out_15), .out_16(screencontrol2_21_out_16), .out_17(screencontrol2_21_out_17),
    .out_18(screencontrol2_21_out_18), .out_19(screencontrol2_21_out_19), .out_20(screencontrol2_21_out_20),
    .out_21(screencontrol2_21_out_21));
  ScreenControl2 screencontrol2_22 (
    .CLK(CLK), .Data(Data), .Reset(RESET), .Enable(screenchip_1_p5_2[9]), .Address(Local_Address),
    .out_6(screencontrol2_22_out_6), .out_7(screencontrol2_22_out_7), .out_8(screencontrol2_22_out_8),
    .out_9(screencontrol2_22_out_9), .out_10(screencontrol2_22_out_10), .out_11(screencontrol2_22_out_11),
    .out_12(screencontrol2_22_out_12), .out_13(screencontrol2_22_out_13), .out_14(screencontrol2_22_out_14),
    .out_15(screencontrol2_22_out_15), .out_16(screencontrol2_22_out_16), .out_17(screencontrol2_22_out_17),
    .out_18(screencontrol2_22_out_18), .out_19(screencontrol2_22_out_19), .out_20(screencontrol2_22_out_20),
    .out_21(screencontrol2_22_out_21));
  DotMatrix #(.inputtype("row"), .matrixcols(16), .matrixrows(16)) dotmatrix_22 (
    .row0(screencontrol2_22_out_6), .row1(screencontrol2_22_out_7), .row2(screencontrol2_22_out_8),
    .row3(screencontrol2_22_out_9), .row4(screencontrol2_22_out_10), .row5(screencontrol2_22_out_11),
    .row6(screencontrol2_22_out_12), .row7(screencontrol2_22_out_13), .row8(screencontrol2_22_out_14),
    .row9(screencontrol2_22_out_15), .row10(screencontrol2_22_out_16), .row11(screencontrol2_22_out_17),
    .row12(screencontrol2_22_out_18), .row13(screencontrol2_22_out_19), .row14(screencontrol2_22_out_20),
    .row15(screencontrol2_22_out_21));
  DotMatrix #(.inputtype("row"), .matrixcols(16), .matrixrows(16)) dotmatrix_23 (
    .row0(screencontrol2_23_out_6), .row1(screencontrol2_23_out_7), .row2(screencontrol2_23_out_8),
    .row3(screencontrol2_23_out_9), .row4(screencontrol2_23_out_10), .row5(screencontrol2_23_out_11),
    .row6(screencontrol2_23_out_12), .row7(screencontrol2_23_out_13), .row8(screencontrol2_23_out_14),
    .row9(screencontrol2_23_out_15), .row10(screencontrol2_23_out_16), .row11(screencontrol2_23_out_17),
    .row12(screencontrol2_23_out_18), .row13(screencontrol2_23_out_19), .row14(screencontrol2_23_out_20),
    .row15(screencontrol2_23_out_21));
  ScreenControl2 screencontrol2_23 (
    .CLK(CLK), .Data(Data), .Reset(RESET), .Enable(screenchip_1_p5_2[10]), .Address(Local_Address),
    .out_6(screencontrol2_23_out_6), .out_7(screencontrol2_23_out_7), .out_8(screencontrol2_23_out_8),
    .out_9(screencontrol2_23_out_9), .out_10(screencontrol2_23_out_10), .out_11(screencontrol2_23_out_11),
    .out_12(screencontrol2_23_out_12), .out_13(screencontrol2_23_out_13), .out_14(screencontrol2_23_out_14),
    .out_15(screencontrol2_23_out_15), .out_16(screencontrol2_23_out_16), .out_17(screencontrol2_23_out_17),
    .out_18(screencontrol2_23_out_18), .out_19(screencontrol2_23_out_19), .out_20(screencontrol2_23_out_20),
    .out_21(screencontrol2_23_out_21));
  DotMatrix #(.inputtype("row"), .matrixcols(16), .matrixrows(16)) dotmatrix_24 (
    .row0(screencontrol2_24_out_6), .row1(screencontrol2_24_out_7), .row2(screencontrol2_24_out_8),
    .row3(screencontrol2_24_out_9), .row4(screencontrol2_24_out_10), .row5(screencontrol2_24_out_11),
    .row6(screencontrol2_24_out_12), .row7(screencontrol2_24_out_13), .row8(screencontrol2_24_out_14),
    .row9(screencontrol2_24_out_15), .row10(screencontrol2_24_out_16), .row11(screencontrol2_24_out_17),
    .row12(screencontrol2_24_out_18), .row13(screencontrol2_24_out_19), .row14(screencontrol2_24_out_20),
    .row15(screencontrol2_24_out_21));
  ScreenControl2 screencontrol2_24 (
    .CLK(CLK), .Data(Data), .Reset(RESET), .Enable(screenchip_1_p5_2[11]), .Address(Local_Address),
    .out_6(screencontrol2_24_out_6), .out_7(screencontrol2_24_out_7), .out_8(screencontrol2_24_out_8),
    .out_9(screencontrol2_24_out_9), .out_10(screencontrol2_24_out_10), .out_11(screencontrol2_24_out_11),
    .out_12(screencontrol2_24_out_12), .out_13(screencontrol2_24_out_13), .out_14(screencontrol2_24_out_14),
    .out_15(screencontrol2_24_out_15), .out_16(screencontrol2_24_out_16), .out_17(screencontrol2_24_out_17),
    .out_18(screencontrol2_24_out_18), .out_19(screencontrol2_24_out_19), .out_20(screencontrol2_24_out_20),
    .out_21(screencontrol2_24_out_21));
  ScreenControl2 screencontrol2_25 (
    .CLK(CLK), .Data(Data), .Reset(RESET), .Enable(screenchip_1_p5_2[4]), .Address(Local_Address),
    .out_6(screencontrol2_25_out_6), .out_7(screencontrol2_25_out_7), .out_8(screencontrol2_25_out_8),
    .out_9(screencontrol2_25_out_9), .out_10(screencontrol2_25_out_10), .out_11(screencontrol2_25_out_11),
    .out_12(screencontrol2_25_out_12), .out_13(screencontrol2_25_out_13), .out_14(screencontrol2_25_out_14),
    .out_15(screencontrol2_25_out_15), .out_16(screencontrol2_25_out_16), .out_17(screencontrol2_25_out_17),
    .out_18(screencontrol2_25_out_18), .out_19(screencontrol2_25_out_19), .out_20(screencontrol2_25_out_20),
    .out_21(screencontrol2_25_out_21));
  DotMatrix #(.inputtype("row"), .matrixcols(16), .matrixrows(16)) dotmatrix_25 (
    .row0(screencontrol2_25_out_6), .row1(screencontrol2_25_out_7), .row2(screencontrol2_25_out_8),
    .row3(screencontrol2_25_out_9), .row4(screencontrol2_25_out_10), .row5(screencontrol2_25_out_11),
    .row6(screencontrol2_25_out_12), .row7(screencontrol2_25_out_13), .row8(screencontrol2_25_out_14),
    .row9(screencontrol2_25_out_15), .row10(screencontrol2_25_out_16), .row11(screencontrol2_25_out_17),
    .row12(screencontrol2_25_out_18), .row13(screencontrol2_25_out_19), .row14(screencontrol2_25_out_20),
    .row15(screencontrol2_25_out_21));
  ScreenControl2 screencontrol2_26 (
    .CLK(CLK), .Data(Data), .Reset(RESET), .Enable(screenchip_1_p5_2[5]), .Address(Local_Address),
    .out_6(screencontrol2_26_out_6), .out_7(screencontrol2_26_out_7), .out_8(screencontrol2_26_out_8),
    .out_9(screencontrol2_26_out_9), .out_10(screencontrol2_26_out_10), .out_11(screencontrol2_26_out_11),
    .out_12(screencontrol2_26_out_12), .out_13(screencontrol2_26_out_13), .out_14(screencontrol2_26_out_14),
    .out_15(screencontrol2_26_out_15), .out_16(screencontrol2_26_out_16), .out_17(screencontrol2_26_out_17),
    .out_18(screencontrol2_26_out_18), .out_19(screencontrol2_26_out_19), .out_20(screencontrol2_26_out_20),
    .out_21(screencontrol2_26_out_21));
  DotMatrix #(.inputtype("row"), .matrixcols(16), .matrixrows(16)) dotmatrix_26 (
    .row0(screencontrol2_26_out_6), .row1(screencontrol2_26_out_7), .row2(screencontrol2_26_out_8),
    .row3(screencontrol2_26_out_9), .row4(screencontrol2_26_out_10), .row5(screencontrol2_26_out_11),
    .row6(screencontrol2_26_out_12), .row7(screencontrol2_26_out_13), .row8(screencontrol2_26_out_14),
    .row9(screencontrol2_26_out_15), .row10(screencontrol2_26_out_16), .row11(screencontrol2_26_out_17),
    .row12(screencontrol2_26_out_18), .row13(screencontrol2_26_out_19), .row14(screencontrol2_26_out_20),
    .row15(screencontrol2_26_out_21));
  ScreenControl2 screencontrol2_27 (
    .CLK(CLK), .Data(Data), .Reset(RESET), .Enable(screenchip_1_p5_2[6]), .Address(Local_Address),
    .out_6(screencontrol2_27_out_6), .out_7(screencontrol2_27_out_7), .out_8(screencontrol2_27_out_8),
    .out_9(screencontrol2_27_out_9), .out_10(screencontrol2_27_out_10), .out_11(screencontrol2_27_out_11),
    .out_12(screencontrol2_27_out_12), .out_13(screencontrol2_27_out_13), .out_14(screencontrol2_27_out_14),
    .out_15(screencontrol2_27_out_15), .out_16(screencontrol2_27_out_16), .out_17(screencontrol2_27_out_17),
    .out_18(screencontrol2_27_out_18), .out_19(screencontrol2_27_out_19), .out_20(screencontrol2_27_out_20),
    .out_21(screencontrol2_27_out_21));
  DotMatrix #(.inputtype("row"), .matrixcols(16), .matrixrows(16)) dotmatrix_27 (
    .row0(screencontrol2_27_out_6), .row1(screencontrol2_27_out_7), .row2(screencontrol2_27_out_8),
    .row3(screencontrol2_27_out_9), .row4(screencontrol2_27_out_10), .row5(screencontrol2_27_out_11),
    .row6(screencontrol2_27_out_12), .row7(screencontrol2_27_out_13), .row8(screencontrol2_27_out_14),
    .row9(screencontrol2_27_out_15), .row10(screencontrol2_27_out_16), .row11(screencontrol2_27_out_17),
    .row12(screencontrol2_27_out_18), .row13(screencontrol2_27_out_19), .row14(screencontrol2_27_out_20),
    .row15(screencontrol2_27_out_21));
  DotMatrix #(.inputtype("row"), .matrixcols(16), .matrixrows(16)) dotmatrix_28 (
    .row0(screencontrol2_28_out_6), .row1(screencontrol2_28_out_7), .row2(screencontrol2_28_out_8),
    .row3(screencontrol2_28_out_9), .row4(screencontrol2_28_out_10), .row5(screencontrol2_28_out_11),
    .row6(screencontrol2_28_out_12), .row7(screencontrol2_28_out_13), .row8(screencontrol2_28_out_14),
    .row9(screencontrol2_28_out_15), .row10(screencontrol2_28_out_16), .row11(screencontrol2_28_out_17),
    .row12(screencontrol2_28_out_18), .row13(screencontrol2_28_out_19), .row14(screencontrol2_28_out_20),
    .row15(screencontrol2_28_out_21));
  ScreenControl2 screencontrol2_28 (
    .CLK(CLK), .Data(Data), .Reset(RESET), .Enable(screenchip_1_p5_2[7]), .Address(Local_Address),
    .out_6(screencontrol2_28_out_6), .out_7(screencontrol2_28_out_7), .out_8(screencontrol2_28_out_8),
    .out_9(screencontrol2_28_out_9), .out_10(screencontrol2_28_out_10), .out_11(screencontrol2_28_out_11),
    .out_12(screencontrol2_28_out_12), .out_13(screencontrol2_28_out_13), .out_14(screencontrol2_28_out_14),
    .out_15(screencontrol2_28_out_15), .out_16(screencontrol2_28_out_16), .out_17(screencontrol2_28_out_17),
    .out_18(screencontrol2_28_out_18), .out_19(screencontrol2_28_out_19), .out_20(screencontrol2_28_out_20),
    .out_21(screencontrol2_28_out_21));
  DotMatrix #(.inputtype("row"), .matrixcols(16), .matrixrows(16)) dotmatrix_29 (
    .row0(screencontrol2_29_out_6), .row1(screencontrol2_29_out_7), .row2(screencontrol2_29_out_8),
    .row3(screencontrol2_29_out_9), .row4(screencontrol2_29_out_10), .row5(screencontrol2_29_out_11),
    .row6(screencontrol2_29_out_12), .row7(screencontrol2_29_out_13), .row8(screencontrol2_29_out_14),
    .row9(screencontrol2_29_out_15), .row10(screencontrol2_29_out_16), .row11(screencontrol2_29_out_17),
    .row12(screencontrol2_29_out_18), .row13(screencontrol2_29_out_19), .row14(screencontrol2_29_out_20),
    .row15(screencontrol2_29_out_21));
  ScreenControl2 screencontrol2_29 (
    .CLK(CLK), .Data(Data), .Reset(RESET), .Enable(screenchip_1_p5_2[0]), .Address(Local_Address),
    .out_6(screencontrol2_29_out_6), .out_7(screencontrol2_29_out_7), .out_8(screencontrol2_29_out_8),
    .out_9(screencontrol2_29_out_9), .out_10(screencontrol2_29_out_10), .out_11(screencontrol2_29_out_11),
    .out_12(screencontrol2_29_out_12), .out_13(screencontrol2_29_out_13), .out_14(screencontrol2_29_out_14),
    .out_15(screencontrol2_29_out_15), .out_16(screencontrol2_29_out_16), .out_17(screencontrol2_29_out_17),
    .out_18(screencontrol2_29_out_18), .out_19(screencontrol2_29_out_19), .out_20(screencontrol2_29_out_20),
    .out_21(screencontrol2_29_out_21));
  DotMatrix #(.inputtype("row"), .matrixcols(16), .matrixrows(16)) dotmatrix_30 (
    .row0(screencontrol2_30_out_6), .row1(screencontrol2_30_out_7), .row2(screencontrol2_30_out_8),
    .row3(screencontrol2_30_out_9), .row4(screencontrol2_30_out_10), .row5(screencontrol2_30_out_11),
    .row6(screencontrol2_30_out_12), .row7(screencontrol2_30_out_13), .row8(screencontrol2_30_out_14),
    .row9(screencontrol2_30_out_15), .row10(screencontrol2_30_out_16), .row11(screencontrol2_30_out_17),
    .row12(screencontrol2_30_out_18), .row13(screencontrol2_30_out_19), .row14(screencontrol2_30_out_20),
    .row15(screencontrol2_30_out_21));
  ScreenControl2 screencontrol2_30 (
    .CLK(CLK), .Data(Data), .Reset(RESET), .Enable(screenchip_1_p5_2[1]), .Address(Local_Address),
    .out_6(screencontrol2_30_out_6), .out_7(screencontrol2_30_out_7), .out_8(screencontrol2_30_out_8),
    .out_9(screencontrol2_30_out_9), .out_10(screencontrol2_30_out_10), .out_11(screencontrol2_30_out_11),
    .out_12(screencontrol2_30_out_12), .out_13(screencontrol2_30_out_13), .out_14(screencontrol2_30_out_14),
    .out_15(screencontrol2_30_out_15), .out_16(screencontrol2_30_out_16), .out_17(screencontrol2_30_out_17),
    .out_18(screencontrol2_30_out_18), .out_19(screencontrol2_30_out_19), .out_20(screencontrol2_30_out_20),
    .out_21(screencontrol2_30_out_21));
  ScreenControl2 screencontrol2_31 (
    .CLK(CLK), .Data(Data), .Reset(RESET), .Enable(screenchip_1_p5_2[2]), .Address(Local_Address),
    .out_6(screencontrol2_31_out_6), .out_7(screencontrol2_31_out_7), .out_8(screencontrol2_31_out_8),
    .out_9(screencontrol2_31_out_9), .out_10(screencontrol2_31_out_10), .out_11(screencontrol2_31_out_11),
    .out_12(screencontrol2_31_out_12), .out_13(screencontrol2_31_out_13), .out_14(screencontrol2_31_out_14),
    .out_15(screencontrol2_31_out_15), .out_16(screencontrol2_31_out_16), .out_17(screencontrol2_31_out_17),
    .out_18(screencontrol2_31_out_18), .out_19(screencontrol2_31_out_19), .out_20(screencontrol2_31_out_20),
    .out_21(screencontrol2_31_out_21));
  DotMatrix #(.inputtype("row"), .matrixcols(16), .matrixrows(16)) dotmatrix_31 (
    .row0(screencontrol2_31_out_6), .row1(screencontrol2_31_out_7), .row2(screencontrol2_31_out_8),
    .row3(screencontrol2_31_out_9), .row4(screencontrol2_31_out_10), .row5(screencontrol2_31_out_11),
    .row6(screencontrol2_31_out_12), .row7(screencontrol2_31_out_13), .row8(screencontrol2_31_out_14),
    .row9(screencontrol2_31_out_15), .row10(screencontrol2_31_out_16), .row11(screencontrol2_31_out_17),
    .row12(screencontrol2_31_out_18), .row13(screencontrol2_31_out_19), .row14(screencontrol2_31_out_20),
    .row15(screencontrol2_31_out_21));
  DotMatrix #(.inputtype("row"), .matrixcols(16), .matrixrows(16)) dotmatrix_32 (
    .row0(screencontrol2_32_out_6), .row1(screencontrol2_32_out_7), .row2(screencontrol2_32_out_8),
    .row3(screencontrol2_32_out_9), .row4(screencontrol2_32_out_10), .row5(screencontrol2_32_out_11),
    .row6(screencontrol2_32_out_12), .row7(screencontrol2_32_out_13), .row8(screencontrol2_32_out_14),
    .row9(screencontrol2_32_out_15), .row10(screencontrol2_32_out_16), .row11(screencontrol2_32_out_17),
    .row12(screencontrol2_32_out_18), .row13(screencontrol2_32_out_19), .row14(screencontrol2_32_out_20),
    .row15(screencontrol2_32_out_21));
  ScreenControl2 screencontrol2_32 (
    .CLK(CLK), .Data(Data), .Reset(RESET), .Enable(screenchip_1_p5_2[3]), .Address(Local_Address),
    .out_6(screencontrol2_32_out_6), .out_7(screencontrol2_32_out_7), .out_8(screencontrol2_32_out_8),
    .out_9(screencontrol2_32_out_9), .out_10(screencontrol2_32_out_10), .out_11(screencontrol2_32_out_11),
    .out_12(screencontrol2_32_out_12), .out_13(screencontrol2_32_out_13), .out_14(screencontrol2_32_out_14),
    .out_15(screencontrol2_32_out_15), .out_16(screencontrol2_32_out_16), .out_17(screencontrol2_32_out_17),
    .out_18(screencontrol2_32_out_18), .out_19(screencontrol2_32_out_19), .out_20(screencontrol2_32_out_20),
    .out_21(screencontrol2_32_out_21));
endmodule

module ScreenChip (
  input  [15:0] Address,
  input  Enable,
  output [15:0] Local_Address,
  output [31:0] OUT
);

  wire decoder_1_out0, decoder_1_out1, decoder_1_out2, decoder_1_out3, decoder_2_out0, decoder_2_out1,
       decoder_2_out2, decoder_2_out3, decoder_2_out4, decoder_2_out5, decoder_2_out6, decoder_2_out7,
       not_1_out;
  wire [1:0] divider_2_out;
  wire [15:0] divider_1_rem;
  wire [15:2] divider_2_out_2;
  wire [31:0] pull_resistor_1_node, screenmatrix_1_out_20;

  Divider #(.width(16)) divider_1 (.a(Address), .b(16'h8), .out(Local_Address), .rem(divider_1_rem));  // open: upper
  Divider #(.width(16)) divider_2 (
    .a(Local_Address), .b(16'h10), .out({divider_2_out_2, divider_2_out}));  // open: upper, rem
  Decoder #(.select(2), .enable("false")) decoder_1 (
    .out0(decoder_1_out0), .out1(decoder_1_out1), .out2(decoder_1_out2), .out3(decoder_1_out3),
    .sel(divider_2_out));
  Decoder #(.select(3), .enable("false")) decoder_2 (
    .out0(decoder_2_out0), .out1(decoder_2_out1), .out2(decoder_2_out2), .out3(decoder_2_out3),
    .out4(decoder_2_out4), .out5(decoder_2_out5), .out6(decoder_2_out6), .out7(decoder_2_out7),
    .sel(divider_1_rem[2:0]));
  ScreenMatrix screenmatrix_1 (
    .in_9(decoder_1_out0), .in_10(decoder_1_out1), .in_11(decoder_1_out2), .in_12(decoder_1_out3),
    .in_1(decoder_2_out0), .in_2(decoder_2_out1), .in_3(decoder_2_out2), .in_4(decoder_2_out3),
    .in_5(decoder_2_out4), .in_6(decoder_2_out5), .in_7(decoder_2_out6), .in_8(decoder_2_out7),
    .out_37(screenmatrix_1_out_20[31]), .out_29(screenmatrix_1_out_20[30]),
    .out_21(screenmatrix_1_out_20[29]), .out_13(screenmatrix_1_out_20[28]),
    .out_38(screenmatrix_1_out_20[27]), .out_30(screenmatrix_1_out_20[26]),
    .out_22(screenmatrix_1_out_20[25]), .out_14(screenmatrix_1_out_20[24]),
    .out_39(screenmatrix_1_out_20[23]), .out_31(screenmatrix_1_out_20[22]),
    .out_23(screenmatrix_1_out_20[21]), .out_15(screenmatrix_1_out_20[20]),
    .out_40(screenmatrix_1_out_20[19]), .out_32(screenmatrix_1_out_20[18]),
    .out_24(screenmatrix_1_out_20[17]), .out_16(screenmatrix_1_out_20[16]),
    .out_41(screenmatrix_1_out_20[15]), .out_33(screenmatrix_1_out_20[14]),
    .out_25(screenmatrix_1_out_20[13]), .out_17(screenmatrix_1_out_20[12]),
    .out_42(screenmatrix_1_out_20[11]), .out_34(screenmatrix_1_out_20[10]),
    .out_26(screenmatrix_1_out_20[9]), .out_18(screenmatrix_1_out_20[8]), .out_43(screenmatrix_1_out_20[7]),
    .out_35(screenmatrix_1_out_20[6]), .out_27(screenmatrix_1_out_20[5]), .out_19(screenmatrix_1_out_20[4]),
    .out_44(screenmatrix_1_out_20[3]), .out_36(screenmatrix_1_out_20[2]), .out_28(screenmatrix_1_out_20[1]),
    .out_20(screenmatrix_1_out_20[0]));
  Pull_Resistor pull_resistor_1 (.node(pull_resistor_1_node));
  Multiplexer #(.width(32), .enable("false")) multiplexer_1 (
    .in0(screenmatrix_1_out_20), .in1(pull_resistor_1_node), .out(OUT), .sel(not_1_out));
  not not_1 (not_1_out, Enable);
endmodule

module SR_Latch (
  input  S,
  input  R,
  output Q,
  output minus_Q
);

  nor nor_1 (minus_Q, S, Q);
  nor nor_2 (Q, minus_Q, R);
endmodule

module Replicator (
  input  [15:0] Address,
  input  [15:0] Data,
  input  Write,
  input  [15:0] Offset,
  input  CLK,
  input  RESET,
  output [15:0] out_7,
  output [15:0] out_8,
  output [15:0] out_9,
  output [15:0] out_10,
  output [15:0] out_11,
  output [15:0] out_12,
  output [15:0] out_13,
  output [15:0] out_14,
  output [15:0] out_15,
  output [15:0] out_16,
  output [15:0] out_17,
  output [15:0] out_18,
  output [15:0] out_19,
  output [15:0] out_20,
  output [15:0] out_21,
  output [15:0] out_22,
  output [15:0] out_23,
  output [15:0] out_24,
  output [15:0] out_25,
  output [15:0] out_26,
  output [15:0] out_27,
  output [15:0] out_28,
  output [15:0] out_29,
  output [15:0] out_30,
  output [15:0] out_31,
  output [15:0] out_32,
  output [15:0] out_33,
  output [15:0] out_34,
  output [15:0] out_35,
  output [15:0] out_36,
  output [15:0] out_37,
  output [15:0] out_38
);

  wire address_translator_1_active, and_1_out;
  wire [15:0] address_translator_1_translated_address;
  wire [31:0] decoder_1_out0, multiplexer_1_out, pull_resistor_1_node;

  Address_Translator address_translator_1 (
    .Address(Address), .Offset(Offset), .Limit(16'h20),
    .Translated_Address(address_translator_1_translated_address), .Active(address_translator_1_active));
  Decoder #(.select(5), .enable("false")) decoder_1 (
    .out0(decoder_1_out0[0]), .out1(decoder_1_out0[1]), .out2(decoder_1_out0[2]), .out3(decoder_1_out0[3]),
    .out4(decoder_1_out0[4]), .out5(decoder_1_out0[5]), .out6(decoder_1_out0[6]), .out7(decoder_1_out0[7]),
    .out8(decoder_1_out0[8]), .out9(decoder_1_out0[9]), .out10(decoder_1_out0[10]),
    .out11(decoder_1_out0[11]), .out12(decoder_1_out0[12]), .out13(decoder_1_out0[13]),
    .out14(decoder_1_out0[14]), .out15(decoder_1_out0[15]), .out16(decoder_1_out0[16]),
    .out17(decoder_1_out0[17]), .out18(decoder_1_out0[18]), .out19(decoder_1_out0[19]),
    .out20(decoder_1_out0[20]), .out21(decoder_1_out0[21]), .out22(decoder_1_out0[22]),
    .out23(decoder_1_out0[23]), .out24(decoder_1_out0[24]), .out25(decoder_1_out0[25]),
    .out26(decoder_1_out0[26]), .out27(decoder_1_out0[27]), .out28(decoder_1_out0[28]),
    .out29(decoder_1_out0[29]), .out30(decoder_1_out0[30]), .out31(decoder_1_out0[31]),
    .sel(address_translator_1_translated_address[4:0]));
  Pull_Resistor pull_resistor_1 (.node(pull_resistor_1_node));
  Multiplexer #(.width(32), .enable("false")) multiplexer_1 (
    .in0(pull_resistor_1_node), .in1(decoder_1_out0), .out(multiplexer_1_out), .sel(and_1_out));
  and and_1 (and_1_out, address_translator_1_active, Write);
  Register #(.width(16)) register_1 (.D(Data), .en(multiplexer_1_out[0]), .Q(out_7), .clk(CLK), .clr(RESET));
  Register #(.width(16)) register_2 (.D(Data), .en(multiplexer_1_out[1]), .Q(out_8), .clk(CLK), .clr(RESET));
  Register #(.width(16)) register_3 (.D(Data), .en(multiplexer_1_out[2]), .Q(out_9), .clk(CLK), .clr(RESET));
  Register #(.width(16)) register_4 (.D(Data), .en(multiplexer_1_out[3]), .Q(out_10), .clk(CLK), .clr(RESET));
  Register #(.width(16)) register_5 (.D(Data), .en(multiplexer_1_out[4]), .Q(out_11), .clk(CLK), .clr(RESET));
  Register #(.width(16)) register_6 (.D(Data), .en(multiplexer_1_out[5]), .Q(out_12), .clk(CLK), .clr(RESET));
  Register #(.width(16)) register_7 (.D(Data), .en(multiplexer_1_out[6]), .Q(out_13), .clk(CLK), .clr(RESET));
  Register #(.width(16)) register_8 (.D(Data), .en(multiplexer_1_out[7]), .Q(out_14), .clk(CLK), .clr(RESET));
  Register #(.width(16)) register_9 (.D(Data), .en(multiplexer_1_out[8]), .Q(out_15), .clk(CLK), .clr(RESET));
  Register #(.width(16)) register_10 (.D(Data), .en(multiplexer_1_out[9]), .Q(out_16), .clk(CLK), .clr(RESET));
  Register #(.width(16)) register_11 (.D(Data), .en(multiplexer_1_out[10]), .Q(out_17), .clk(CLK), .clr(RESET));
  Register #(.width(16)) register_12 (.D(Data), .en(multiplexer_1_out[11]), .Q(out_18), .clk(CLK), .clr(RESET));
  Register #(.width(16)) register_13 (.D(Data), .en(multiplexer_1_out[12]), .Q(out_19), .clk(CLK), .clr(RESET));
  Register #(.width(16)) register_14 (.D(Data), .en(multiplexer_1_out[13]), .Q(out_20), .clk(CLK), .clr(RESET));
  Register #(.width(16)) register_15 (.D(Data), .en(multiplexer_1_out[14]), .Q(out_21), .clk(CLK), .clr(RESET));
  Register #(.width(16)) register_16 (.D(Data), .en(multiplexer_1_out[15]), .Q(out_22), .clk(CLK), .clr(RESET));
  Register #(.width(16)) register_17 (.D(Data), .en(multiplexer_1_out[16]), .Q(out_23), .clk(CLK), .clr(RESET));
  Register #(.width(16)) register_18 (.D(Data), .en(multiplexer_1_out[17]), .Q(out_24), .clk(CLK), .clr(RESET));
  Register #(.width(16)) register_19 (.D(Data), .en(multiplexer_1_out[18]), .Q(out_25), .clk(CLK), .clr(RESET));
  Register #(.width(16)) register_20 (.D(Data), .en(multiplexer_1_out[19]), .Q(out_26), .clk(CLK), .clr(RESET));
  Register #(.width(16)) register_21 (.D(Data), .en(multiplexer_1_out[20]), .Q(out_27), .clk(CLK), .clr(RESET));
  Register #(.width(16)) register_22 (.D(Data), .en(multiplexer_1_out[21]), .Q(out_28), .clk(CLK), .clr(RESET));
  Register #(.width(16)) register_23 (.D(Data), .en(multiplexer_1_out[22]), .Q(out_29), .clk(CLK), .clr(RESET));
  Register #(.width(16)) register_24 (.D(Data), .en(multiplexer_1_out[23]), .Q(out_30), .clk(CLK), .clr(RESET));
  Register #(.width(16)) register_25 (.D(Data), .en(multiplexer_1_out[24]), .Q(out_31), .clk(CLK), .clr(RESET));
  Register #(.width(16)) register_26 (.D(Data), .en(multiplexer_1_out[25]), .Q(out_32), .clk(CLK), .clr(RESET));
  Register #(.width(16)) register_27 (.D(Data), .en(multiplexer_1_out[26]), .Q(out_33), .clk(CLK), .clr(RESET));
  Register #(.width(16)) register_28 (.D(Data), .en(multiplexer_1_out[27]), .Q(out_34), .clk(CLK), .clr(RESET));
  Register #(.width(16)) register_29 (.D(Data), .en(multiplexer_1_out[28]), .Q(out_35), .clk(CLK), .clr(RESET));
  Register #(.width(16)) register_30 (.D(Data), .en(multiplexer_1_out[29]), .Q(out_36), .clk(CLK), .clr(RESET));
  Register #(.width(16)) register_31 (.D(Data), .en(multiplexer_1_out[30]), .Q(out_37), .clk(CLK), .clr(RESET));
  Register #(.width(16)) register_32 (.D(Data), .en(multiplexer_1_out[31]), .Q(out_38), .clk(CLK), .clr(RESET));

  // Notes on the sheet:
  //   32 values
endmodule

module Debug_Board (
  input  [15:0] Address,
  input  [15:0] Data,
  input  Write,
  input  CLK,
  input  RESET
);

  wire [15:0] replicator_1_out_7, replicator_1_out_8, replicator_1_out_9, replicator_1_out_10,
       replicator_1_out_11, replicator_1_out_12, replicator_1_out_13, replicator_1_out_14,
       replicator_1_out_15, replicator_1_out_16, replicator_1_out_17, replicator_1_out_18,
       replicator_1_out_19, replicator_1_out_20, replicator_1_out_21, replicator_1_out_22,
       replicator_1_out_23, replicator_1_out_24, replicator_1_out_25, replicator_1_out_26,
       replicator_1_out_27, replicator_1_out_28, replicator_1_out_29, replicator_1_out_30,
       replicator_1_out_31, replicator_1_out_32, replicator_1_out_33, replicator_1_out_34,
       replicator_1_out_35, replicator_1_out_36, replicator_1_out_37, replicator_1_out_38,
       replicator_2_out_7, replicator_2_out_8, replicator_2_out_9, replicator_2_out_10, replicator_2_out_11,
       replicator_2_out_12, replicator_2_out_13, replicator_2_out_14, replicator_2_out_15,
       replicator_2_out_16, replicator_2_out_17, replicator_2_out_18, replicator_2_out_19,
       replicator_2_out_20, replicator_2_out_21, replicator_2_out_22, replicator_2_out_23,
       replicator_2_out_24, replicator_2_out_25, replicator_2_out_26, replicator_2_out_27,
       replicator_2_out_28, replicator_2_out_29, replicator_2_out_30, replicator_2_out_31,
       replicator_2_out_32, replicator_2_out_33, replicator_2_out_34, replicator_2_out_35,
       replicator_2_out_36, replicator_2_out_37, replicator_2_out_38, replicator_3_out_7, replicator_3_out_8,
       replicator_3_out_9, replicator_3_out_10, replicator_3_out_11, replicator_3_out_12,
       replicator_3_out_13, replicator_3_out_14, replicator_3_out_15, replicator_3_out_16,
       replicator_3_out_17, replicator_3_out_18, replicator_3_out_19, replicator_3_out_20,
       replicator_3_out_21, replicator_3_out_22, replicator_3_out_23, replicator_3_out_24,
       replicator_3_out_25, replicator_3_out_26, replicator_3_out_27, replicator_3_out_28,
       replicator_3_out_29, replicator_3_out_30, replicator_3_out_31, replicator_3_out_32,
       replicator_3_out_33, replicator_3_out_34, replicator_3_out_35, replicator_3_out_36,
       replicator_3_out_37, replicator_3_out_38, replicator_4_out_7, replicator_4_out_8, replicator_4_out_9,
       replicator_4_out_10, replicator_4_out_11, replicator_4_out_12, replicator_4_out_13,
       replicator_4_out_14, replicator_4_out_15, replicator_4_out_16, replicator_5_out_7, replicator_5_out_8,
       replicator_5_out_9, replicator_5_out_10, replicator_5_out_11, replicator_5_out_12,
       replicator_5_out_13, replicator_5_out_14, replicator_5_out_15, replicator_5_out_16,
       replicator_5_out_17, replicator_5_out_18, replicator_5_out_19, replicator_5_out_20,
       replicator_5_out_21, replicator_5_out_22, replicator_5_out_23, replicator_5_out_24,
       replicator_5_out_25, replicator_5_out_26, replicator_5_out_27, replicator_5_out_28,
       replicator_5_out_29, replicator_5_out_30, replicator_5_out_31, replicator_5_out_32,
       replicator_5_out_33, replicator_5_out_34, replicator_5_out_35, replicator_5_out_36,
       replicator_5_out_37, replicator_5_out_38;

  Replicator replicator_1 (
    .Address(Address), .Data(Data), .Write(Write), .Offset(16'h100), .CLK(CLK), .RESET(RESET),
    .out_7(replicator_1_out_7), .out_8(replicator_1_out_8), .out_9(replicator_1_out_9),
    .out_10(replicator_1_out_10), .out_11(replicator_1_out_11), .out_12(replicator_1_out_12),
    .out_13(replicator_1_out_13), .out_14(replicator_1_out_14), .out_15(replicator_1_out_15),
    .out_16(replicator_1_out_16), .out_17(replicator_1_out_17), .out_18(replicator_1_out_18),
    .out_19(replicator_1_out_19), .out_20(replicator_1_out_20), .out_21(replicator_1_out_21),
    .out_22(replicator_1_out_22), .out_23(replicator_1_out_23), .out_24(replicator_1_out_24),
    .out_25(replicator_1_out_25), .out_26(replicator_1_out_26), .out_27(replicator_1_out_27),
    .out_28(replicator_1_out_28), .out_29(replicator_1_out_29), .out_30(replicator_1_out_30),
    .out_31(replicator_1_out_31), .out_32(replicator_1_out_32), .out_33(replicator_1_out_33),
    .out_34(replicator_1_out_34), .out_35(replicator_1_out_35), .out_36(replicator_1_out_36),
    .out_37(replicator_1_out_37), .out_38(replicator_1_out_38));
  // Probe on replicator_1_out_7
  // Probe on replicator_1_out_8
  // Probe on replicator_1_out_9
  // Probe on replicator_1_out_10
  // Probe on replicator_1_out_11
  // Probe on replicator_1_out_12
  // Probe on replicator_1_out_13
  // Probe on replicator_1_out_14
  // Probe on replicator_1_out_15
  // Probe on replicator_1_out_16
  // Probe on replicator_1_out_17
  // Probe on replicator_1_out_18
  // Probe on replicator_1_out_19
  // Probe on replicator_1_out_20
  // Probe on replicator_1_out_21
  // Probe on replicator_1_out_22
  // Probe on replicator_1_out_23
  // Probe on replicator_1_out_24
  // Probe on replicator_1_out_25
  // Probe on replicator_1_out_26
  // Probe on replicator_1_out_27
  // Probe on replicator_1_out_28
  // Probe on replicator_1_out_29
  // Probe on replicator_1_out_30
  // Probe on replicator_1_out_31
  // Probe on replicator_1_out_32
  // Probe on replicator_1_out_33
  // Probe on replicator_1_out_34
  // Probe on replicator_1_out_35
  // Probe on replicator_1_out_36
  // Probe on replicator_1_out_37
  // Probe on replicator_1_out_38
  Replicator replicator_2 (
    .Address(Address), .Data(Data), .Write(Write), .Offset(16'h12c), .CLK(CLK), .RESET(RESET),
    .out_7(replicator_2_out_7), .out_8(replicator_2_out_8), .out_9(replicator_2_out_9),
    .out_10(replicator_2_out_10), .out_11(replicator_2_out_11), .out_12(replicator_2_out_12),
    .out_13(replicator_2_out_13), .out_14(replicator_2_out_14), .out_15(replicator_2_out_15),
    .out_16(replicator_2_out_16), .out_17(replicator_2_out_17), .out_18(replicator_2_out_18),
    .out_19(replicator_2_out_19), .out_20(replicator_2_out_20), .out_21(replicator_2_out_21),
    .out_22(replicator_2_out_22), .out_23(replicator_2_out_23), .out_24(replicator_2_out_24),
    .out_25(replicator_2_out_25), .out_26(replicator_2_out_26), .out_27(replicator_2_out_27),
    .out_28(replicator_2_out_28), .out_29(replicator_2_out_29), .out_30(replicator_2_out_30),
    .out_31(replicator_2_out_31), .out_32(replicator_2_out_32), .out_33(replicator_2_out_33),
    .out_34(replicator_2_out_34), .out_35(replicator_2_out_35), .out_36(replicator_2_out_36),
    .out_37(replicator_2_out_37), .out_38(replicator_2_out_38));
  // Probe on replicator_2_out_7
  // Probe on replicator_2_out_8
  // Probe on replicator_2_out_9
  // Probe on replicator_2_out_10
  // Probe on replicator_2_out_11
  // Probe on replicator_2_out_12
  // Probe on replicator_2_out_13
  // Probe on replicator_2_out_14
  // Probe on replicator_2_out_15
  // Probe on replicator_2_out_16
  // Probe on replicator_2_out_17
  // Probe on replicator_2_out_18
  // Probe on replicator_2_out_19
  // Probe on replicator_2_out_20
  // Probe on replicator_2_out_21
  // Probe on replicator_2_out_22
  // Probe on replicator_2_out_23
  // Probe on replicator_2_out_24
  // Probe on replicator_2_out_25
  // Probe on replicator_2_out_26
  // Probe on replicator_2_out_27
  // Probe on replicator_2_out_28
  // Probe on replicator_2_out_29
  // Probe on replicator_2_out_30
  // Probe on replicator_2_out_31
  // Probe on replicator_2_out_32
  // Probe on replicator_2_out_33
  // Probe on replicator_2_out_34
  // Probe on replicator_2_out_35
  // Probe on replicator_2_out_36
  // Probe on replicator_2_out_37
  // Probe on replicator_2_out_38
  Replicator replicator_3 (
    .Address(Address), .Data(Data), .Write(Write), .Offset(16'h190), .CLK(CLK), .RESET(RESET),
    .out_7(replicator_3_out_7), .out_8(replicator_3_out_8), .out_9(replicator_3_out_9),
    .out_10(replicator_3_out_10), .out_11(replicator_3_out_11), .out_12(replicator_3_out_12),
    .out_13(replicator_3_out_13), .out_14(replicator_3_out_14), .out_15(replicator_3_out_15),
    .out_16(replicator_3_out_16), .out_17(replicator_3_out_17), .out_18(replicator_3_out_18),
    .out_19(replicator_3_out_19), .out_20(replicator_3_out_20), .out_21(replicator_3_out_21),
    .out_22(replicator_3_out_22), .out_23(replicator_3_out_23), .out_24(replicator_3_out_24),
    .out_25(replicator_3_out_25), .out_26(replicator_3_out_26), .out_27(replicator_3_out_27),
    .out_28(replicator_3_out_28), .out_29(replicator_3_out_29), .out_30(replicator_3_out_30),
    .out_31(replicator_3_out_31), .out_32(replicator_3_out_32), .out_33(replicator_3_out_33),
    .out_34(replicator_3_out_34), .out_35(replicator_3_out_35), .out_36(replicator_3_out_36),
    .out_37(replicator_3_out_37), .out_38(replicator_3_out_38));
  // Probe on replicator_3_out_7
  // Probe on replicator_3_out_8
  // Probe on replicator_3_out_9
  // Probe on replicator_3_out_10
  // Probe on replicator_3_out_11
  // Probe on replicator_3_out_12
  // Probe on replicator_3_out_13
  // Probe on replicator_3_out_14
  // Probe on replicator_3_out_15
  // Probe on replicator_3_out_16
  // Probe on replicator_3_out_17
  // Probe on replicator_3_out_18
  // Probe on replicator_3_out_19
  // Probe on replicator_3_out_20
  // Probe on replicator_3_out_21
  // Probe on replicator_3_out_22
  // Probe on replicator_3_out_23
  // Probe on replicator_3_out_24
  // Probe on replicator_3_out_25
  // Probe on replicator_3_out_26
  // Probe on replicator_3_out_27
  // Probe on replicator_3_out_28
  // Probe on replicator_3_out_29
  // Probe on replicator_3_out_30
  // Probe on replicator_3_out_31
  // Probe on replicator_3_out_32
  // Probe on replicator_3_out_33
  // Probe on replicator_3_out_34
  // Probe on replicator_3_out_35
  // Probe on replicator_3_out_36
  // Probe on replicator_3_out_37
  // Probe on replicator_3_out_38
  Replicator replicator_4 (
    .Address(Address), .Data(Data), .Write(Write), .Offset(16'hbb8), .CLK(CLK), .RESET(RESET),
    .out_7(replicator_4_out_7), .out_8(replicator_4_out_8), .out_9(replicator_4_out_9),
    .out_10(replicator_4_out_10), .out_11(replicator_4_out_11), .out_12(replicator_4_out_12),
    .out_13(replicator_4_out_13), .out_14(replicator_4_out_14), .out_15(replicator_4_out_15),
    .out_16(replicator_4_out_16));  // open: out_17, out_18, out_19, out_20, out_21, out_22, out_23, out_24, out_25, out_26, out_27, out_28, out_29, out_30, out_31, out_32, out_33, out_34, out_35, out_36, out_37, out_38
  // Probe on replicator_4_out_7
  // Probe on replicator_4_out_8
  // Probe on replicator_4_out_9
  // Probe on replicator_4_out_10
  // Probe on replicator_4_out_11
  // Probe on replicator_4_out_12
  // Probe on replicator_4_out_13
  // Probe on replicator_4_out_14
  // Probe on replicator_4_out_15
  // Probe on replicator_4_out_16
  Replicator replicator_5 (
    .Address(Address), .Data(Data), .Write(Write), .Offset(16'hbc2), .CLK(CLK), .RESET(RESET),
    .out_7(replicator_5_out_7), .out_8(replicator_5_out_8), .out_9(replicator_5_out_9),
    .out_10(replicator_5_out_10), .out_11(replicator_5_out_11), .out_12(replicator_5_out_12),
    .out_13(replicator_5_out_13), .out_14(replicator_5_out_14), .out_15(replicator_5_out_15),
    .out_16(replicator_5_out_16), .out_17(replicator_5_out_17), .out_18(replicator_5_out_18),
    .out_19(replicator_5_out_19), .out_20(replicator_5_out_20), .out_21(replicator_5_out_21),
    .out_22(replicator_5_out_22), .out_23(replicator_5_out_23), .out_24(replicator_5_out_24),
    .out_25(replicator_5_out_25), .out_26(replicator_5_out_26), .out_27(replicator_5_out_27),
    .out_28(replicator_5_out_28), .out_29(replicator_5_out_29), .out_30(replicator_5_out_30),
    .out_31(replicator_5_out_31), .out_32(replicator_5_out_32), .out_33(replicator_5_out_33),
    .out_34(replicator_5_out_34), .out_35(replicator_5_out_35), .out_36(replicator_5_out_36),
    .out_37(replicator_5_out_37), .out_38(replicator_5_out_38));
  // Probe on replicator_5_out_7
  // Probe on replicator_5_out_8
  // Probe on replicator_5_out_9
  // Probe on replicator_5_out_10
  // Probe on replicator_5_out_11
  // Probe on replicator_5_out_12
  // Probe on replicator_5_out_13
  // Probe on replicator_5_out_14
  // Probe on replicator_5_out_15
  // Probe on replicator_5_out_16
  // Probe on replicator_5_out_17
  // Probe on replicator_5_out_18
  // Probe on replicator_5_out_19
  // Probe on replicator_5_out_20
  // Probe on replicator_5_out_21
  // Probe on replicator_5_out_22
  // Probe on replicator_5_out_23
  // Probe on replicator_5_out_24
  // Probe on replicator_5_out_25
  // Probe on replicator_5_out_26
  // Probe on replicator_5_out_27
  // Probe on replicator_5_out_28
  // Probe on replicator_5_out_29
  // Probe on replicator_5_out_30
  // Probe on replicator_5_out_31
  // Probe on replicator_5_out_32
  // Probe on replicator_5_out_33
  // Probe on replicator_5_out_34
  // Probe on replicator_5_out_35
  // Probe on replicator_5_out_36
  // Probe on replicator_5_out_37
  // Probe on replicator_5_out_38

  // Notes on the sheet:
  //   STACK POINTER
  //   0
  //   1
  //   2
  //   3
  //   4
  //   5
  //   6
  //   7
  //   8
  //   9
  //   10
  //   11
  //   12
  //   13
  //   14
  //   15
  //   16
  //   17
  //   18
  //   19
  //   20
  //   21
  //   22
  //   23
  //   24
  //   25
  //   26
  //   27
  //   28
  //   29
  //   30
  //   31
  //   LOCAL
  //   0
  //   1
  //   2
  //   3
  //   4
  //   5
  //   6
  //   7
  //   8
  //   9
  //   10
  //   11
  //   12
  //   13
  //   14
  //   15
  //   16
  //   17
  //   18
  //   19
  //   20
  //   21
  //   22
  //   23
  //   24
  //   25
  //   26
  //   27
  //   28
  //   29
  //   30
  //   31
  //   ARG
  //   0
  //   1
  //   2
  //   3
  //   4
  //   5
  //   6
  //   7
  //   8
  //   9
  //   10
  //   11
  //   12
  //   13
  //   14
  //   15
  //   16
  //   17
  //   18
  //   19
  //   20
  //   21
  //   22
  //   23
  //   24
  //   25
  //   26
  //   27
  //   28
  //   29
  //   30
  //   31
  //   THIS
  //   0
  //   1
  //   2
  //   3
  //   4
  //   5
  //   6
  //   7
  //   8
  //   9
  //   THAT
  //   0
  //   1
  //   2
  //   4
  //   5
  //   8
  //   9
  //   3
  //   6
  //   7
  //   10
  //   11
  //   12
  //   13
  //   14
  //   15
  //   16
  //   17
  //   18
  //   19
  //   20
  //   21
  //   22
  //   23
  //   24
  //   25
  //   26
  //   27
  //   28
  //   29
  //   30
  //   31
endmodule

module Address_Translator (
  input  [15:0] Address,
  input  [15:0] Offset,
  input  [15:0] Limit,
  output [15:0] Translated_Address,
  output Active
);

  wire comparator_1_eq, comparator_1_gt, comparator_2_lt, or_1_out;
  wire [15:0] adder_1_out;

  Subtractor #(.width(16)) subtractor_1 (.a(Address), .b(Offset), .out(Translated_Address));  // open: bin, bout
  Comparator #(.width(16)) comparator_1 (
    .a(Address), .b(Offset), .gt(comparator_1_gt), .eq(comparator_1_eq));  // open: lt
  Comparator #(.width(16)) comparator_2 (.a(Address), .b(adder_1_out), .lt(comparator_2_lt));  // open: gt, eq
  Adder #(.width(16)) adder_1 (.a(Offset), .b(Limit), .out(adder_1_out));  // open: cin, cout
  or or_1 (or_1_out, comparator_1_gt, comparator_1_eq);
  and and_1 (Active, or_1_out, comparator_2_lt);
endmodule
